// Logisim project cpu24.circ as structural Verilog: 25 circuits, main circuit ◇单周期MIPS
module \单周期MIPS  (
);

  wire and_1_out, and_2_out, and_3_out, and_4_out, and_5_out, Bench, BLTZ, CLK, comparator_1_lt, Enable, Go,
       heigh, JMP, mips_alu_1_equal, not_1_out, not_3_out, or_2_out, or_3_out, register_1_q, RST, SH, Show,
       SignedExt, \硬布线控制器_1_alu_src , \硬布线控制器_1_beq , \硬布线控制器_1_bne , \硬布线控制器_1_jal , \硬布线控制器_1_jr ,
       \硬布线控制器_1_memtoreg , \硬布线控制器_1_memwrite , \硬布线控制器_1_regdst , \硬布线控制器_1_regwrite , \硬布线控制器_1_syscall ;
  wire [3:0] multiplexer_14_out, multiplexer_15_out, \硬布线控制器_1_alu_op ;
  wire [4:0] multiplexer_5_out, multiplexer_6_out, multiplexer_7_out, multiplexer_8_out, rom_1_data_2;
  wire [15:0] \总周期数 , \无条件分支数 , \条件分支成功数 ;
  wire [31:0] adder_1_out, adder_2_out, bit_extender_1_out, bit_extender_2_out, bit_extender_3_out, LedData,
       mips_alu_1_result, mips_ram_1_p8, mips_regifile_1_r1, mips_regifile_1_r2, multiplexer_1_out,
       multiplexer_2_out, multiplexer_3_out, multiplexer_4_out, multiplexer_9_out, multiplexer_10_out,
       multiplexer_11_out, multiplexer_12_out, multiplexer_13_out, multiplexer_16_out, PC_q, rom_1_data,
       shifter_1_out, shifter_2_out;

  Button \u_总复位  (.out(RST));
  Button \u_继续运行  (.out(Go));
  Clock clock_1 (.out(CLK));
  Comparator #(.width(32)) comparator_1 (.a(mips_regifile_1_r1), .b({32{1'b0}}), .lt(comparator_1_lt));  // open: gt, eq
  or or_1 (Bench, or_3_out, and_1_out);
  Multiplexer #(.width(32), .enable("false")) multiplexer_1 (
    .in0(adder_1_out), .in1(adder_2_out), .out(multiplexer_1_out), .sel(or_3_out));
  Hex_Digit_Display hex_digit_display_1 (.value(LedData[31:28]));  // open: dp
  Hex_Digit_Display hex_digit_display_2 (.value(LedData[27:24]));  // open: dp
  and and_1 (and_1_out, comparator_1_lt, BLTZ);
  Multiplexer #(.width(32), .enable("false")) multiplexer_2 (
    .in0(multiplexer_1_out), .in1(adder_2_out), .out(multiplexer_2_out), .sel(and_1_out));
  Hex_Digit_Display hex_digit_display_3 (.value(LedData[19:16]));  // open: dp
  Hex_Digit_Display hex_digit_display_4 (.value(LedData[23:20]));  // open: dp
  not not_1 (not_1_out, Show);
  Multiplexer #(.width(32), .enable("false")) multiplexer_3 (
    .in0(multiplexer_2_out), .in1(multiplexer_4_out), .out(multiplexer_3_out), .sel(JMP));
  Multiplexer #(.width(32), .enable("false")) multiplexer_4 (
    .in0(shifter_2_out), .in1(mips_regifile_1_r1), .out(multiplexer_4_out), .sel(\硬布线控制器_1_jr ));
  Hex_Digit_Display hex_digit_display_5 (.value(LedData[11:8]));  // open: dp
  Hex_Digit_Display hex_digit_display_6 (.value(LedData[15:12]));  // open: dp
  Register #(.width(1)) register_1 (
    .D(\硬布线控制器_1_syscall ), .en(and_2_out), .Q(register_1_q), .clk(CLK), .clr(or_2_out));
  and and_2 (and_2_out, not_1_out, \硬布线控制器_1_syscall );
  or or_2 (or_2_out, Go, RST);
  Register #(.width(32)) PC (.D(multiplexer_3_out), .en(Enable), .Q(PC_q), .clk(CLK), .clr(RST));
  Hex_Digit_Display hex_digit_display_7 (.value(LedData[3:0]));  // open: dp
  Hex_Digit_Display hex_digit_display_8 (.value(LedData[7:4]));  // open: dp
  not not_2 (Enable, register_1_q);
  ROM #(.addrWidth(10), .dataWidth(32)) rom_1 (
    .addr(PC_q[11:2]), .data({rom_1_data[31:11], rom_1_data_2, rom_1_data[5:0]}));  // open: sel
  Adder #(.width(32)) adder_1 (.a(PC_q), .b(32'h4), .out(adder_1_out));  // open: cin, cout
  // Probe on \总周期数 
  // Probe on \无条件分支数 
  // Probe on \条件分支成功数 
  \硬布线控制器  \u_硬布线控制器_1  (
    .Func(rom_1_data[5:0]), .OP(rom_1_data[31:26]), .ALU_OP(\硬布线控制器_1_alu_op ),
    .MemToReg(\硬布线控制器_1_memtoreg ), .MemWrite(\硬布线控制器_1_memwrite ), .ALU_SRC(\硬布线控制器_1_alu_src ),
    .RegWrite(\硬布线控制器_1_regwrite ), .SysCALL(\硬布线控制器_1_syscall ), .SignedExt(SignedExt),
    .RegDst(\硬布线控制器_1_regdst ), .JR(\硬布线控制器_1_jr ), .JMP(JMP), .Beq(\硬布线控制器_1_beq ), .JAL(\硬布线控制器_1_jal ),
    .Bne(\硬布线控制器_1_bne ), .SH(SH), .BLTZ(BLTZ));  // open: ERET, MF, MFC0, MTC0
  Multiplexer #(.width(5), .enable("false")) multiplexer_5 (
    .in0(rom_1_data[20:16]), .in1(rom_1_data[15:11]), .out(multiplexer_5_out), .sel(\硬布线控制器_1_regdst ));
  Multiplexer #(.width(5), .enable("false")) multiplexer_6 (
    .in0(rom_1_data[25:21]), .in1(5'b00100), .out(multiplexer_6_out), .sel(\硬布线控制器_1_syscall ));
  Multiplexer #(.width(5), .enable("false")) multiplexer_7 (
    .in0(rom_1_data[20:16]), .in1(5'b00010), .out(multiplexer_7_out), .sel(\硬布线控制器_1_syscall ));
  Multiplexer #(.width(5), .enable("false")) multiplexer_8 (
    .in0(multiplexer_5_out), .in1({5{1'b1}}), .out(multiplexer_8_out), .sel(\硬布线控制器_1_jal ));
  Counter #(.width(16), .max('hffff)) counter_1 (
    .count(Enable), .Q(\总周期数 ), .clk(CLK), .clr(RST));  // open: load, D, carry
  Multiplexer #(.width(32), .enable("false")) multiplexer_9 (
    .in0(multiplexer_16_out), .in1(adder_1_out), .out(multiplexer_9_out), .sel(\硬布线控制器_1_jal ));
  MIPS_Regifile mips_regifile_1 (
    .Din(multiplexer_9_out), .Clk(CLK), .R1(mips_regifile_1_r1), .R2(mips_regifile_1_r2),
    .WE(\硬布线控制器_1_regwrite ), .W_num(multiplexer_8_out), .R1_num(multiplexer_6_out),
    .R2_num(multiplexer_7_out));
  assign bit_extender_1_out = {{16{1'b0}}, {rom_1_data[15:11], rom_1_data_2, rom_1_data[5:0]}};  // Bit_Extender bit_extender_1
  Multiplexer #(.width(32), .enable("false")) multiplexer_10 (
    .in0(bit_extender_1_out), .in1(bit_extender_2_out), .out(multiplexer_10_out), .sel(SignedExt));
  assign bit_extender_2_out = {{16{rom_1_data[15]}}, {rom_1_data[15:11], rom_1_data_2, rom_1_data[5:0]}};  // Bit_Extender bit_extender_2
  assign bit_extender_3_out = {{6{rom_1_data[25]}}, {rom_1_data[25:11], rom_1_data_2, rom_1_data[5:0]}};  // Bit_Extender bit_extender_3
  Register #(.width(32)) register_2 (.D(mips_regifile_1_r1), .en(and_3_out), .Q(LedData), .clk(CLK), .clr(RST));
  and and_3 (and_3_out, Show, \硬布线控制器_1_syscall );
  Counter #(.width(16), .max('hffff)) counter_2 (
    .count(JMP), .Q(\无条件分支数 ), .clk(CLK), .clr(RST));  // open: load, D, carry
  Comparator #(.width(32)) comparator_2 (.a(32'h22), .b(mips_regifile_1_r2), .eq(Show));  // open: gt, lt
  Multiplexer #(.width(32), .enable("false")) multiplexer_11 (
    .in0(mips_regifile_1_r2), .in1(multiplexer_10_out), .out(multiplexer_11_out), .sel(\硬布线控制器_1_alu_src ));
  Shifter #(.width(32)) shifter_1 (.in(multiplexer_10_out), .\dist (5'b00010), .out(shifter_1_out));
  Shifter #(.width(32)) shifter_2 (.in(bit_extender_3_out), .\dist (5'b00010), .out(shifter_2_out));
  MIPS_ALU mips_alu_1 (
    .X(mips_regifile_1_r1), .Y(multiplexer_11_out), .AluOP(\硬布线控制器_1_alu_op ), .Equal(mips_alu_1_equal),
    .Result({mips_alu_1_result[31:2], heigh, mips_alu_1_result[0]}), .shamt(rom_1_data_2));  // open: Result_2
  Multiplexer #(.width(32), .enable("false")) multiplexer_12 (
    .in0({{16{1'b0}}, mips_regifile_1_r2[15:0]}), .in1({mips_regifile_1_r2[15:0], {16{1'b0}}}),
    .out(multiplexer_12_out), .sel(heigh));
  Adder #(.width(32)) adder_2 (.a(shifter_1_out), .b(adder_1_out), .out(adder_2_out));  // open: cin, cout
  Counter #(.width(16), .max('hffff)) counter_3 (
    .count(Bench), .Q(\条件分支成功数 ), .clk(CLK), .clr(RST));  // open: load, D, carry
  and and_4 (and_4_out, \硬布线控制器_1_beq , mips_alu_1_equal);
  and and_5 (and_5_out, \硬布线控制器_1_bne , not_3_out);
  not not_3 (not_3_out, mips_alu_1_equal);
  Multiplexer #(.width(32), .enable("false")) multiplexer_13 (
    .in0(mips_regifile_1_r2), .in1(multiplexer_12_out), .out(multiplexer_13_out), .sel(SH));
  or or_3 (or_3_out, and_4_out, and_5_out);
  Multiplexer #(.width(4), .enable("false")) multiplexer_14 (
    .in0(4'b1111), .in1(multiplexer_15_out), .out(multiplexer_14_out), .sel(SH));
  Multiplexer #(.width(4), .enable("false")) multiplexer_15 (
    .in0(4'b0011), .in1(4'b1100), .out(multiplexer_15_out), .sel(heigh));
  // MIPS_RAM mips_ram_1: pin names not known; wires that end beside it: mips_alu_1_result[11:2], multiplexer_13_out, \硬布线控制器_1_memwrite , multiplexer_14_out, CLK, 1'b1, RST, mips_ram_1_p8
  Multiplexer #(.width(32), .enable("false")) multiplexer_16 (
    .in0({mips_alu_1_result[31:2], heigh, mips_alu_1_result[0]}), .in1(mips_ram_1_p8),
    .out(multiplexer_16_out), .sel(\硬布线控制器_1_memtoreg ));

  // Notes on the sheet:
  //   数码管输出应该用寄存器锁存，否则显示数据只能一闪而过
  //   可以通过项目增加Logisim库的方式将前几次实验完成的电路作为子电路引入到本电路中使用
  //   数码管输出
  //   指令存储器
  //   指令字
  //   contents of rom_1 (hex, n*v repeats v):
  //   20100001 201200ff 20110001 20130003 12120004 12100003 20110001 20120002 20130003 102020 20020001 c
  //   16310004 16320003 20110001 20120002 20130003 132020 20020022 c 2002000a c
  //   总复位信号应将除ROM以外所有存储组件全部清零
  //   JMP
  //   JR
  //   OP
  //   OP
  //   Func
  //   Func
  //   rs
  //   rt
  //   rd
  //   Beq
  //   Bne
  //   MemToReg
  //   MemWrite
  //   AluOP
  //   AluSrcB
  //   RegWrite
  //   JAL
  //   RegDst
  //   Syscall
  //   周期数计算
endmodule

// 单周期硬布线控制器
module \硬布线控制器  (
  input  [5:0] OP,
  input  [5:0] Func,
  input  [4:0] MF,
  output [3:0] ALU_OP,
  output MemToReg,
  output MemWrite,
  output ALU_SRC,
  output SysCALL,
  output SignedExt,
  output RegDst,
  output Beq,
  output Bne,
  output JR,
  output JMP,
  output JAL,
  output SH,
  output BLTZ,
  output ERET,
  output RegWrite,
  output MFC0,
  output MTC0
);

  wire comparator_1_eq, comparator_2_eq, comparator_3_eq, RegWrite_t;

  Comparator #(.width(6)) comparator_1 (.a(OP), .b(6'b010000), .eq(comparator_1_eq));  // open: gt, lt
  Comparator #(.width(5)) comparator_2 (.a(MF), .b({5{1'b0}}), .eq(comparator_2_eq));  // open: gt, lt
  Comparator #(.width(5)) comparator_3 (.a(MF), .b(5'b00100), .eq(comparator_3_eq));  // open: gt, lt
  \运算控制器  \u_运算控制器_1  (
    .OP0(OP[0]), .OP1(OP[1]), .OP2(OP[2]), .OP3(OP[3]), .OP4(OP[4]), .OP5(OP[5]), .F0(Func[0]), .F1(Func[1]),
    .F2(Func[2]), .F3(Func[3]), .F4(Func[4]), .F5(Func[5]), .S0(ALU_OP[0]), .S1(ALU_OP[1]), .S2(ALU_OP[2]),
    .S3(ALU_OP[3]));
  \控制信号生成  \u_控制信号生成_1  (
    .OP0(OP[0]), .OP1(OP[1]), .OP2(OP[2]), .OP3(OP[3]), .OP4(OP[4]), .OP5(OP[5]), .F0(Func[0]), .F1(Func[1]),
    .F2(Func[2]), .F3(Func[3]), .F4(Func[4]), .F5(Func[5]), .MemToReg(MemToReg), .MemWrite(MemWrite),
    .ALU_SRC(ALU_SRC), .RegWrite(RegWrite_t), .SysCALL(SysCALL), .SignedExt(SignedExt), .RegDst(RegDst),
    .BEQ(Beq), .BNE(Bne), .JR(JR), .JMP(JMP), .JAL(JAL));
  \扩展信号控制器  \u_扩展信号控制器_1  (
    .OP0(OP[0]), .OP1(OP[1]), .OP2(OP[2]), .OP3(OP[3]), .OP4(OP[4]), .OP5(OP[5]), .F0(Func[0]), .F1(Func[1]),
    .F2(Func[2]), .F3(Func[3]), .F4(Func[4]), .F5(Func[5]), .SH(SH), .BLTZ(BLTZ), .ERET(ERET));
  and and_1 (MFC0, comparator_1_eq, comparator_2_eq);
  and and_2 (MTC0, comparator_1_eq, comparator_3_eq);
  or or_1 (RegWrite, RegWrite_t, MFC0);

  // Other names for the same wires on the sheet: OP_CODE[5:0] = OP

  // Notes on the sheet:
  //   运算器控制器，根据指令生成运算器功能选择信号
  //   控制信号生成，产生数据通路需要的其他控制信号
endmodule

// 运算器控制器
module \运算控制器  (
  input  OP0,
  input  OP1,
  input  OP2,
  input  OP3,
  input  OP4,
  input  OP5,
  input  F0,
  input  F1,
  input  F2,
  input  F3,
  input  F4,
  input  F5,
  output S0,
  output S1,
  output S2,
  output S3
);

  wire and_1_out, and_2_out, and_3_out, and_4_out, and_5_out, and_6_out, and_7_out, and_8_out, and_9_out,
       and_10_out, and_11_out, and_12_out, and_13_out, and_14_out, and_15_out, and_16_out, and_17_out,
       and_18_out, and_19_out, and_20_out, and_21_out, and_22_out, and_23_out, and_24_out, and_25_out,
       and_26_out, and_27_out, and_28_out, and_29_out, and_30_out, and_31_out, and_32_out, and_33_out,
       and_34_out, and_35_out, and_36_out, and_37_out, and_38_out, and_39_out, and_40_out, and_41_out,
       and_42_out, not_1_out, not_2_out, not_3_out, not_4_out, not_5_out, not_6_out, not_7_out, not_8_out,
       not_9_out, not_10_out, not_11_out, not_12_out, not_13_out, not_14_out, not_15_out, not_16_out,
       not_17_out, not_18_out, not_19_out, not_20_out, not_21_out, not_22_out, not_23_out, not_24_out,
       not_25_out, not_26_out, not_27_out, not_28_out, not_29_out, not_30_out, not_31_out, not_32_out,
       not_33_out, not_34_out, not_35_out, not_36_out, not_37_out, not_38_out, not_39_out, not_40_out,
       not_41_out, not_42_out, not_43_out, not_44_out, not_45_out, not_46_out, not_47_out, not_48_out,
       not_49_out, not_50_out, not_51_out, not_52_out, not_53_out, not_54_out, not_55_out, not_56_out,
       not_57_out, not_58_out, not_59_out, not_60_out, not_61_out, not_62_out, not_63_out, not_64_out,
       not_65_out, not_66_out, not_67_out, not_68_out, not_69_out, not_70_out, not_71_out, not_72_out,
       not_73_out, not_74_out, not_75_out, not_76_out, not_77_out, not_78_out, not_79_out, not_80_out,
       not_81_out, not_82_out, not_83_out, not_84_out, not_85_out, not_86_out, not_87_out, not_88_out,
       not_89_out, not_90_out, not_91_out, not_92_out, not_93_out, not_94_out, not_95_out, not_96_out,
       not_97_out, not_98_out, not_99_out, not_100_out, not_101_out, not_102_out, not_103_out, not_104_out,
       not_105_out, not_106_out, not_107_out, not_108_out, not_109_out, not_110_out, not_111_out,
       not_112_out, not_113_out, not_114_out, not_115_out, not_116_out, not_117_out, not_118_out,
       not_119_out, not_120_out, not_121_out, not_122_out, not_123_out, not_124_out, not_125_out,
       not_126_out, not_127_out, not_128_out, not_129_out, not_130_out, not_131_out, not_132_out,
       not_133_out, not_134_out, not_135_out, not_136_out, not_137_out, not_138_out, not_139_out,
       not_140_out, not_141_out, not_142_out, not_143_out, not_144_out, not_145_out, not_146_out,
       not_147_out, not_148_out, not_149_out, not_150_out, not_151_out, not_152_out, not_153_out,
       not_154_out, not_155_out, not_156_out, not_157_out, not_158_out, not_159_out, not_160_out,
       not_161_out, not_162_out, not_163_out, not_164_out, not_165_out, not_166_out, not_167_out,
       not_168_out, not_169_out, not_170_out, not_171_out, not_172_out, not_173_out, not_174_out,
       not_175_out, not_176_out, not_177_out, not_178_out, not_179_out, not_180_out, not_181_out,
       not_182_out, not_183_out, not_184_out, not_185_out, not_186_out, not_187_out, not_188_out,
       not_189_out, not_190_out, not_191_out, not_192_out, not_193_out, not_194_out, not_195_out,
       not_196_out, not_197_out, not_198_out, not_199_out, not_200_out, not_201_out, not_202_out,
       not_203_out, not_204_out, not_205_out, not_206_out, not_207_out, not_208_out, not_209_out,
       not_210_out, not_211_out, not_212_out, not_213_out, not_214_out, not_215_out, not_216_out,
       not_217_out, not_218_out, not_219_out, not_220_out, not_221_out, not_222_out, not_223_out,
       not_224_out, not_225_out, not_226_out, not_227_out, not_228_out, not_229_out, not_230_out,
       not_231_out, not_232_out, not_233_out, not_234_out, not_235_out, not_236_out, not_237_out,
       not_238_out, not_239_out, not_240_out, not_241_out, not_242_out, not_243_out, not_244_out,
       not_245_out, not_246_out, not_247_out, not_248_out, not_249_out, not_250_out, not_251_out,
       not_252_out, not_253_out, not_254_out, not_255_out, not_256_out, not_257_out, not_258_out,
       not_259_out, not_260_out, not_261_out, not_262_out, not_263_out, not_264_out, not_265_out,
       not_266_out, not_267_out, not_268_out, not_269_out, not_270_out, not_271_out, not_272_out,
       not_273_out, not_274_out, not_275_out, not_276_out, not_277_out, not_278_out, not_279_out,
       not_280_out, not_281_out, not_282_out, not_283_out, not_284_out, not_285_out, not_286_out,
       not_287_out, not_288_out;

  not not_1 (not_1_out, OP5);
  not not_2 (not_2_out, OP4);
  not not_3 (not_3_out, OP3);
  not not_4 (not_4_out, OP2);
  not not_5 (not_5_out, OP1);
  not not_6 (not_6_out, OP0);
  not not_7 (not_7_out, F5);
  not not_8 (not_8_out, F4);
  not not_9 (not_9_out, F3);
  not not_10 (not_10_out, F2);
  not not_11 (not_11_out, OP5);
  not not_12 (not_12_out, OP4);
  not not_13 (not_13_out, OP3);
  not not_14 (not_14_out, OP2);
  not not_15 (not_15_out, OP1);
  not not_16 (not_16_out, OP0);
  not not_17 (not_17_out, F4);
  not not_18 (not_18_out, F3);
  not not_19 (not_19_out, F2);
  not not_20 (not_20_out, F1);
  not not_21 (not_21_out, F0);
  not not_22 (not_22_out, OP5);
  not not_23 (not_23_out, OP4);
  not not_24 (not_24_out, OP3);
  not not_25 (not_25_out, OP2);
  not not_26 (not_26_out, OP1);
  not not_27 (not_27_out, OP0);
  not not_28 (not_28_out, F4);
  not not_29 (not_29_out, F3);
  not not_30 (not_30_out, F2);
  not not_31 (not_31_out, F1);
  not not_32 (not_32_out, OP5);
  not not_33 (not_33_out, OP4);
  not not_34 (not_34_out, OP3);
  not not_35 (not_35_out, OP2);
  not not_36 (not_36_out, OP1);
  not not_37 (not_37_out, OP0);
  not not_38 (not_38_out, F4);
  not not_39 (not_39_out, F3);
  not not_40 (not_40_out, F1);
  not not_41 (not_41_out, F0);
  not not_42 (not_42_out, OP5);
  not not_43 (not_43_out, OP4);
  not not_44 (not_44_out, OP3);
  not not_45 (not_45_out, OP2);
  not not_46 (not_46_out, OP1);
  not not_47 (not_47_out, OP0);
  not not_48 (not_48_out, F4);
  not not_49 (not_49_out, F2);
  not not_50 (not_50_out, F0);
  not not_51 (not_51_out, OP5);
  not not_52 (not_52_out, OP4);
  not not_53 (not_53_out, OP2);
  not not_54 (not_54_out, OP1);
  not not_55 (not_55_out, OP0);
  not not_56 (not_56_out, OP5);
  not not_57 (not_57_out, OP4);
  not not_58 (not_58_out, OP1);
  not not_59 (not_59_out, OP0);
  not not_60 (not_60_out, OP5);
  not not_61 (not_61_out, OP4);
  not not_62 (not_62_out, OP2);
  not not_63 (not_63_out, OP1);
  not not_64 (not_64_out, OP5);
  not not_65 (not_65_out, OP4);
  not not_66 (not_66_out, OP2);
  not not_67 (not_67_out, OP0);
  not not_68 (not_68_out, OP4);
  not not_69 (not_69_out, OP3);
  not not_70 (not_70_out, OP2);
  not not_71 (not_71_out, OP4);
  not not_72 (not_72_out, OP2);
  not not_73 (not_73_out, OP5);
  not not_74 (not_74_out, OP4);
  not not_75 (not_75_out, OP3);
  not not_76 (not_76_out, OP2);
  not not_77 (not_77_out, OP1);
  not not_78 (not_78_out, OP0);
  not not_79 (not_79_out, F4);
  not not_80 (not_80_out, F3);
  not not_81 (not_81_out, F0);
  not not_82 (not_82_out, OP4);
  not not_83 (not_83_out, OP2);
  not not_84 (not_84_out, OP1);
  not not_85 (not_85_out, OP5);
  not not_86 (not_86_out, OP4);
  not not_87 (not_87_out, OP3);
  not not_88 (not_88_out, OP2);
  not not_89 (not_89_out, OP1);
  not not_90 (not_90_out, OP5);
  not not_91 (not_91_out, OP4);
  not not_92 (not_92_out, OP3);
  not not_93 (not_93_out, OP2);
  not not_94 (not_94_out, OP1);
  not not_95 (not_95_out, OP0);
  not not_96 (not_96_out, F5);
  not not_97 (not_97_out, F4);
  not not_98 (not_98_out, F3);
  not not_99 (not_99_out, F2);
  not not_100 (not_100_out, F0);
  not not_101 (not_101_out, OP5);
  not not_102 (not_102_out, OP4);
  not not_103 (not_103_out, OP3);
  not not_104 (not_104_out, OP2);
  not not_105 (not_105_out, OP1);
  not not_106 (not_106_out, OP0);
  not not_107 (not_107_out, F4);
  not not_108 (not_108_out, F3);
  not not_109 (not_109_out, F2);
  not not_110 (not_110_out, F0);
  not not_111 (not_111_out, OP5);
  not not_112 (not_112_out, OP4);
  not not_113 (not_113_out, OP3);
  not not_114 (not_114_out, OP2);
  not not_115 (not_115_out, OP1);
  not not_116 (not_116_out, OP0);
  not not_117 (not_117_out, F4);
  not not_118 (not_118_out, F3);
  not not_119 (not_119_out, F1);
  not not_120 (not_120_out, F0);
  not not_121 (not_121_out, OP5);
  not not_122 (not_122_out, OP4);
  not not_123 (not_123_out, OP3);
  not not_124 (not_124_out, OP2);
  not not_125 (not_125_out, OP1);
  not not_126 (not_126_out, OP0);
  not not_127 (not_127_out, F4);
  not not_128 (not_128_out, F3);
  not not_129 (not_129_out, OP5);
  not not_130 (not_130_out, OP4);
  not not_131 (not_131_out, OP3);
  not not_132 (not_132_out, OP2);
  not not_133 (not_133_out, OP1);
  not not_134 (not_134_out, OP0);
  not not_135 (not_135_out, F4);
  not not_136 (not_136_out, F2);
  not not_137 (not_137_out, F0);
  not not_138 (not_138_out, OP5);
  not not_139 (not_139_out, OP4);
  not not_140 (not_140_out, OP1);
  not not_141 (not_141_out, OP0);
  not not_142 (not_142_out, OP5);
  not not_143 (not_143_out, OP4);
  not not_144 (not_144_out, OP2);
  not not_145 (not_145_out, OP0);
  not not_146 (not_146_out, OP5);
  not not_147 (not_147_out, OP4);
  not not_148 (not_148_out, OP3);
  not not_149 (not_149_out, OP2);
  not not_150 (not_150_out, OP1);
  not not_151 (not_151_out, OP0);
  not not_152 (not_152_out, F4);
  not not_153 (not_153_out, F3);
  not not_154 (not_154_out, F2);
  not not_155 (not_155_out, OP5);
  not not_156 (not_156_out, OP4);
  not not_157 (not_157_out, OP3);
  not not_158 (not_158_out, OP2);
  not not_159 (not_159_out, OP1);
  not not_160 (not_160_out, OP0);
  not not_161 (not_161_out, F4);
  not not_162 (not_162_out, F3);
  not not_163 (not_163_out, F2);
  not not_164 (not_164_out, F1);
  not not_165 (not_165_out, F0);
  not not_166 (not_166_out, OP5);
  not not_167 (not_167_out, OP4);
  not not_168 (not_168_out, OP3);
  not not_169 (not_169_out, OP2);
  not not_170 (not_170_out, OP1);
  not not_171 (not_171_out, OP0);
  not not_172 (not_172_out, F4);
  not not_173 (not_173_out, F3);
  not not_174 (not_174_out, F2);
  not not_175 (not_175_out, F1);
  not not_176 (not_176_out, OP5);
  not not_177 (not_177_out, OP4);
  not not_178 (not_178_out, OP3);
  not not_179 (not_179_out, OP2);
  not not_180 (not_180_out, OP1);
  not not_181 (not_181_out, OP0);
  not not_182 (not_182_out, F4);
  not not_183 (not_183_out, F3);
  not not_184 (not_184_out, F2);
  not not_185 (not_185_out, F0);
  not not_186 (not_186_out, OP5);
  not not_187 (not_187_out, OP4);
  not not_188 (not_188_out, OP3);
  not not_189 (not_189_out, OP2);
  not not_190 (not_190_out, OP1);
  not not_191 (not_191_out, OP0);
  not not_192 (not_192_out, F4);
  not not_193 (not_193_out, F3);
  not not_194 (not_194_out, F1);
  not not_195 (not_195_out, F0);
  not not_196 (not_196_out, OP5);
  not not_197 (not_197_out, OP4);
  not not_198 (not_198_out, OP3);
  not not_199 (not_199_out, OP2);
  not not_200 (not_200_out, OP1);
  not not_201 (not_201_out, OP0);
  not not_202 (not_202_out, F4);
  not not_203 (not_203_out, F2);
  not not_204 (not_204_out, OP5);
  not not_205 (not_205_out, OP4);
  not not_206 (not_206_out, OP2);
  not not_207 (not_207_out, OP1);
  not not_208 (not_208_out, OP0);
  not not_209 (not_209_out, OP5);
  not not_210 (not_210_out, OP4);
  not not_211 (not_211_out, OP1);
  not not_212 (not_212_out, OP0);
  not not_213 (not_213_out, OP5);
  not not_214 (not_214_out, OP4);
  not not_215 (not_215_out, OP2);
  not not_216 (not_216_out, OP1);
  not not_217 (not_217_out, OP4);
  not not_218 (not_218_out, OP3);
  not not_219 (not_219_out, OP2);
  not not_220 (not_220_out, OP4);
  not not_221 (not_221_out, OP2);
  not not_222 (not_222_out, OP5);
  not not_223 (not_223_out, OP4);
  not not_224 (not_224_out, OP3);
  not not_225 (not_225_out, OP2);
  not not_226 (not_226_out, OP1);
  not not_227 (not_227_out, OP0);
  not not_228 (not_228_out, F4);
  not not_229 (not_229_out, F3);
  not not_230 (not_230_out, F2);
  not not_231 (not_231_out, OP4);
  not not_232 (not_232_out, OP2);
  not not_233 (not_233_out, OP1);
  not not_234 (not_234_out, OP5);
  not not_235 (not_235_out, OP4);
  not not_236 (not_236_out, OP3);
  not not_237 (not_237_out, OP2);
  not not_238 (not_238_out, OP1);
  not not_239 (not_239_out, OP5);
  not not_240 (not_240_out, OP4);
  not not_241 (not_241_out, OP3);
  not not_242 (not_242_out, OP2);
  not not_243 (not_243_out, OP1);
  not not_244 (not_244_out, OP0);
  not not_245 (not_245_out, F4);
  not not_246 (not_246_out, F3);
  not not_247 (not_247_out, F1);
  not not_248 (not_248_out, OP5);
  not not_249 (not_249_out, OP4);
  not not_250 (not_250_out, OP3);
  not not_251 (not_251_out, OP2);
  not not_252 (not_252_out, OP1);
  not not_253 (not_253_out, OP0);
  not not_254 (not_254_out, F4);
  not not_255 (not_255_out, F3);
  not not_256 (not_256_out, OP5);
  not not_257 (not_257_out, OP4);
  not not_258 (not_258_out, OP3);
  not not_259 (not_259_out, OP2);
  not not_260 (not_260_out, OP1);
  not not_261 (not_261_out, OP0);
  not not_262 (not_262_out, F4);
  not not_263 (not_263_out, F2);
  not not_264 (not_264_out, F0);
  not not_265 (not_265_out, OP5);
  not not_266 (not_266_out, OP4);
  not not_267 (not_267_out, OP3);
  not not_268 (not_268_out, OP2);
  not not_269 (not_269_out, OP1);
  not not_270 (not_270_out, OP0);
  not not_271 (not_271_out, F4);
  not not_272 (not_272_out, F2);
  not not_273 (not_273_out, OP5);
  not not_274 (not_274_out, OP4);
  not not_275 (not_275_out, OP2);
  not not_276 (not_276_out, OP0);
  not not_277 (not_277_out, OP5);
  not not_278 (not_278_out, OP4);
  not not_279 (not_279_out, OP1);
  not not_280 (not_280_out, OP5);
  not not_281 (not_281_out, OP4);
  not not_282 (not_282_out, OP3);
  not not_283 (not_283_out, OP2);
  not not_284 (not_284_out, OP1);
  not not_285 (not_285_out, OP0);
  not not_286 (not_286_out, F4);
  not not_287 (not_287_out, F3);
  not not_288 (not_288_out, F0);
  and and_1 (and_1_out, not_1_out, not_2_out, not_3_out, not_4_out, not_5_out, not_6_out, not_7_out, not_8_out, not_9_out, not_10_out, F1, F0);
  and and_2 (and_2_out, not_11_out, not_12_out, not_13_out, not_14_out, not_15_out, not_16_out, F5, not_17_out, not_18_out, not_19_out, not_20_out, not_21_out);
  and and_3 (and_3_out, not_22_out, not_23_out, not_24_out, not_25_out, not_26_out, not_27_out, F5, not_28_out, not_29_out, not_30_out, not_31_out, F0);
  and and_4 (and_4_out, not_32_out, not_33_out, not_34_out, not_35_out, not_36_out, not_37_out, F5, not_38_out, not_39_out, F2, not_40_out, not_41_out);
  and and_5 (and_5_out, not_42_out, not_43_out, not_44_out, not_45_out, not_46_out, not_47_out, F5, not_48_out, F3, not_49_out, F1, not_50_out);
  and and_6 (and_6_out, not_51_out, not_52_out, OP3, not_53_out, not_54_out, not_55_out);
  and and_7 (and_7_out, not_56_out, not_57_out, OP3, OP2, not_58_out, not_59_out);
  and and_8 (and_8_out, not_60_out, not_61_out, OP3, not_62_out, not_63_out, OP0);
  and and_9 (and_9_out, not_64_out, not_65_out, OP3, not_66_out, OP1, not_67_out);
  and and_10 (and_10_out, OP5, not_68_out, not_69_out, not_70_out, OP1, OP0);
  and and_11 (and_11_out, OP5, not_71_out, OP3, not_72_out, OP1, OP0);
  and and_12 (and_12_out, not_73_out, not_74_out, not_75_out, not_76_out, not_77_out, not_78_out, F5, not_79_out, not_80_out, F2, F1, not_81_out);
  and and_13 (and_13_out, OP5, not_82_out, OP3, not_83_out, not_84_out, OP0);
  and and_14 (and_14_out, not_85_out, not_86_out, not_87_out, not_88_out, not_89_out, OP0);
  and and_15 (and_15_out, not_90_out, not_91_out, not_92_out, not_93_out, not_94_out, not_95_out, not_96_out, not_97_out, not_98_out, not_99_out, F1, not_100_out);
  and and_16 (and_16_out, not_101_out, not_102_out, not_103_out, not_104_out, not_105_out, not_106_out, F5, not_107_out, not_108_out, not_109_out, F1, not_110_out);
  and and_17 (and_17_out, not_111_out, not_112_out, not_113_out, not_114_out, not_115_out, not_116_out, F5, not_117_out, not_118_out, F2, not_119_out, not_120_out);
  and and_18 (and_18_out, not_121_out, not_122_out, not_123_out, not_124_out, not_125_out, not_126_out, F5, not_127_out, not_128_out, F2, F1, F0);
  and and_19 (and_19_out, not_129_out, not_130_out, not_131_out, not_132_out, not_133_out, not_134_out, F5, not_135_out, F3, not_136_out, F1, not_137_out);
  and and_20 (and_20_out, not_138_out, not_139_out, OP3, OP2, not_140_out, not_141_out);
  and and_21 (and_21_out, not_142_out, not_143_out, OP3, not_144_out, OP1, not_145_out);
  and and_22 (and_22_out, not_146_out, not_147_out, not_148_out, not_149_out, not_150_out, not_151_out, F5, not_152_out, not_153_out, not_154_out, F1, F0);
  and and_23 (and_23_out, not_155_out, not_156_out, not_157_out, not_158_out, not_159_out, not_160_out, F5, not_161_out, not_162_out, not_163_out, not_164_out, not_165_out);
  and and_24 (and_24_out, not_166_out, not_167_out, not_168_out, not_169_out, not_170_out, not_171_out, F5, not_172_out, not_173_out, not_174_out, not_175_out, F0);
  and and_25 (and_25_out, not_176_out, not_177_out, not_178_out, not_179_out, not_180_out, not_181_out, F5, not_182_out, not_183_out, not_184_out, F1, not_185_out);
  and and_26 (and_26_out, not_186_out, not_187_out, not_188_out, not_189_out, not_190_out, not_191_out, F5, not_192_out, not_193_out, F2, not_194_out, not_195_out);
  and and_27 (and_27_out, not_196_out, not_197_out, not_198_out, not_199_out, not_200_out, not_201_out, F5, not_202_out, F3, not_203_out, F1, F0);
  and and_28 (and_28_out, not_204_out, not_205_out, OP3, not_206_out, not_207_out, not_208_out);
  and and_29 (and_29_out, not_209_out, not_210_out, OP3, OP2, not_211_out, not_212_out);
  and and_30 (and_30_out, not_213_out, not_214_out, OP3, not_215_out, not_216_out, OP0);
  and and_31 (and_31_out, OP5, not_217_out, not_218_out, not_219_out, OP1, OP0);
  and and_32 (and_32_out, OP5, not_220_out, OP3, not_221_out, OP1, OP0);
  and and_33 (and_33_out, not_222_out, not_223_out, not_224_out, not_225_out, not_226_out, not_227_out, F5, not_228_out, not_229_out, not_230_out, F1, F0);
  and and_34 (and_34_out, OP5, not_231_out, OP3, not_232_out, not_233_out, OP0);
  and and_35 (and_35_out, not_234_out, not_235_out, not_236_out, not_237_out, not_238_out, OP0);
  and and_36 (and_36_out, not_239_out, not_240_out, not_241_out, not_242_out, not_243_out, not_244_out, F5, not_245_out, not_246_out, F2, not_247_out, F0);
  and and_37 (and_37_out, not_248_out, not_249_out, not_250_out, not_251_out, not_252_out, not_253_out, F5, not_254_out, not_255_out, F2, F1, F0);
  and and_38 (and_38_out, not_256_out, not_257_out, not_258_out, not_259_out, not_260_out, not_261_out, F5, not_262_out, F3, not_263_out, F1, not_264_out);
  and and_39 (and_39_out, not_265_out, not_266_out, not_267_out, not_268_out, not_269_out, not_270_out, F5, not_271_out, F3, not_272_out, F1, F0);
  and and_40 (and_40_out, not_273_out, not_274_out, OP3, not_275_out, OP1, not_276_out);
  and and_41 (and_41_out, not_277_out, not_278_out, OP3, OP2, not_279_out, OP0);
  and and_42 (and_42_out, not_280_out, not_281_out, not_282_out, not_283_out, not_284_out, not_285_out, F5, not_286_out, not_287_out, F2, F1, not_288_out);
  or or_1 (S1, and_15_out, and_16_out, and_17_out, and_18_out, and_19_out, and_20_out, and_21_out, and_22_out);
  or or_2 (S3, and_36_out, and_37_out, and_38_out, and_39_out, and_40_out, and_41_out, and_42_out);
  or or_3 (S0, and_1_out, and_2_out, and_3_out, and_4_out, and_5_out, and_6_out, and_7_out, and_8_out, and_9_out, and_10_out, and_11_out, and_12_out, and_13_out, and_14_out);
  or or_4 (S2, and_23_out, and_24_out, and_25_out, and_26_out, and_27_out, and_28_out, and_29_out, and_30_out, and_31_out, and_32_out, and_33_out, and_34_out, and_35_out);
endmodule

// 控制信号生成
module \控制信号生成  (
  input  OP0,
  input  OP1,
  input  OP2,
  input  OP3,
  input  OP4,
  input  OP5,
  input  F0,
  input  F1,
  input  F2,
  input  F3,
  input  F4,
  input  F5,
  output MemToReg,
  output MemWrite,
  output ALU_SRC,
  output RegWrite,
  output SysCALL,
  output SignedExt,
  output RegDst,
  output BEQ,
  output BNE,
  output JR,
  output JMP,
  output JAL
);

  wire and_2_out, and_3_out, and_4_out, and_5_out, and_6_out, and_7_out, and_8_out, and_9_out, and_10_out,
       and_11_out, and_12_out, and_13_out, and_14_out, and_15_out, and_16_out, and_17_out, and_18_out,
       and_19_out, and_20_out, and_21_out, and_22_out, and_23_out, and_24_out, and_25_out, and_26_out,
       and_27_out, and_28_out, and_29_out, and_30_out, and_31_out, and_33_out, and_34_out, and_35_out,
       and_36_out, and_37_out, and_38_out, and_39_out, and_40_out, and_41_out, and_42_out, and_43_out,
       and_44_out, and_45_out, and_46_out, and_47_out, and_48_out, and_49_out, and_50_out, and_51_out,
       and_52_out, and_53_out, and_57_out, and_58_out, and_59_out, not_1_out, not_2_out, not_3_out,
       not_4_out, not_5_out, not_6_out, not_7_out, not_8_out, not_9_out, not_10_out, not_11_out, not_12_out,
       not_13_out, not_14_out, not_15_out, not_16_out, not_17_out, not_18_out, not_19_out, not_20_out,
       not_21_out, not_22_out, not_23_out, not_24_out, not_25_out, not_26_out, not_27_out, not_28_out,
       not_29_out, not_30_out, not_31_out, not_32_out, not_33_out, not_34_out, not_35_out, not_36_out,
       not_37_out, not_38_out, not_39_out, not_40_out, not_41_out, not_42_out, not_43_out, not_44_out,
       not_45_out, not_46_out, not_47_out, not_48_out, not_49_out, not_50_out, not_51_out, not_52_out,
       not_53_out, not_54_out, not_55_out, not_56_out, not_57_out, not_58_out, not_59_out, not_60_out,
       not_61_out, not_62_out, not_63_out, not_64_out, not_65_out, not_66_out, not_67_out, not_68_out,
       not_69_out, not_70_out, not_71_out, not_72_out, not_73_out, not_74_out, not_75_out, not_76_out,
       not_77_out, not_78_out, not_79_out, not_80_out, not_81_out, not_82_out, not_83_out, not_84_out,
       not_85_out, not_86_out, not_87_out, not_88_out, not_89_out, not_90_out, not_91_out, not_92_out,
       not_93_out, not_94_out, not_95_out, not_96_out, not_97_out, not_98_out, not_99_out, not_100_out,
       not_101_out, not_102_out, not_103_out, not_104_out, not_105_out, not_106_out, not_107_out,
       not_108_out, not_109_out, not_110_out, not_111_out, not_112_out, not_113_out, not_114_out,
       not_115_out, not_116_out, not_117_out, not_118_out, not_119_out, not_120_out, not_121_out,
       not_122_out, not_123_out, not_124_out, not_125_out, not_126_out, not_127_out, not_128_out,
       not_129_out, not_130_out, not_131_out, not_132_out, not_133_out, not_134_out, not_135_out,
       not_136_out, not_137_out, not_138_out, not_139_out, not_140_out, not_141_out, not_142_out,
       not_143_out, not_144_out, not_145_out, not_146_out, not_147_out, not_148_out, not_149_out,
       not_150_out, not_151_out, not_152_out, not_153_out, not_154_out, not_155_out, not_156_out,
       not_157_out, not_158_out, not_159_out, not_160_out, not_161_out, not_162_out, not_163_out,
       not_164_out, not_165_out, not_166_out, not_167_out, not_168_out, not_169_out, not_170_out,
       not_171_out, not_172_out, not_173_out, not_174_out, not_175_out, not_176_out, not_177_out,
       not_178_out, not_179_out, not_180_out, not_181_out, not_182_out, not_183_out, not_184_out,
       not_185_out, not_186_out, not_187_out, not_188_out, not_189_out, not_190_out, not_191_out,
       not_192_out, not_193_out, not_194_out, not_195_out, not_196_out, not_197_out, not_198_out,
       not_199_out, not_200_out, not_201_out, not_202_out, not_203_out, not_204_out, not_205_out,
       not_206_out, not_207_out, not_208_out, not_209_out, not_210_out, not_211_out, not_212_out,
       not_213_out, not_214_out, not_215_out, not_216_out, not_217_out, not_218_out, not_219_out,
       not_220_out, not_221_out, not_222_out, not_223_out, not_224_out, not_225_out, not_226_out,
       not_227_out, not_228_out, not_229_out, not_230_out, not_231_out, not_232_out, not_233_out,
       not_234_out, not_235_out, not_236_out, not_237_out, not_238_out, not_239_out, not_240_out,
       not_241_out, not_242_out, not_243_out, not_244_out, not_245_out, not_246_out, not_247_out,
       not_248_out, not_249_out, not_250_out, not_251_out, not_252_out, not_253_out, not_254_out,
       not_255_out, not_256_out, not_257_out, not_258_out, not_259_out, not_260_out, not_261_out,
       not_262_out, not_263_out, not_264_out, not_265_out, not_266_out, not_267_out, not_268_out,
       not_269_out, not_270_out, not_271_out, not_272_out, not_273_out, not_274_out, not_275_out,
       not_276_out, not_277_out, not_278_out, not_279_out, not_280_out, not_281_out, not_282_out,
       not_283_out, not_284_out, not_285_out, not_286_out, not_287_out, not_288_out, not_289_out,
       not_290_out, not_291_out, not_292_out, not_293_out, not_294_out, not_295_out, not_296_out,
       not_297_out, not_298_out, not_299_out, not_300_out, not_301_out, not_302_out, not_303_out,
       not_304_out, not_305_out, not_306_out, not_307_out, not_308_out, not_309_out, not_310_out,
       not_311_out, not_312_out, not_313_out, not_314_out, not_315_out, not_316_out, not_317_out,
       not_318_out, not_319_out, not_320_out, not_321_out, not_322_out, not_323_out, not_324_out,
       not_325_out, not_326_out, not_327_out, not_328_out, not_329_out, not_330_out, not_331_out,
       not_332_out, not_333_out, not_334_out, not_335_out, not_336_out, not_337_out, not_338_out,
       not_339_out, not_340_out, not_341_out, not_342_out, not_343_out, not_344_out, not_345_out,
       not_346_out, not_347_out, not_348_out, not_349_out, not_350_out, not_351_out, not_352_out,
       not_353_out, not_354_out, not_355_out, not_356_out, not_357_out, not_358_out, not_359_out,
       not_360_out, not_361_out, not_362_out, not_363_out, not_364_out, not_365_out, not_366_out,
       not_367_out, not_368_out, not_369_out, not_370_out, not_371_out, not_372_out, not_373_out,
       not_374_out, not_375_out, not_376_out, not_377_out, not_378_out, not_379_out, not_380_out,
       not_381_out, not_382_out, not_383_out, not_384_out, not_385_out, not_386_out, not_387_out,
       not_388_out, not_389_out, not_390_out, not_391_out, not_392_out, not_393_out, not_394_out,
       not_395_out, not_396_out, not_397_out, not_398_out, not_399_out, not_400_out, not_401_out,
       not_402_out, not_403_out, not_404_out, not_405_out, not_406_out, not_407_out, not_408_out,
       not_409_out, not_410_out;

  not not_1 (not_1_out, OP4);
  not not_2 (not_2_out, OP3);
  not not_3 (not_3_out, OP2);
  not not_4 (not_4_out, OP4);
  not not_5 (not_5_out, OP2);
  not not_6 (not_6_out, OP4);
  not not_7 (not_7_out, OP2);
  not not_8 (not_8_out, OP1);
  not not_9 (not_9_out, OP5);
  not not_10 (not_10_out, OP4);
  not not_11 (not_11_out, OP2);
  not not_12 (not_12_out, OP1);
  not not_13 (not_13_out, OP0);
  not not_14 (not_14_out, OP5);
  not not_15 (not_15_out, OP4);
  not not_16 (not_16_out, OP1);
  not not_17 (not_17_out, OP0);
  not not_18 (not_18_out, OP5);
  not not_19 (not_19_out, OP4);
  not not_20 (not_20_out, OP2);
  not not_21 (not_21_out, OP1);
  not not_22 (not_22_out, OP5);
  not not_23 (not_23_out, OP4);
  not not_24 (not_24_out, OP2);
  not not_25 (not_25_out, OP0);
  not not_26 (not_26_out, OP5);
  not not_27 (not_27_out, OP4);
  not not_28 (not_28_out, OP1);
  not not_29 (not_29_out, OP4);
  not not_30 (not_30_out, OP3);
  not not_31 (not_31_out, OP2);
  not not_32 (not_32_out, OP4);
  not not_33 (not_33_out, OP2);
  not not_34 (not_34_out, OP4);
  not not_35 (not_35_out, OP2);
  not not_36 (not_36_out, OP1);
  not not_37 (not_37_out, OP5);
  not not_38 (not_38_out, OP4);
  not not_39 (not_39_out, OP3);
  not not_40 (not_40_out, OP2);
  not not_41 (not_41_out, OP1);
  not not_42 (not_42_out, OP0);
  not not_43 (not_43_out, F5);
  not not_44 (not_44_out, F4);
  not not_45 (not_45_out, F3);
  not not_46 (not_46_out, F2);
  not not_47 (not_47_out, F1);
  not not_48 (not_48_out, F0);
  not not_49 (not_49_out, OP5);
  not not_50 (not_50_out, OP4);
  not not_51 (not_51_out, OP3);
  not not_52 (not_52_out, OP2);
  not not_53 (not_53_out, OP1);
  not not_54 (not_54_out, OP0);
  not not_55 (not_55_out, F5);
  not not_56 (not_56_out, F4);
  not not_57 (not_57_out, F3);
  not not_58 (not_58_out, F2);
  not not_59 (not_59_out, OP5);
  not not_60 (not_60_out, OP4);
  not not_61 (not_61_out, OP3);
  not not_62 (not_62_out, OP2);
  not not_63 (not_63_out, OP1);
  not not_64 (not_64_out, OP0);
  not not_65 (not_65_out, F5);
  not not_66 (not_66_out, F4);
  not not_67 (not_67_out, F3);
  not not_68 (not_68_out, F2);
  not not_69 (not_69_out, F0);
  not not_70 (not_70_out, OP5);
  not not_71 (not_71_out, OP4);
  not not_72 (not_72_out, OP3);
  not not_73 (not_73_out, OP2);
  not not_74 (not_74_out, OP1);
  not not_75 (not_75_out, OP0);
  not not_76 (not_76_out, F4);
  not not_77 (not_77_out, F3);
  not not_78 (not_78_out, F2);
  not not_79 (not_79_out, F1);
  not not_80 (not_80_out, F0);
  not not_81 (not_81_out, OP5);
  not not_82 (not_82_out, OP4);
  not not_83 (not_83_out, OP3);
  not not_84 (not_84_out, OP2);
  not not_85 (not_85_out, OP1);
  not not_86 (not_86_out, OP0);
  not not_87 (not_87_out, F4);
  not not_88 (not_88_out, F3);
  not not_89 (not_89_out, F2);
  not not_90 (not_90_out, F1);
  not not_91 (not_91_out, OP5);
  not not_92 (not_92_out, OP4);
  not not_93 (not_93_out, OP3);
  not not_94 (not_94_out, OP2);
  not not_95 (not_95_out, OP1);
  not not_96 (not_96_out, OP0);
  not not_97 (not_97_out, F4);
  not not_98 (not_98_out, F3);
  not not_99 (not_99_out, F2);
  not not_100 (not_100_out, F0);
  not not_101 (not_101_out, OP5);
  not not_102 (not_102_out, OP4);
  not not_103 (not_103_out, OP3);
  not not_104 (not_104_out, OP2);
  not not_105 (not_105_out, OP1);
  not not_106 (not_106_out, OP0);
  not not_107 (not_107_out, F4);
  not not_108 (not_108_out, F3);
  not not_109 (not_109_out, F1);
  not not_110 (not_110_out, F0);
  not not_111 (not_111_out, OP5);
  not not_112 (not_112_out, OP4);
  not not_113 (not_113_out, OP3);
  not not_114 (not_114_out, OP2);
  not not_115 (not_115_out, OP1);
  not not_116 (not_116_out, OP0);
  not not_117 (not_117_out, F4);
  not not_118 (not_118_out, F3);
  not not_119 (not_119_out, F1);
  not not_120 (not_120_out, OP5);
  not not_121 (not_121_out, OP4);
  not not_122 (not_122_out, OP3);
  not not_123 (not_123_out, OP2);
  not not_124 (not_124_out, OP1);
  not not_125 (not_125_out, OP0);
  not not_126 (not_126_out, F4);
  not not_127 (not_127_out, F3);
  not not_128 (not_128_out, OP5);
  not not_129 (not_129_out, OP4);
  not not_130 (not_130_out, OP3);
  not not_131 (not_131_out, OP2);
  not not_132 (not_132_out, OP1);
  not not_133 (not_133_out, OP0);
  not not_134 (not_134_out, F4);
  not not_135 (not_135_out, F2);
  not not_136 (not_136_out, F0);
  not not_137 (not_137_out, OP5);
  not not_138 (not_138_out, OP4);
  not not_139 (not_139_out, OP3);
  not not_140 (not_140_out, OP2);
  not not_141 (not_141_out, OP1);
  not not_142 (not_142_out, OP0);
  not not_143 (not_143_out, F4);
  not not_144 (not_144_out, F2);
  not not_145 (not_145_out, OP5);
  not not_146 (not_146_out, OP4);
  not not_147 (not_147_out, OP3);
  not not_148 (not_148_out, OP2);
  not not_149 (not_149_out, OP5);
  not not_150 (not_150_out, OP4);
  not not_151 (not_151_out, OP2);
  not not_152 (not_152_out, OP1);
  not not_153 (not_153_out, OP0);
  not not_154 (not_154_out, OP5);
  not not_155 (not_155_out, OP4);
  not not_156 (not_156_out, OP1);
  not not_157 (not_157_out, OP0);
  not not_158 (not_158_out, OP5);
  not not_159 (not_159_out, OP4);
  not not_160 (not_160_out, OP2);
  not not_161 (not_161_out, OP1);
  not not_162 (not_162_out, OP5);
  not not_163 (not_163_out, OP4);
  not not_164 (not_164_out, OP2);
  not not_165 (not_165_out, OP0);
  not not_166 (not_166_out, OP5);
  not not_167 (not_167_out, OP4);
  not not_168 (not_168_out, OP1);
  not not_169 (not_169_out, OP4);
  not not_170 (not_170_out, OP3);
  not not_171 (not_171_out, OP2);
  not not_172 (not_172_out, OP5);
  not not_173 (not_173_out, OP4);
  not not_174 (not_174_out, OP3);
  not not_175 (not_175_out, OP2);
  not not_176 (not_176_out, OP1);
  not not_177 (not_177_out, OP0);
  not not_178 (not_178_out, F4);
  not not_179 (not_179_out, F3);
  not not_180 (not_180_out, F2);
  not not_181 (not_181_out, OP5);
  not not_182 (not_182_out, OP4);
  not not_183 (not_183_out, OP3);
  not not_184 (not_184_out, OP2);
  not not_185 (not_185_out, OP1);
  not not_186 (not_186_out, OP0);
  not not_187 (not_187_out, F4);
  not not_188 (not_188_out, F3);
  not not_189 (not_189_out, F0);
  not not_190 (not_190_out, OP5);
  not not_191 (not_191_out, OP4);
  not not_192 (not_192_out, OP3);
  not not_193 (not_193_out, OP2);
  not not_194 (not_194_out, OP1);
  not not_195 (not_195_out, OP0);
  not not_196 (not_196_out, F5);
  not not_197 (not_197_out, F4);
  not not_198 (not_198_out, F1);
  not not_199 (not_199_out, F0);
  not not_200 (not_200_out, OP5);
  not not_201 (not_201_out, OP4);
  not not_202 (not_202_out, OP3);
  not not_203 (not_203_out, OP1);
  not not_204 (not_204_out, OP0);
  not not_205 (not_205_out, OP5);
  not not_206 (not_206_out, OP4);
  not not_207 (not_207_out, OP3);
  not not_208 (not_208_out, OP1);
  not not_209 (not_209_out, OP5);
  not not_210 (not_210_out, OP4);
  not not_211 (not_211_out, OP2);
  not not_212 (not_212_out, OP1);
  not not_213 (not_213_out, OP0);
  not not_214 (not_214_out, OP5);
  not not_215 (not_215_out, OP4);
  not not_216 (not_216_out, OP2);
  not not_217 (not_217_out, OP1);
  not not_218 (not_218_out, OP5);
  not not_219 (not_219_out, OP4);
  not not_220 (not_220_out, OP2);
  not not_221 (not_221_out, OP0);
  not not_222 (not_222_out, OP4);
  not not_223 (not_223_out, OP2);
  not not_224 (not_224_out, OP1);
  not not_225 (not_225_out, OP5);
  not not_226 (not_226_out, OP4);
  not not_227 (not_227_out, OP3);
  not not_228 (not_228_out, OP2);
  not not_229 (not_229_out, OP1);
  not not_230 (not_230_out, OP5);
  not not_231 (not_231_out, OP4);
  not not_232 (not_232_out, OP3);
  not not_233 (not_233_out, OP2);
  not not_234 (not_234_out, OP1);
  not not_235 (not_235_out, OP0);
  not not_236 (not_236_out, F5);
  not not_237 (not_237_out, F4);
  not not_238 (not_238_out, F3);
  not not_239 (not_239_out, F2);
  not not_240 (not_240_out, F1);
  not not_241 (not_241_out, F0);
  not not_242 (not_242_out, OP5);
  not not_243 (not_243_out, OP4);
  not not_244 (not_244_out, OP3);
  not not_245 (not_245_out, OP2);
  not not_246 (not_246_out, OP1);
  not not_247 (not_247_out, OP0);
  not not_248 (not_248_out, F5);
  not not_249 (not_249_out, F4);
  not not_250 (not_250_out, F3);
  not not_251 (not_251_out, F2);
  not not_252 (not_252_out, OP5);
  not not_253 (not_253_out, OP4);
  not not_254 (not_254_out, OP3);
  not not_255 (not_255_out, OP2);
  not not_256 (not_256_out, OP1);
  not not_257 (not_257_out, OP0);
  not not_258 (not_258_out, F5);
  not not_259 (not_259_out, F4);
  not not_260 (not_260_out, F3);
  not not_261 (not_261_out, F2);
  not not_262 (not_262_out, F0);
  not not_263 (not_263_out, OP5);
  not not_264 (not_264_out, OP4);
  not not_265 (not_265_out, OP3);
  not not_266 (not_266_out, OP2);
  not not_267 (not_267_out, OP1);
  not not_268 (not_268_out, OP0);
  not not_269 (not_269_out, F4);
  not not_270 (not_270_out, F3);
  not not_271 (not_271_out, F2);
  not not_272 (not_272_out, F1);
  not not_273 (not_273_out, F0);
  not not_274 (not_274_out, OP5);
  not not_275 (not_275_out, OP4);
  not not_276 (not_276_out, OP3);
  not not_277 (not_277_out, OP2);
  not not_278 (not_278_out, OP1);
  not not_279 (not_279_out, OP0);
  not not_280 (not_280_out, F4);
  not not_281 (not_281_out, F3);
  not not_282 (not_282_out, F2);
  not not_283 (not_283_out, F1);
  not not_284 (not_284_out, OP5);
  not not_285 (not_285_out, OP4);
  not not_286 (not_286_out, OP3);
  not not_287 (not_287_out, OP2);
  not not_288 (not_288_out, OP1);
  not not_289 (not_289_out, OP0);
  not not_290 (not_290_out, F4);
  not not_291 (not_291_out, F3);
  not not_292 (not_292_out, F2);
  not not_293 (not_293_out, F0);
  not not_294 (not_294_out, OP5);
  not not_295 (not_295_out, OP4);
  not not_296 (not_296_out, OP3);
  not not_297 (not_297_out, OP2);
  not not_298 (not_298_out, OP1);
  not not_299 (not_299_out, OP0);
  not not_300 (not_300_out, F4);
  not not_301 (not_301_out, F3);
  not not_302 (not_302_out, F1);
  not not_303 (not_303_out, F0);
  not not_304 (not_304_out, OP5);
  not not_305 (not_305_out, OP4);
  not not_306 (not_306_out, OP3);
  not not_307 (not_307_out, OP2);
  not not_308 (not_308_out, OP1);
  not not_309 (not_309_out, OP0);
  not not_310 (not_310_out, F4);
  not not_311 (not_311_out, F3);
  not not_312 (not_312_out, F1);
  not not_313 (not_313_out, OP5);
  not not_314 (not_314_out, OP4);
  not not_315 (not_315_out, OP3);
  not not_316 (not_316_out, OP2);
  not not_317 (not_317_out, OP1);
  not not_318 (not_318_out, OP0);
  not not_319 (not_319_out, F4);
  not not_320 (not_320_out, F3);
  not not_321 (not_321_out, OP5);
  not not_322 (not_322_out, OP4);
  not not_323 (not_323_out, OP3);
  not not_324 (not_324_out, OP2);
  not not_325 (not_325_out, OP1);
  not not_326 (not_326_out, OP0);
  not not_327 (not_327_out, F4);
  not not_328 (not_328_out, F2);
  not not_329 (not_329_out, F0);
  not not_330 (not_330_out, OP5);
  not not_331 (not_331_out, OP4);
  not not_332 (not_332_out, OP3);
  not not_333 (not_333_out, OP2);
  not not_334 (not_334_out, OP1);
  not not_335 (not_335_out, OP0);
  not not_336 (not_336_out, F4);
  not not_337 (not_337_out, F2);
  not not_338 (not_338_out, OP5);
  not not_339 (not_339_out, OP4);
  not not_340 (not_340_out, OP3);
  not not_341 (not_341_out, OP2);
  not not_342 (not_342_out, OP1);
  not not_343 (not_343_out, OP0);
  not not_344 (not_344_out, F5);
  not not_345 (not_345_out, F4);
  not not_346 (not_346_out, F2);
  not not_347 (not_347_out, F1);
  not not_348 (not_348_out, F0);
  not not_349 (not_349_out, OP5);
  not not_350 (not_350_out, OP4);
  not not_351 (not_351_out, OP3);
  not not_352 (not_352_out, OP2);
  not not_353 (not_353_out, OP1);
  not not_354 (not_354_out, OP0);
  not not_355 (not_355_out, F4);
  not not_356 (not_356_out, F3);
  not not_357 (not_357_out, F2);
  not not_358 (not_358_out, OP5);
  not not_359 (not_359_out, OP4);
  not not_360 (not_360_out, OP3);
  not not_361 (not_361_out, OP2);
  not not_362 (not_362_out, OP1);
  not not_363 (not_363_out, OP0);
  not not_364 (not_364_out, F4);
  not not_365 (not_365_out, F3);
  not not_366 (not_366_out, F0);
  not not_367 (not_367_out, OP5);
  not not_368 (not_368_out, OP4);
  not not_369 (not_369_out, OP3);
  not not_370 (not_370_out, OP1);
  not not_371 (not_371_out, OP0);
  not not_372 (not_372_out, OP5);
  not not_373 (not_373_out, OP4);
  not not_374 (not_374_out, OP3);
  not not_375 (not_375_out, OP1);
  not not_376 (not_376_out, OP5);
  not not_377 (not_377_out, OP4);
  not not_378 (not_378_out, OP3);
  not not_379 (not_379_out, OP2);
  not not_380 (not_380_out, OP1);
  not not_381 (not_381_out, OP0);
  not not_382 (not_382_out, F5);
  not not_383 (not_383_out, F4);
  not not_384 (not_384_out, F2);
  not not_385 (not_385_out, F1);
  not not_386 (not_386_out, F0);
  not not_387 (not_387_out, OP5);
  not not_388 (not_388_out, OP4);
  not not_389 (not_389_out, OP3);
  not not_390 (not_390_out, OP2);
  not not_391 (not_391_out, OP1);
  not not_392 (not_392_out, OP0);
  not not_393 (not_393_out, F5);
  not not_394 (not_394_out, F4);
  not not_395 (not_395_out, F2);
  not not_396 (not_396_out, F1);
  not not_397 (not_397_out, F0);
  not not_398 (not_398_out, OP5);
  not not_399 (not_399_out, OP4);
  not not_400 (not_400_out, OP3);
  not not_401 (not_401_out, OP2);
  not not_402 (not_402_out, OP0);
  not not_403 (not_403_out, OP5);
  not not_404 (not_404_out, OP4);
  not not_405 (not_405_out, OP3);
  not not_406 (not_406_out, OP2);
  not not_407 (not_407_out, OP5);
  not not_408 (not_408_out, OP4);
  not not_409 (not_409_out, OP3);
  not not_410 (not_410_out, OP2);
  and and_1 (MemToReg, OP5, not_1_out, not_2_out, not_3_out, OP1, OP0);
  and and_2 (and_2_out, OP5, not_4_out, OP3, not_5_out, OP1, OP0);
  and and_3 (and_3_out, OP5, not_6_out, OP3, not_7_out, not_8_out, OP0);
  and and_4 (and_4_out, not_9_out, not_10_out, OP3, not_11_out, not_12_out, not_13_out);
  and and_5 (and_5_out, not_14_out, not_15_out, OP3, OP2, not_16_out, not_17_out);
  and and_6 (and_6_out, not_18_out, not_19_out, OP3, not_20_out, not_21_out, OP0);
  and and_7 (and_7_out, not_22_out, not_23_out, OP3, not_24_out, OP1, not_25_out);
  and and_8 (and_8_out, not_26_out, not_27_out, OP3, OP2, not_28_out, OP0);
  and and_9 (and_9_out, OP5, not_29_out, not_30_out, not_31_out, OP1, OP0);
  and and_10 (and_10_out, OP5, not_32_out, OP3, not_33_out, OP1, OP0);
  and and_11 (and_11_out, OP5, not_34_out, OP3, not_35_out, not_36_out, OP0);
  and and_12 (and_12_out, not_37_out, not_38_out, not_39_out, not_40_out, not_41_out, not_42_out, not_43_out, not_44_out, not_45_out, not_46_out, not_47_out, not_48_out);
  and and_13 (and_13_out, not_49_out, not_50_out, not_51_out, not_52_out, not_53_out, not_54_out, not_55_out, not_56_out, not_57_out, not_58_out, F1, F0);
  and and_14 (and_14_out, not_59_out, not_60_out, not_61_out, not_62_out, not_63_out, not_64_out, not_65_out, not_66_out, not_67_out, not_68_out, F1, not_69_out);
  and and_15 (and_15_out, not_70_out, not_71_out, not_72_out, not_73_out, not_74_out, not_75_out, F5, not_76_out, not_77_out, not_78_out, not_79_out, not_80_out);
  and and_16 (and_16_out, not_81_out, not_82_out, not_83_out, not_84_out, not_85_out, not_86_out, F5, not_87_out, not_88_out, not_89_out, not_90_out, F0);
  and and_17 (and_17_out, not_91_out, not_92_out, not_93_out, not_94_out, not_95_out, not_96_out, F5, not_97_out, not_98_out, not_99_out, F1, not_100_out);
  and and_18 (and_18_out, not_101_out, not_102_out, not_103_out, not_104_out, not_105_out, not_106_out, F5, not_107_out, not_108_out, F2, not_109_out, not_110_out);
  and and_19 (and_19_out, not_111_out, not_112_out, not_113_out, not_114_out, not_115_out, not_116_out, F5, not_117_out, not_118_out, F2, not_119_out, F0);
  and and_20 (and_20_out, not_120_out, not_121_out, not_122_out, not_123_out, not_124_out, not_125_out, F5, not_126_out, not_127_out, F2, F1, F0);
  and and_21 (and_21_out, not_128_out, not_129_out, not_130_out, not_131_out, not_132_out, not_133_out, F5, not_134_out, F3, not_135_out, F1, not_136_out);
  and and_22 (and_22_out, not_137_out, not_138_out, not_139_out, not_140_out, not_141_out, not_142_out, F5, not_143_out, F3, not_144_out, F1, F0);
  and and_23 (and_23_out, not_145_out, not_146_out, not_147_out, not_148_out, OP1, OP0);
  and and_24 (and_24_out, not_149_out, not_150_out, OP3, not_151_out, not_152_out, not_153_out);
  and and_25 (and_25_out, not_154_out, not_155_out, OP3, OP2, not_156_out, not_157_out);
  and and_26 (and_26_out, not_158_out, not_159_out, OP3, not_160_out, not_161_out, OP0);
  and and_27 (and_27_out, not_162_out, not_163_out, OP3, not_164_out, OP1, not_165_out);
  and and_28 (and_28_out, not_166_out, not_167_out, OP3, OP2, not_168_out, OP0);
  and and_29 (and_29_out, OP5, not_169_out, not_170_out, not_171_out, OP1, OP0);
  and and_30 (and_30_out, not_172_out, not_173_out, not_174_out, not_175_out, not_176_out, not_177_out, F5, not_178_out, not_179_out, not_180_out, F1, F0);
  and and_31 (and_31_out, not_181_out, not_182_out, not_183_out, not_184_out, not_185_out, not_186_out, F5, not_187_out, not_188_out, F2, F1, not_189_out);
  and and_32 (SysCALL, not_190_out, not_191_out, not_192_out, not_193_out, not_194_out, not_195_out, not_196_out, not_197_out, F3, F2, not_198_out, not_199_out);
  and and_33 (and_33_out, not_200_out, not_201_out, not_202_out, OP2, not_203_out, not_204_out);
  and and_34 (and_34_out, not_205_out, not_206_out, not_207_out, OP2, not_208_out, OP0);
  and and_35 (and_35_out, not_209_out, not_210_out, OP3, not_211_out, not_212_out, not_213_out);
  and and_36 (and_36_out, not_214_out, not_215_out, OP3, not_216_out, not_217_out, OP0);
  and and_37 (and_37_out, not_218_out, not_219_out, OP3, not_220_out, OP1, not_221_out);
  and and_38 (and_38_out, OP5, not_222_out, OP3, not_223_out, not_224_out, OP0);
  and and_39 (and_39_out, not_225_out, not_226_out, not_227_out, not_228_out, not_229_out, OP0);
  and and_40 (and_40_out, not_230_out, not_231_out, not_232_out, not_233_out, not_234_out, not_235_out, not_236_out, not_237_out, not_238_out, not_239_out, not_240_out, not_241_out);
  and and_41 (and_41_out, not_242_out, not_243_out, not_244_out, not_245_out, not_246_out, not_247_out, not_248_out, not_249_out, not_250_out, not_251_out, F1, F0);
  and and_42 (and_42_out, not_252_out, not_253_out, not_254_out, not_255_out, not_256_out, not_257_out, not_258_out, not_259_out, not_260_out, not_261_out, F1, not_262_out);
  and and_43 (and_43_out, not_263_out, not_264_out, not_265_out, not_266_out, not_267_out, not_268_out, F5, not_269_out, not_270_out, not_271_out, not_272_out, not_273_out);
  and and_44 (and_44_out, not_274_out, not_275_out, not_276_out, not_277_out, not_278_out, not_279_out, F5, not_280_out, not_281_out, not_282_out, not_283_out, F0);
  and and_45 (and_45_out, not_284_out, not_285_out, not_286_out, not_287_out, not_288_out, not_289_out, F5, not_290_out, not_291_out, not_292_out, F1, not_293_out);
  and and_46 (and_46_out, not_294_out, not_295_out, not_296_out, not_297_out, not_298_out, not_299_out, F5, not_300_out, not_301_out, F2, not_302_out, not_303_out);
  and and_47 (and_47_out, not_304_out, not_305_out, not_306_out, not_307_out, not_308_out, not_309_out, F5, not_310_out, not_311_out, F2, not_312_out, F0);
  and and_48 (and_48_out, not_313_out, not_314_out, not_315_out, not_316_out, not_317_out, not_318_out, F5, not_319_out, not_320_out, F2, F1, F0);
  and and_49 (and_49_out, not_321_out, not_322_out, not_323_out, not_324_out, not_325_out, not_326_out, F5, not_327_out, F3, not_328_out, F1, not_329_out);
  and and_50 (and_50_out, not_330_out, not_331_out, not_332_out, not_333_out, not_334_out, not_335_out, F5, not_336_out, F3, not_337_out, F1, F0);
  and and_51 (and_51_out, not_338_out, not_339_out, not_340_out, not_341_out, not_342_out, not_343_out, not_344_out, not_345_out, F3, not_346_out, not_347_out, not_348_out);
  and and_52 (and_52_out, not_349_out, not_350_out, not_351_out, not_352_out, not_353_out, not_354_out, F5, not_355_out, not_356_out, not_357_out, F1, F0);
  and and_53 (and_53_out, not_358_out, not_359_out, not_360_out, not_361_out, not_362_out, not_363_out, F5, not_364_out, not_365_out, F2, F1, not_366_out);
  and and_54 (BEQ, not_367_out, not_368_out, not_369_out, OP2, not_370_out, not_371_out);
  and and_55 (BNE, not_372_out, not_373_out, not_374_out, OP2, not_375_out, OP0);
  and and_56 (JR, not_376_out, not_377_out, not_378_out, not_379_out, not_380_out, not_381_out, not_382_out, not_383_out, F3, not_384_out, not_385_out, not_386_out);
  and and_57 (and_57_out, not_387_out, not_388_out, not_389_out, not_390_out, not_391_out, not_392_out, not_393_out, not_394_out, F3, not_395_out, not_396_out, not_397_out);
  and and_58 (and_58_out, not_398_out, not_399_out, not_400_out, not_401_out, OP1, not_402_out);
  and and_59 (and_59_out, not_403_out, not_404_out, not_405_out, not_406_out, OP1, OP0);
  and and_60 (JAL, not_407_out, not_408_out, not_409_out, not_410_out, OP1, OP0);
  or or_1 (MemWrite, and_2_out, and_3_out);
  or or_2 (ALU_SRC, and_4_out, and_5_out, and_6_out, and_7_out, and_8_out, and_9_out, and_10_out, and_11_out);
  or or_3 (SignedExt, and_33_out, and_34_out, and_35_out, and_36_out, and_37_out, and_38_out, and_39_out);
  or or_4 (JMP, and_57_out, and_58_out, and_59_out);
  or or_5 (RegWrite, and_12_out, and_13_out, and_14_out, and_15_out, and_16_out, and_17_out, and_18_out, and_19_out, and_20_out, and_21_out, and_22_out, and_23_out, and_24_out, and_25_out, and_26_out, and_27_out, and_28_out, and_29_out, and_30_out, and_31_out);
  or or_6 (RegDst, and_40_out, and_41_out, and_42_out, and_43_out, and_44_out, and_45_out, and_46_out, and_47_out, and_48_out, and_49_out, and_50_out, and_51_out, and_52_out, and_53_out);
endmodule

// ALU
module MIPS_ALU (
  input  [4:0] shamt,
  input  [31:0] X,
  input  [31:0] Y,
  input  [3:0] AluOP,
  output Equal,
  output [31:0] Result,
  output [31:0] Result_2
);

  wire [0:0] comparator_1_lt, comparator_2_lt;
  wire [31:0] adder_1_out, AND_out, divider_1_out, divider_1_rem, multiplier_1_cout, multiplier_1_out,
       NOR_out, OR_out, shifter_1_out, shifter_2_out, shifter_3_out, subtractor_1_out, XOR_out;

  assign AND_out = X & Y;  // AND_Gate AND, 32 bits wide
  assign OR_out = X | Y;  // OR_Gate OR, 32 bits wide
  Shifter #(.width(32)) shifter_1 (.in(Y), .\dist (shamt), .out(shifter_1_out));
  Shifter #(.width(32), .shift("ar")) shifter_2 (.in(Y), .\dist (shamt), .out(shifter_2_out));
  Shifter #(.width(32), .shift("lr")) shifter_3 (.in(Y), .\dist (shamt), .out(shifter_3_out));
  Multiplier #(.width(32)) multiplier_1 (.a(X), .b(Y), .out(multiplier_1_out), .cout(multiplier_1_cout));  // open: cin
  Divider #(.width(32)) divider_1 (.a(X), .b(Y), .out(divider_1_out), .rem(divider_1_rem));  // open: upper
  Adder #(.width(32)) adder_1 (.a(X), .b(Y), .out(adder_1_out));  // open: cin, cout
  Subtractor #(.width(32)) subtractor_1 (.a(X), .b(Y), .out(subtractor_1_out));  // open: bin, bout
  assign XOR_out = X ^ Y;  // XOR_Gate XOR, 32 bits wide
  assign NOR_out = ~(X | Y);  // NOR_Gate NOR, 32 bits wide
  Comparator #(.width(32)) comparator_1 (.a(X), .b(Y), .eq(Equal), .lt(comparator_1_lt[0]));  // open: gt
  Comparator #(.width(32), .mode("unsigned")) comparator_2 (.a(X), .b(Y), .lt(comparator_2_lt[0]));  // open: gt, eq
  Multiplexer #(.select(4), .width(32), .enable("false")) multiplexer_1 (
    .in0(shifter_1_out), .in1(shifter_2_out), .in2(shifter_3_out), .in3(multiplier_1_out),
    .in4(divider_1_out), .in5(adder_1_out), .in6(subtractor_1_out), .in7(AND_out), .in8(OR_out),
    .in9(XOR_out), .in10(NOR_out), .in11({{31{1'b0}}, comparator_1_lt[0]}),
    .in12({{31{1'b0}}, comparator_2_lt[0]}), .in13({32{1'b0}}), .in14({32{1'b0}}), .in15({32{1'b0}}),
    .out(Result), .sel(AluOP));
  Multiplexer #(.select(4), .width(32), .enable("false")) multiplexer_2 (
    .in0({32{1'b0}}), .in1({32{1'b0}}), .in2({32{1'b0}}), .in3(multiplier_1_cout), .in4(divider_1_rem),
    .in5({32{1'b0}}), .in6({32{1'b0}}), .in7({32{1'b0}}), .in8({32{1'b0}}), .in9({32{1'b0}}),
    .in10({32{1'b0}}), .in11({32{1'b0}}), .in12({32{1'b0}}), .in13({32{1'b0}}), .in14({32{1'b0}}),
    .in15({32{1'b0}}), .out(Result_2), .sel(AluOP));

  // Other names for the same wires on the sheet: Result2[31:0] = Result_2; S[3:0] = AluOP

  // Notes on the sheet:
  //   不要改变此引脚区域内容，也不要改变ALU封装形式
  //   输入引脚
  //   输出引脚
endmodule

module MIPS_Regifile (
  input  [31:0] Din,
  input  Clk,
  input  WE,
  input  [4:0] R1_num,
  input  [4:0] W_num,
  input  [4:0] R2_num,
  output [31:0] R1,
  output [31:0] R2
);

  // RegisterFile registerfile_1: pin names not known; wires that end beside it: Din, Clk, WE, W_num, R1_num, R2_num, R1, R2
endmodule

module \理想流水线  (
);

  wire and_1_out, and_2_out, and_3_out, and_4_out, and_5_out, CLK, comparator_1_eq, comparator_2_lt,
       ex_mem_1_dout_1, ex_mem_1_dout_1_2, ex_mem_1_dout_1_3, ex_mem_1_dout_1_4, ex_mem_1_dout_1_5,
       ex_mem_1_dout_1_6, ex_mem_1_dout_1_7, \ex_mem_1_传输状态out_表明当前传输数据有效 , Go, \id_ex_1_传输状态out_表明当前传输数据有效 ,
       \if_id_1_传输状态out_表明当前传输数据有效 , IR1, IR2, IR3, mem_wb_1_dout_1, mem_wb_1_dout_1_2, mem_wb_1_dout_1_3,
       mem_wb_1_dout_1_4, mem_wb_1_dout_1_5, mips_alu_1_equal, nor_1_out, not_1_out, not_2_out, not_3_out,
       not_4_out, not_5_out, or_1_out, or_2_out, or_3_out, register_1_q, RST, W1, W2, W3, \硬布线控制器_1_regdst ,
       \硬布线控制器_1_signedext ;
  wire [3:0] id_ex_1_dout_4, id_ex_1_dout_4_2, id_ex_1_dout_4_3, id_ex_1_dout_4_4, multiplexer_13_out,
       multiplexer_14_out, \硬布线控制器_1_alu_op , \硬布线控制器_1_alu_src , \硬布线控制器_1_beq , \硬布线控制器_1_bltz ;
  wire [4:0] ex_mem_1_dout_5, id_ex_1_dout_5, id_ex_1_dout_5_2, mem_wb_1_dout_5, multiplexer_2_out,
       multiplexer_3_out, multiplexer_4_out, multiplexer_6_out;
  wire [11:0] EX_PC, ID_PC, IF_PC, MEM_PC, WB_PC;
  wire [15:0] \LoadUse次数 , \总周期数 , \插入气泡数 , \无条件分支数 , \条件分支成功数 ;
  wire [31:0] adder_1_out, adder_2_out, bit_extender_1_out, bit_extender_2_out, bit_extender_3_out,
       ex_mem_1_dout_32, ex_mem_1_dout_32_2, ex_mem_1_dout_32_3, ex_mem_1_dout_32_4, id_ex_1_dout_32,
       id_ex_1_dout_32_2, id_ex_1_dout_32_3, id_ex_1_dout_32_4, id_ex_1_dout_32_5, if_id_1_dout_ins,
       if_id_1_dout_pc_4, LedData, mem_wb_1_dout_32_2, mem_wb_1_dout_32_3, mem_wb_1_dout_32_4,
       mips_alu_1_result, mips_ram_1_p8, mips_regifile_1_r1, mips_regifile_1_r2, multiplexer_1_out,
       multiplexer_5_out, multiplexer_7_out, multiplexer_8_out, multiplexer_9_out, multiplexer_10_out,
       multiplexer_11_out, multiplexer_12_out, multiplexer_15_out, multiplexer_16_out, PC_q, register_2_q,
       rom_1_data, shifter_1_out, shifter_2_out;

  Button \u_总复位  (.out(RST));
  Button _1 (.out(IR1));
  Button _2 (.out(IR2));
  Button _3 (.out(IR3));
  and and_1 (and_1_out, mem_wb_1_dout_1_2, not_1_out);
  not not_1 (not_1_out, mem_wb_1_dout_1);
  Button \u_继续运行  (.out(Go));
  LED led_1 (.in(W1));
  LED led_2 (.in(W2));
  LED led_3 (.in(W3));
  Counter #(.width(16), .max('hffff)) counter_1 (
    .count(not_2_out), .Q(\总周期数 ), .clk(CLK), .clr(RST));  // open: load, D, carry
  Register #(.width(32)) PC (.D(multiplexer_1_out), .en(not_2_out), .Q(PC_q), .clk(CLK), .clr(RST));
  Register #(.width(1)) register_1 (.D(mem_wb_1_dout_1_2), .en(and_1_out), .Q(register_1_q), .clk(CLK), .clr(or_1_out));
  or or_1 (or_1_out, Go, RST);
  Hex_Digit_Display hex_digit_display_1 (.value(LedData[31:28]));  // open: dp
  Adder #(.width(32)) adder_1 (.a(PC_q), .b(32'h4), .out(adder_1_out));  // open: cin, cout
  not not_2 (not_2_out, register_1_q);
  Multiplexer #(.width(32), .enable("false")) multiplexer_1 (
    .in0(adder_1_out), .in1(multiplexer_10_out), .out(multiplexer_1_out), .sel(or_3_out));
  Hex_Digit_Display hex_digit_display_2 (.value(LedData[27:24]));  // open: dp
  Hex_Digit_Display hex_digit_display_3 (.value(LedData[23:20]));  // open: dp
  Hex_Digit_Display hex_digit_display_4 (.value(LedData[19:16]));  // open: dp
  Hex_Digit_Display hex_digit_display_5 (.value(LedData[15:12]));  // open: dp
  ROM #(.addrWidth(10), .dataWidth(32)) rom_1 (.addr(PC_q[11:2]), .data(rom_1_data));  // open: sel
  IF_ID if_id_1 (
    .Din_Ins(rom_1_data), .Din_PC_4(adder_1_out), .\传输状态In_表明当前传输数据有效 (1'b1), .CLK(CLK),
    .Dout_Ins(if_id_1_dout_ins), .Dout_PC_4(if_id_1_dout_pc_4),
    .\传输状态Out_表明当前传输数据有效 (\if_id_1_传输状态out_表明当前传输数据有效 ), .\同步清零_气泡_高电平有效 (1'b0),
    .\使能端_低电平有效_stall_高电平有效 (1'b0));  // open: Din_PC, Dout_PC, Din_Status, Dout_Status, Din_Addr, Dout_Addr, Din_Miss, Dout_Miss, Din_Hit, Dout_Hit
  Hex_Digit_Display hex_digit_display_6 (.value(LedData[11:8]));  // open: dp
  Hex_Digit_Display hex_digit_display_7 (.value(LedData[7:4]));  // open: dp
  Clock clock_1 (.out(CLK));
  Hex_Digit_Display hex_digit_display_8 (.value(LedData[3:0]));  // open: dp
  \硬布线控制器  \u_硬布线控制器_1  (
    .Func(if_id_1_dout_ins[5:0]), .OP(if_id_1_dout_ins[31:26]), .ALU_OP(\硬布线控制器_1_alu_op ),
    .MemToReg(\硬布线控制器_1_beq [2]), .MemWrite(\硬布线控制器_1_beq [3]), .ALU_SRC(\硬布线控制器_1_alu_src [0]),
    .RegWrite(\硬布线控制器_1_alu_src [1]), .SysCALL(\硬布线控制器_1_alu_src [3]), .SignedExt(\硬布线控制器_1_signedext ),
    .RegDst(\硬布线控制器_1_regdst ), .JR(\硬布线控制器_1_bltz [2]), .JMP(\硬布线控制器_1_bltz [3]), .Beq(\硬布线控制器_1_beq [0]),
    .JAL(\硬布线控制器_1_alu_src [2]), .Bne(\硬布线控制器_1_beq [1]), .SH(\硬布线控制器_1_bltz [1]), .BLTZ(\硬布线控制器_1_bltz [0]));  // open: ERET, MF, MFC0, MTC0
  Multiplexer #(.width(5), .enable("false")) multiplexer_2 (
    .in0(if_id_1_dout_ins[20:16]), .in1(if_id_1_dout_ins[15:11]), .out(multiplexer_2_out),
    .sel(\硬布线控制器_1_regdst ));
  assign bit_extender_1_out = {{16{1'b0}}, if_id_1_dout_ins[15:0]};  // Bit_Extender bit_extender_1
  assign bit_extender_2_out = {{16{if_id_1_dout_ins[15]}}, if_id_1_dout_ins[15:0]};  // Bit_Extender bit_extender_2
  assign bit_extender_3_out = {{6{if_id_1_dout_ins[25]}}, if_id_1_dout_ins[25:0]};  // Bit_Extender bit_extender_3
  Multiplexer #(.width(5), .enable("false")) multiplexer_3 (
    .in0(if_id_1_dout_ins[25:21]), .in1(5'b00100), .out(multiplexer_3_out), .sel(\硬布线控制器_1_alu_src [3]));
  Multiplexer #(.width(5), .enable("false")) multiplexer_4 (
    .in0(multiplexer_2_out), .in1({5{1'b1}}), .out(multiplexer_4_out), .sel(\硬布线控制器_1_alu_src [2]));
  Multiplexer #(.width(32), .enable("false")) multiplexer_5 (
    .in0(bit_extender_1_out), .in1(bit_extender_2_out), .out(multiplexer_5_out), .sel(\硬布线控制器_1_signedext ));
  // Probe on \总周期数 
  // Probe on \无条件分支数 
  // Probe on \条件分支成功数 
  // Probe on \插入气泡数 
  // Probe on \LoadUse次数 
  Multiplexer #(.width(5), .enable("false")) multiplexer_6 (
    .in0(if_id_1_dout_ins[20:16]), .in1(5'b00010), .out(multiplexer_6_out), .sel(\硬布线控制器_1_alu_src [3]));
  // Probe on IF_PC
  MIPS_Regifile mips_regifile_1 (
    .Din(multiplexer_16_out), .Clk(CLK), .R1(mips_regifile_1_r1), .R2(mips_regifile_1_r2),
    .WE(mem_wb_1_dout_1_4), .W_num(mem_wb_1_dout_5), .R1_num(multiplexer_3_out), .R2_num(multiplexer_6_out));
  // Probe on ID_PC
  ID_EX id_ex_1 (
    .Din_4(\硬布线控制器_1_bltz ), .Din_4_2(\硬布线控制器_1_beq ), .Din_4_3(\硬布线控制器_1_alu_op ),
    .Din_4_4(\硬布线控制器_1_alu_src ), .Din_32(mips_regifile_1_r1), .Din_32_2(mips_regifile_1_r2),
    .Din_32_3(multiplexer_5_out), .Din_32_4(bit_extender_3_out), .Din_5(if_id_1_dout_ins[10:6]),
    .Din_32_5(if_id_1_dout_pc_4), .\传输状态In_表明当前传输数据有效 (\if_id_1_传输状态out_表明当前传输数据有效 ), .CLK(CLK),
    .Dout_4(id_ex_1_dout_4), .Dout_4_2(id_ex_1_dout_4_2), .Dout_4_3(id_ex_1_dout_4_3),
    .Dout_4_4(id_ex_1_dout_4_4), .Dout_32(id_ex_1_dout_32), .Dout_32_2(id_ex_1_dout_32_2),
    .Dout_32_3(id_ex_1_dout_32_3), .Dout_32_4(id_ex_1_dout_32_4), .Dout_5(id_ex_1_dout_5),
    .Dout_32_5(id_ex_1_dout_32_5), .\传输状态Out_表明当前传输数据有效 (\id_ex_1_传输状态out_表明当前传输数据有效 ),
    .\同步清零_气泡_高电平有效 (1'b0), .\使能端_低电平有效_stall_高电平有效 (1'b0), .Din_5_2(multiplexer_4_out),
    .Dout_5_2(id_ex_1_dout_5_2));  // open: Din_32_6, Dout_32_6, Din_2, Dout_2, Din_2_2, Dout_2_2, Din_2_3, Dout_2_3, Din_32_7, Dout_32_7, Din_1, Dout_1, Din_1_2, Dout_1_2
  // Probe on EX_PC
  // Probe on MEM_PC
  and and_2 (and_2_out, comparator_1_eq, id_ex_1_dout_4_4[3]);
  // Probe on WB_PC
  Register #(.width(32)) register_2 (.D(id_ex_1_dout_32), .en(and_2_out), .Q(register_2_q), .clk(CLK), .clr(RST));
  Comparator #(.width(32)) comparator_1 (.a(32'h22), .b(id_ex_1_dout_32_2), .eq(comparator_1_eq));  // open: gt, lt
  Multiplexer #(.width(32), .enable("false")) multiplexer_7 (
    .in0(id_ex_1_dout_32_2), .in1(id_ex_1_dout_32_3), .out(multiplexer_7_out), .sel(id_ex_1_dout_4_4[0]));
  Shifter #(.width(32)) shifter_1 (.in(id_ex_1_dout_32_3), .\dist (5'b00010), .out(shifter_1_out));
  Shifter #(.width(32)) shifter_2 (.in(id_ex_1_dout_32_4), .\dist (5'b00010), .out(shifter_2_out));
  MIPS_ALU mips_alu_1 (
    .X(id_ex_1_dout_32), .Y(multiplexer_7_out), .AluOP(id_ex_1_dout_4_3), .Equal(mips_alu_1_equal),
    .Result(mips_alu_1_result), .shamt(id_ex_1_dout_5));  // open: Result_2
  not not_3 (not_3_out, mips_alu_1_equal);
  Adder #(.width(32)) adder_2 (.a(shifter_1_out), .b(id_ex_1_dout_32_5), .out(adder_2_out));  // open: cin, cout
  and and_3 (and_3_out, id_ex_1_dout_4_2[0], mips_alu_1_equal);
  or or_2 (or_2_out, and_3_out, and_4_out);
  and and_4 (and_4_out, id_ex_1_dout_4_2[1], not_3_out);
  Comparator #(.width(32)) comparator_2 (.a(id_ex_1_dout_32), .b({32{1'b0}}), .lt(comparator_2_lt));  // open: gt, eq
  not not_4 (not_4_out, id_ex_1_dout_4[2]);
  and and_5 (and_5_out, id_ex_1_dout_4[0], comparator_2_lt);
  nor nor_1 (nor_1_out, and_5_out, or_2_out);
  Multiplexer #(.width(32), .enable("false")) multiplexer_8 (
    .in0(adder_2_out), .in1(id_ex_1_dout_32_5), .out(multiplexer_8_out), .sel(nor_1_out));
  not not_5 (not_5_out, id_ex_1_dout_4[3]);
  Multiplexer #(.width(32), .enable("false")) multiplexer_9 (
    .in0(id_ex_1_dout_32), .in1(shifter_2_out), .out(multiplexer_9_out), .sel(not_4_out));
  or or_3 (or_3_out, and_5_out, or_2_out, id_ex_1_dout_4[3]);
  Multiplexer #(.width(32), .enable("false")) multiplexer_10 (
    .in0(multiplexer_9_out), .in1(multiplexer_8_out), .out(multiplexer_10_out), .sel(not_5_out));
  EX_MEM ex_mem_1 (
    .Din_1_4(id_ex_1_dout_4_2[2]), .Din_1_5(id_ex_1_dout_4_2[3]), .Din_32_2(mips_alu_1_result),
    .Din_32_3(id_ex_1_dout_32_2), .Din_32_4(id_ex_1_dout_32_5),
    .\传输状态In_表明当前传输数据有效 (\id_ex_1_传输状态out_表明当前传输数据有效 ), .CLK(CLK), .Dout_1_4(ex_mem_1_dout_1_4),
    .Dout_1_5(ex_mem_1_dout_1_5), .Dout_32_2(ex_mem_1_dout_32_2), .Dout_32_3(ex_mem_1_dout_32_3),
    .Dout_32_4(ex_mem_1_dout_32_4), .\传输状态Out_表明当前传输数据有效 (\ex_mem_1_传输状态out_表明当前传输数据有效 ),
    .\同步清零_气泡_高电平有效 (1'b0), .\使能端_低电平有效_stall_高电平有效 (1'b0), .Din_1_6(id_ex_1_dout_4_4[1]),
    .Dout_1_6(ex_mem_1_dout_1_6), .Din_1_7(id_ex_1_dout_4_4[2]), .Dout_1_7(ex_mem_1_dout_1_7),
    .Din_32(register_2_q), .Dout_32(ex_mem_1_dout_32), .Dout_1_3(ex_mem_1_dout_1_3),
    .Din_1_3(id_ex_1_dout_4_4[3]), .Din_1_2(comparator_1_eq), .Dout_1_2(ex_mem_1_dout_1_2),
    .Din_1(id_ex_1_dout_4[1]), .Dout_1(ex_mem_1_dout_1), .Din_5(id_ex_1_dout_5_2), .Dout_5(ex_mem_1_dout_5));  // open: Din_32_5, Dout_32_5, Din_1_8, Dout_1_8, Din_1_9, Dout_1_9, Dout_32_6, Dout_32_7, Din_32_6, Din_32_7, Din_1_10, Dout_1_10
  Multiplexer #(.width(32), .enable("false")) multiplexer_11 (
    .in0(ex_mem_1_dout_32_3), .in1(multiplexer_12_out), .out(multiplexer_11_out), .sel(ex_mem_1_dout_1));
  Multiplexer #(.width(32), .enable("false")) multiplexer_12 (
    .in0({{16{1'b0}}, ex_mem_1_dout_32_3[15:0]}), .in1({ex_mem_1_dout_32_3[15:0], {16{1'b0}}}),
    .out(multiplexer_12_out), .sel(ex_mem_1_dout_32_2[1]));
  Multiplexer #(.width(4), .enable("false")) multiplexer_13 (
    .in0(4'b1111), .in1(multiplexer_14_out), .out(multiplexer_13_out), .sel(ex_mem_1_dout_1));
  Multiplexer #(.width(4), .enable("false")) multiplexer_14 (
    .in0(4'b0011), .in1(4'b1100), .out(multiplexer_14_out), .sel(ex_mem_1_dout_32_2[1]));
  MEM_WB mem_wb_1 (
    .Din_1_4(ex_mem_1_dout_1_6), .Din_1_5(ex_mem_1_dout_1_7), .Din_32(ex_mem_1_dout_32),
    .Din_32_3(mips_ram_1_p8), .Din_32_4(ex_mem_1_dout_32_4),
    .\传输状态In_表明当前传输数据有效 (\ex_mem_1_传输状态out_表明当前传输数据有效 ), .CLK(CLK), .Dout_1_4(mem_wb_1_dout_1_4),
    .Dout_1_5(mem_wb_1_dout_1_5), .Dout_32(LedData), .Dout_32_3(mem_wb_1_dout_32_3),
    .Dout_32_4(mem_wb_1_dout_32_4), .\同步清零_气泡_高电平有效 (1'b0), .\使能端_低电平有效_stall_高电平有效 (1'b0),
    .Dout_1(mem_wb_1_dout_1), .Dout_1_2(mem_wb_1_dout_1_2), .Din_1(ex_mem_1_dout_1_2),
    .Din_1_2(ex_mem_1_dout_1_3), .Din_5(ex_mem_1_dout_5), .Dout_5(mem_wb_1_dout_5),
    .Din_1_3(ex_mem_1_dout_1_4), .Dout_1_3(mem_wb_1_dout_1_3), .Din_32_2(ex_mem_1_dout_32_2),
    .Dout_32_2(mem_wb_1_dout_32_2));  // open: 传输状态Out_表明当前传输数据有效, Din_32_5, Dout_32_5, Din_1_6, Dout_1_6, Din_1_7, Dout_1_7, Din_32_6, Dout_32_6, Din_32_7, Dout_32_7, Din_1_8, Dout_1_8
  // MIPS_RAM mips_ram_1: pin names not known; wires that end beside it: ex_mem_1_dout_32_2[11:2], multiplexer_11_out, ex_mem_1_dout_1_5, multiplexer_13_out, CLK, 1'b1, RST, mips_ram_1_p8
  Multiplexer #(.width(32), .enable("false")) multiplexer_15 (
    .in0(mem_wb_1_dout_32_2), .in1(mem_wb_1_dout_32_3), .out(multiplexer_15_out), .sel(mem_wb_1_dout_1_3));
  Multiplexer #(.width(32), .enable("false")) multiplexer_16 (
    .in0(multiplexer_15_out), .in1(mem_wb_1_dout_32_4), .out(multiplexer_16_out), .sel(mem_wb_1_dout_1_5));

  // Notes on the sheet:
  //   中断源
  //   中断等待指示
  //   指令字
  //   指令存储器
  //   数码管输出
  //   IF/ID
  //   contents of rom_1 (hex, n*v repeats v):
  //   20100000 20110000 20120000 20130000 36100000 36310001 36520002 36730003 ae100000 ae110004 ae120008
  //   ae13000c 2002000a 20110000 20120000 20130000 c
  //   JMP
  //   JR
  //   SH
  //   Bltz
  //   OP
  //   Func
  //   rs
  //   rt
  //   rd
  //   Beq
  //   Bne
  //   MemToReg
  //   MemWrite
  //   AluOP
  //   AluSrcB
  //   RegWrite
  //   JAL
  //   RegDst
  //   Syscall
  //   ID/EX
  //   流水调试日志用
  //   EX/MEM
  //   MEM/WB
endmodule

// 源寄存器使用情况
module \源寄存器使用情况  (
  input  OP0,
  input  OP1,
  input  OP2,
  input  OP3,
  input  OP4,
  input  OP5,
  input  F0,
  input  F1,
  input  F2,
  input  F3,
  input  F4,
  input  F5,
  output R1_Used,
  output R2_Used
);

  wire and_1_out, and_2_out, and_3_out, and_4_out, and_5_out, and_6_out, and_7_out, and_8_out, and_9_out,
       and_10_out, and_11_out, and_12_out, and_13_out, and_14_out, and_15_out, and_16_out, and_17_out,
       and_18_out, and_19_out, and_20_out, and_21_out, and_22_out, and_23_out, and_24_out, and_25_out,
       and_26_out, and_27_out, and_28_out, and_29_out, and_30_out, and_31_out, and_32_out, and_33_out,
       and_34_out, and_35_out, and_36_out, and_37_out, and_38_out, and_39_out, and_40_out, and_41_out,
       and_42_out, and_43_out, and_44_out, and_45_out, and_46_out, and_47_out, not_1_out, not_2_out,
       not_3_out, not_4_out, not_5_out, not_6_out, not_7_out, not_8_out, not_9_out, not_10_out, not_11_out,
       not_12_out, not_13_out, not_14_out, not_15_out, not_16_out, not_17_out, not_18_out, not_19_out,
       not_20_out, not_21_out, not_22_out, not_23_out, not_24_out, not_25_out, not_26_out, not_27_out,
       not_28_out, not_29_out, not_30_out, not_31_out, not_32_out, not_33_out, not_34_out, not_35_out,
       not_36_out, not_37_out, not_38_out, not_39_out, not_40_out, not_41_out, not_42_out, not_43_out,
       not_44_out, not_45_out, not_46_out, not_47_out, not_48_out, not_49_out, not_50_out, not_51_out,
       not_52_out, not_53_out, not_54_out, not_55_out, not_56_out, not_57_out, not_58_out, not_59_out,
       not_60_out, not_61_out, not_62_out, not_63_out, not_64_out, not_65_out, not_66_out, not_67_out,
       not_68_out, not_69_out, not_70_out, not_71_out, not_72_out, not_73_out, not_74_out, not_75_out,
       not_76_out, not_77_out, not_78_out, not_79_out, not_80_out, not_81_out, not_82_out, not_83_out,
       not_84_out, not_85_out, not_86_out, not_87_out, not_88_out, not_89_out, not_90_out, not_91_out,
       not_92_out, not_93_out, not_94_out, not_95_out, not_96_out, not_97_out, not_98_out, not_99_out,
       not_100_out, not_101_out, not_102_out, not_103_out, not_104_out, not_105_out, not_106_out,
       not_107_out, not_108_out, not_109_out, not_110_out, not_111_out, not_112_out, not_113_out,
       not_114_out, not_115_out, not_116_out, not_117_out, not_118_out, not_119_out, not_120_out,
       not_121_out, not_122_out, not_123_out, not_124_out, not_125_out, not_126_out, not_127_out,
       not_128_out, not_129_out, not_130_out, not_131_out, not_132_out, not_133_out, not_134_out,
       not_135_out, not_136_out, not_137_out, not_138_out, not_139_out, not_140_out, not_141_out,
       not_142_out, not_143_out, not_144_out, not_145_out, not_146_out, not_147_out, not_148_out,
       not_149_out, not_150_out, not_151_out, not_152_out, not_153_out, not_154_out, not_155_out,
       not_156_out, not_157_out, not_158_out, not_159_out, not_160_out, not_161_out, not_162_out,
       not_163_out, not_164_out, not_165_out, not_166_out, not_167_out, not_168_out, not_169_out,
       not_170_out, not_171_out, not_172_out, not_173_out, not_174_out, not_175_out, not_176_out,
       not_177_out, not_178_out, not_179_out, not_180_out, not_181_out, not_182_out, not_183_out,
       not_184_out, not_185_out, not_186_out, not_187_out, not_188_out, not_189_out, not_190_out,
       not_191_out, not_192_out, not_193_out, not_194_out, not_195_out, not_196_out, not_197_out,
       not_198_out, not_199_out, not_200_out, not_201_out, not_202_out, not_203_out, not_204_out,
       not_205_out, not_206_out, not_207_out, not_208_out, not_209_out, not_210_out, not_211_out,
       not_212_out, not_213_out, not_214_out, not_215_out, not_216_out, not_217_out, not_218_out,
       not_219_out, not_220_out, not_221_out, not_222_out, not_223_out, not_224_out, not_225_out,
       not_226_out, not_227_out, not_228_out, not_229_out, not_230_out, not_231_out, not_232_out,
       not_233_out, not_234_out, not_235_out, not_236_out, not_237_out, not_238_out, not_239_out,
       not_240_out, not_241_out, not_242_out, not_243_out, not_244_out, not_245_out, not_246_out,
       not_247_out, not_248_out, not_249_out, not_250_out, not_251_out, not_252_out, not_253_out,
       not_254_out, not_255_out, not_256_out, not_257_out, not_258_out, not_259_out, not_260_out,
       not_261_out, not_262_out, not_263_out, not_264_out, not_265_out, not_266_out, not_267_out,
       not_268_out, not_269_out, not_270_out, not_271_out, not_272_out, not_273_out, not_274_out,
       not_275_out, not_276_out, not_277_out, not_278_out, not_279_out, not_280_out, not_281_out,
       not_282_out, not_283_out, not_284_out, not_285_out, not_286_out, not_287_out, not_288_out,
       not_289_out, not_290_out, not_291_out, not_292_out, not_293_out, not_294_out, not_295_out,
       not_296_out, not_297_out, not_298_out, not_299_out, not_300_out, not_301_out, not_302_out,
       not_303_out, not_304_out, not_305_out, not_306_out, not_307_out, not_308_out, not_309_out,
       not_310_out, not_311_out, not_312_out, not_313_out, not_314_out, not_315_out, not_316_out,
       not_317_out, not_318_out, not_319_out, not_320_out, not_321_out, not_322_out, not_323_out,
       not_324_out, not_325_out, not_326_out, not_327_out, not_328_out, not_329_out, not_330_out,
       not_331_out, not_332_out, not_333_out, not_334_out, not_335_out, not_336_out, not_337_out,
       not_338_out, not_339_out, not_340_out, not_341_out, not_342_out, not_343_out, not_344_out,
       not_345_out, not_346_out, not_347_out, not_348_out, not_349_out, not_350_out, not_351_out, not_352_out;

  not not_1 (not_1_out, OP5);
  not not_2 (not_2_out, OP4);
  not not_3 (not_3_out, OP3);
  not not_4 (not_4_out, OP2);
  not not_5 (not_5_out, OP1);
  not not_6 (not_6_out, OP0);
  not not_7 (not_7_out, F5);
  not not_8 (not_8_out, F4);
  not not_9 (not_9_out, F3);
  not not_10 (not_10_out, F2);
  not not_11 (not_11_out, F1);
  not not_12 (not_12_out, F0);
  not not_13 (not_13_out, OP5);
  not not_14 (not_14_out, OP4);
  not not_15 (not_15_out, OP3);
  not not_16 (not_16_out, OP2);
  not not_17 (not_17_out, OP1);
  not not_18 (not_18_out, OP0);
  not not_19 (not_19_out, F5);
  not not_20 (not_20_out, F4);
  not not_21 (not_21_out, F3);
  not not_22 (not_22_out, F2);
  not not_23 (not_23_out, OP5);
  not not_24 (not_24_out, OP4);
  not not_25 (not_25_out, OP3);
  not not_26 (not_26_out, OP2);
  not not_27 (not_27_out, OP1);
  not not_28 (not_28_out, OP0);
  not not_29 (not_29_out, F5);
  not not_30 (not_30_out, F4);
  not not_31 (not_31_out, F3);
  not not_32 (not_32_out, F2);
  not not_33 (not_33_out, F0);
  not not_34 (not_34_out, OP5);
  not not_35 (not_35_out, OP4);
  not not_36 (not_36_out, OP3);
  not not_37 (not_37_out, OP2);
  not not_38 (not_38_out, OP1);
  not not_39 (not_39_out, OP0);
  not not_40 (not_40_out, F4);
  not not_41 (not_41_out, F3);
  not not_42 (not_42_out, F2);
  not not_43 (not_43_out, F1);
  not not_44 (not_44_out, F0);
  not not_45 (not_45_out, OP5);
  not not_46 (not_46_out, OP4);
  not not_47 (not_47_out, OP3);
  not not_48 (not_48_out, OP2);
  not not_49 (not_49_out, OP1);
  not not_50 (not_50_out, OP0);
  not not_51 (not_51_out, F4);
  not not_52 (not_52_out, F3);
  not not_53 (not_53_out, F2);
  not not_54 (not_54_out, F1);
  not not_55 (not_55_out, OP5);
  not not_56 (not_56_out, OP4);
  not not_57 (not_57_out, OP3);
  not not_58 (not_58_out, OP2);
  not not_59 (not_59_out, OP1);
  not not_60 (not_60_out, OP0);
  not not_61 (not_61_out, F4);
  not not_62 (not_62_out, F3);
  not not_63 (not_63_out, F2);
  not not_64 (not_64_out, F0);
  not not_65 (not_65_out, OP5);
  not not_66 (not_66_out, OP4);
  not not_67 (not_67_out, OP3);
  not not_68 (not_68_out, OP2);
  not not_69 (not_69_out, OP1);
  not not_70 (not_70_out, OP0);
  not not_71 (not_71_out, F4);
  not not_72 (not_72_out, F3);
  not not_73 (not_73_out, F1);
  not not_74 (not_74_out, F0);
  not not_75 (not_75_out, OP5);
  not not_76 (not_76_out, OP4);
  not not_77 (not_77_out, OP3);
  not not_78 (not_78_out, OP2);
  not not_79 (not_79_out, OP1);
  not not_80 (not_80_out, OP0);
  not not_81 (not_81_out, F4);
  not not_82 (not_82_out, F3);
  not not_83 (not_83_out, F1);
  not not_84 (not_84_out, OP5);
  not not_85 (not_85_out, OP4);
  not not_86 (not_86_out, OP3);
  not not_87 (not_87_out, OP2);
  not not_88 (not_88_out, OP1);
  not not_89 (not_89_out, OP0);
  not not_90 (not_90_out, F4);
  not not_91 (not_91_out, F3);
  not not_92 (not_92_out, OP5);
  not not_93 (not_93_out, OP4);
  not not_94 (not_94_out, OP3);
  not not_95 (not_95_out, OP2);
  not not_96 (not_96_out, OP1);
  not not_97 (not_97_out, OP0);
  not not_98 (not_98_out, F4);
  not not_99 (not_99_out, F2);
  not not_100 (not_100_out, F0);
  not not_101 (not_101_out, OP5);
  not not_102 (not_102_out, OP4);
  not not_103 (not_103_out, OP3);
  not not_104 (not_104_out, OP2);
  not not_105 (not_105_out, OP1);
  not not_106 (not_106_out, OP0);
  not not_107 (not_107_out, F4);
  not not_108 (not_108_out, F2);
  not not_109 (not_109_out, OP5);
  not not_110 (not_110_out, OP4);
  not not_111 (not_111_out, OP3);
  not not_112 (not_112_out, OP2);
  not not_113 (not_113_out, OP1);
  not not_114 (not_114_out, OP0);
  not not_115 (not_115_out, F5);
  not not_116 (not_116_out, F4);
  not not_117 (not_117_out, F2);
  not not_118 (not_118_out, F1);
  not not_119 (not_119_out, F0);
  not not_120 (not_120_out, OP5);
  not not_121 (not_121_out, OP4);
  not not_122 (not_122_out, OP3);
  not not_123 (not_123_out, OP2);
  not not_124 (not_124_out, OP1);
  not not_125 (not_125_out, OP0);
  not not_126 (not_126_out, F5);
  not not_127 (not_127_out, F4);
  not not_128 (not_128_out, F1);
  not not_129 (not_129_out, F0);
  not not_130 (not_130_out, OP5);
  not not_131 (not_131_out, OP4);
  not not_132 (not_132_out, OP3);
  not not_133 (not_133_out, OP1);
  not not_134 (not_134_out, OP0);
  not not_135 (not_135_out, OP5);
  not not_136 (not_136_out, OP4);
  not not_137 (not_137_out, OP3);
  not not_138 (not_138_out, OP1);
  not not_139 (not_139_out, OP5);
  not not_140 (not_140_out, OP4);
  not not_141 (not_141_out, OP2);
  not not_142 (not_142_out, OP1);
  not not_143 (not_143_out, OP0);
  not not_144 (not_144_out, OP5);
  not not_145 (not_145_out, OP4);
  not not_146 (not_146_out, OP1);
  not not_147 (not_147_out, OP0);
  not not_148 (not_148_out, OP5);
  not not_149 (not_149_out, OP4);
  not not_150 (not_150_out, OP2);
  not not_151 (not_151_out, OP1);
  not not_152 (not_152_out, OP5);
  not not_153 (not_153_out, OP4);
  not not_154 (not_154_out, OP2);
  not not_155 (not_155_out, OP0);
  not not_156 (not_156_out, OP5);
  not not_157 (not_157_out, OP4);
  not not_158 (not_158_out, OP1);
  not not_159 (not_159_out, OP4);
  not not_160 (not_160_out, OP3);
  not not_161 (not_161_out, OP2);
  not not_162 (not_162_out, OP4);
  not not_163 (not_163_out, OP2);
  not not_164 (not_164_out, OP5);
  not not_165 (not_165_out, OP4);
  not not_166 (not_166_out, OP3);
  not not_167 (not_167_out, OP2);
  not not_168 (not_168_out, OP1);
  not not_169 (not_169_out, OP0);
  not not_170 (not_170_out, F4);
  not not_171 (not_171_out, F3);
  not not_172 (not_172_out, F2);
  not not_173 (not_173_out, OP5);
  not not_174 (not_174_out, OP4);
  not not_175 (not_175_out, OP3);
  not not_176 (not_176_out, OP2);
  not not_177 (not_177_out, OP1);
  not not_178 (not_178_out, OP0);
  not not_179 (not_179_out, F4);
  not not_180 (not_180_out, F3);
  not not_181 (not_181_out, F0);
  not not_182 (not_182_out, OP4);
  not not_183 (not_183_out, OP2);
  not not_184 (not_184_out, OP1);
  not not_185 (not_185_out, OP5);
  not not_186 (not_186_out, OP4);
  not not_187 (not_187_out, OP3);
  not not_188 (not_188_out, OP2);
  not not_189 (not_189_out, OP1);
  not not_190 (not_190_out, OP5);
  not not_191 (not_191_out, OP3);
  not not_192 (not_192_out, OP2);
  not not_193 (not_193_out, OP1);
  not not_194 (not_194_out, OP0);
  not not_195 (not_195_out, OP5);
  not not_196 (not_196_out, OP4);
  not not_197 (not_197_out, OP3);
  not not_198 (not_198_out, OP2);
  not not_199 (not_199_out, OP1);
  not not_200 (not_200_out, OP0);
  not not_201 (not_201_out, F5);
  not not_202 (not_202_out, F4);
  not not_203 (not_203_out, F3);
  not not_204 (not_204_out, F2);
  not not_205 (not_205_out, F1);
  not not_206 (not_206_out, F0);
  not not_207 (not_207_out, OP5);
  not not_208 (not_208_out, OP4);
  not not_209 (not_209_out, OP3);
  not not_210 (not_210_out, OP2);
  not not_211 (not_211_out, OP1);
  not not_212 (not_212_out, OP0);
  not not_213 (not_213_out, F5);
  not not_214 (not_214_out, F4);
  not not_215 (not_215_out, F3);
  not not_216 (not_216_out, F2);
  not not_217 (not_217_out, OP5);
  not not_218 (not_218_out, OP4);
  not not_219 (not_219_out, OP3);
  not not_220 (not_220_out, OP2);
  not not_221 (not_221_out, OP1);
  not not_222 (not_222_out, OP0);
  not not_223 (not_223_out, F5);
  not not_224 (not_224_out, F4);
  not not_225 (not_225_out, F3);
  not not_226 (not_226_out, F2);
  not not_227 (not_227_out, F0);
  not not_228 (not_228_out, OP5);
  not not_229 (not_229_out, OP4);
  not not_230 (not_230_out, OP3);
  not not_231 (not_231_out, OP2);
  not not_232 (not_232_out, OP1);
  not not_233 (not_233_out, OP0);
  not not_234 (not_234_out, F4);
  not not_235 (not_235_out, F3);
  not not_236 (not_236_out, F2);
  not not_237 (not_237_out, F1);
  not not_238 (not_238_out, F0);
  not not_239 (not_239_out, OP5);
  not not_240 (not_240_out, OP4);
  not not_241 (not_241_out, OP3);
  not not_242 (not_242_out, OP2);
  not not_243 (not_243_out, OP1);
  not not_244 (not_244_out, OP0);
  not not_245 (not_245_out, F4);
  not not_246 (not_246_out, F3);
  not not_247 (not_247_out, F2);
  not not_248 (not_248_out, F1);
  not not_249 (not_249_out, OP5);
  not not_250 (not_250_out, OP4);
  not not_251 (not_251_out, OP3);
  not not_252 (not_252_out, OP2);
  not not_253 (not_253_out, OP1);
  not not_254 (not_254_out, OP0);
  not not_255 (not_255_out, F4);
  not not_256 (not_256_out, F3);
  not not_257 (not_257_out, F2);
  not not_258 (not_258_out, F0);
  not not_259 (not_259_out, OP5);
  not not_260 (not_260_out, OP4);
  not not_261 (not_261_out, OP3);
  not not_262 (not_262_out, OP2);
  not not_263 (not_263_out, OP1);
  not not_264 (not_264_out, OP0);
  not not_265 (not_265_out, F4);
  not not_266 (not_266_out, F3);
  not not_267 (not_267_out, F1);
  not not_268 (not_268_out, F0);
  not not_269 (not_269_out, OP5);
  not not_270 (not_270_out, OP4);
  not not_271 (not_271_out, OP3);
  not not_272 (not_272_out, OP2);
  not not_273 (not_273_out, OP1);
  not not_274 (not_274_out, OP0);
  not not_275 (not_275_out, F4);
  not not_276 (not_276_out, F3);
  not not_277 (not_277_out, F1);
  not not_278 (not_278_out, OP5);
  not not_279 (not_279_out, OP4);
  not not_280 (not_280_out, OP3);
  not not_281 (not_281_out, OP2);
  not not_282 (not_282_out, OP1);
  not not_283 (not_283_out, OP0);
  not not_284 (not_284_out, F4);
  not not_285 (not_285_out, F3);
  not not_286 (not_286_out, OP5);
  not not_287 (not_287_out, OP4);
  not not_288 (not_288_out, OP3);
  not not_289 (not_289_out, OP2);
  not not_290 (not_290_out, OP1);
  not not_291 (not_291_out, OP0);
  not not_292 (not_292_out, F4);
  not not_293 (not_293_out, F2);
  not not_294 (not_294_out, F0);
  not not_295 (not_295_out, OP5);
  not not_296 (not_296_out, OP4);
  not not_297 (not_297_out, OP3);
  not not_298 (not_298_out, OP2);
  not not_299 (not_299_out, OP1);
  not not_300 (not_300_out, OP0);
  not not_301 (not_301_out, F4);
  not not_302 (not_302_out, F2);
  not not_303 (not_303_out, OP5);
  not not_304 (not_304_out, OP4);
  not not_305 (not_305_out, OP3);
  not not_306 (not_306_out, OP2);
  not not_307 (not_307_out, OP1);
  not not_308 (not_308_out, OP0);
  not not_309 (not_309_out, F5);
  not not_310 (not_310_out, F4);
  not not_311 (not_311_out, F1);
  not not_312 (not_312_out, F0);
  not not_313 (not_313_out, OP5);
  not not_314 (not_314_out, OP4);
  not not_315 (not_315_out, OP3);
  not not_316 (not_316_out, OP1);
  not not_317 (not_317_out, OP0);
  not not_318 (not_318_out, OP5);
  not not_319 (not_319_out, OP4);
  not not_320 (not_320_out, OP3);
  not not_321 (not_321_out, OP1);
  not not_322 (not_322_out, OP4);
  not not_323 (not_323_out, OP3);
  not not_324 (not_324_out, OP2);
  not not_325 (not_325_out, OP4);
  not not_326 (not_326_out, OP2);
  not not_327 (not_327_out, OP5);
  not not_328 (not_328_out, OP4);
  not not_329 (not_329_out, OP3);
  not not_330 (not_330_out, OP2);
  not not_331 (not_331_out, OP1);
  not not_332 (not_332_out, OP0);
  not not_333 (not_333_out, F4);
  not not_334 (not_334_out, F3);
  not not_335 (not_335_out, F2);
  not not_336 (not_336_out, OP5);
  not not_337 (not_337_out, OP4);
  not not_338 (not_338_out, OP3);
  not not_339 (not_339_out, OP2);
  not not_340 (not_340_out, OP1);
  not not_341 (not_341_out, OP0);
  not not_342 (not_342_out, F4);
  not not_343 (not_343_out, F3);
  not not_344 (not_344_out, F0);
  not not_345 (not_345_out, OP4);
  not not_346 (not_346_out, OP2);
  not not_347 (not_347_out, OP1);
  not not_348 (not_348_out, OP5);
  not not_349 (not_349_out, OP3);
  not not_350 (not_350_out, OP2);
  not not_351 (not_351_out, OP1);
  not not_352 (not_352_out, OP0);
  and and_1 (and_1_out, not_1_out, not_2_out, not_3_out, not_4_out, not_5_out, not_6_out, not_7_out, not_8_out, not_9_out, not_10_out, not_11_out, not_12_out);
  and and_2 (and_2_out, not_13_out, not_14_out, not_15_out, not_16_out, not_17_out, not_18_out, not_19_out, not_20_out, not_21_out, not_22_out, F1, F0);
  and and_3 (and_3_out, not_23_out, not_24_out, not_25_out, not_26_out, not_27_out, not_28_out, not_29_out, not_30_out, not_31_out, not_32_out, F1, not_33_out);
  and and_4 (and_4_out, not_34_out, not_35_out, not_36_out, not_37_out, not_38_out, not_39_out, F5, not_40_out, not_41_out, not_42_out, not_43_out, not_44_out);
  and and_5 (and_5_out, not_45_out, not_46_out, not_47_out, not_48_out, not_49_out, not_50_out, F5, not_51_out, not_52_out, not_53_out, not_54_out, F0);
  and and_6 (and_6_out, not_55_out, not_56_out, not_57_out, not_58_out, not_59_out, not_60_out, F5, not_61_out, not_62_out, not_63_out, F1, not_64_out);
  and and_7 (and_7_out, not_65_out, not_66_out, not_67_out, not_68_out, not_69_out, not_70_out, F5, not_71_out, not_72_out, F2, not_73_out, not_74_out);
  and and_8 (and_8_out, not_75_out, not_76_out, not_77_out, not_78_out, not_79_out, not_80_out, F5, not_81_out, not_82_out, F2, not_83_out, F0);
  and and_9 (and_9_out, not_84_out, not_85_out, not_86_out, not_87_out, not_88_out, not_89_out, F5, not_90_out, not_91_out, F2, F1, F0);
  and and_10 (and_10_out, not_92_out, not_93_out, not_94_out, not_95_out, not_96_out, not_97_out, F5, not_98_out, F3, not_99_out, F1, not_100_out);
  and and_11 (and_11_out, not_101_out, not_102_out, not_103_out, not_104_out, not_105_out, not_106_out, F5, not_107_out, F3, not_108_out, F1, F0);
  and and_12 (and_12_out, not_109_out, not_110_out, not_111_out, not_112_out, not_113_out, not_114_out, not_115_out, not_116_out, F3, not_117_out, not_118_out, not_119_out);
  and and_13 (and_13_out, not_120_out, not_121_out, not_122_out, not_123_out, not_124_out, not_125_out, not_126_out, not_127_out, F3, F2, not_128_out, not_129_out);
  and and_14 (and_14_out, not_130_out, not_131_out, not_132_out, OP2, not_133_out, not_134_out);
  and and_15 (and_15_out, not_135_out, not_136_out, not_137_out, OP2, not_138_out, OP0);
  and and_16 (and_16_out, not_139_out, not_140_out, OP3, not_141_out, not_142_out, not_143_out);
  and and_17 (and_17_out, not_144_out, not_145_out, OP3, OP2, not_146_out, not_147_out);
  and and_18 (and_18_out, not_148_out, not_149_out, OP3, not_150_out, not_151_out, OP0);
  and and_19 (and_19_out, not_152_out, not_153_out, OP3, not_154_out, OP1, not_155_out);
  and and_20 (and_20_out, not_156_out, not_157_out, OP3, OP2, not_158_out, OP0);
  and and_21 (and_21_out, OP5, not_159_out, not_160_out, not_161_out, OP1, OP0);
  and and_22 (and_22_out, OP5, not_162_out, OP3, not_163_out, OP1, OP0);
  and and_23 (and_23_out, not_164_out, not_165_out, not_166_out, not_167_out, not_168_out, not_169_out, F5, not_170_out, not_171_out, not_172_out, F1, F0);
  and and_24 (and_24_out, not_173_out, not_174_out, not_175_out, not_176_out, not_177_out, not_178_out, F5, not_179_out, not_180_out, F2, F1, not_181_out);
  and and_25 (and_25_out, OP5, not_182_out, OP3, not_183_out, not_184_out, OP0);
  and and_26 (and_26_out, not_185_out, not_186_out, not_187_out, not_188_out, not_189_out, OP0);
  and and_27 (and_27_out, not_190_out, OP4, not_191_out, not_192_out, not_193_out, not_194_out);
  and and_28 (and_28_out, not_195_out, not_196_out, not_197_out, not_198_out, not_199_out, not_200_out, not_201_out, not_202_out, not_203_out, not_204_out, not_205_out, not_206_out);
  and and_29 (and_29_out, not_207_out, not_208_out, not_209_out, not_210_out, not_211_out, not_212_out, not_213_out, not_214_out, not_215_out, not_216_out, F1, F0);
  and and_30 (and_30_out, not_217_out, not_218_out, not_219_out, not_220_out, not_221_out, not_222_out, not_223_out, not_224_out, not_225_out, not_226_out, F1, not_227_out);
  and and_31 (and_31_out, not_228_out, not_229_out, not_230_out, not_231_out, not_232_out, not_233_out, F5, not_234_out, not_235_out, not_236_out, not_237_out, not_238_out);
  and and_32 (and_32_out, not_239_out, not_240_out, not_241_out, not_242_out, not_243_out, not_244_out, F5, not_245_out, not_246_out, not_247_out, not_248_out, F0);
  and and_33 (and_33_out, not_249_out, not_250_out, not_251_out, not_252_out, not_253_out, not_254_out, F5, not_255_out, not_256_out, not_257_out, F1, not_258_out);
  and and_34 (and_34_out, not_259_out, not_260_out, not_261_out, not_262_out, not_263_out, not_264_out, F5, not_265_out, not_266_out, F2, not_267_out, not_268_out);
  and and_35 (and_35_out, not_269_out, not_270_out, not_271_out, not_272_out, not_273_out, not_274_out, F5, not_275_out, not_276_out, F2, not_277_out, F0);
  and and_36 (and_36_out, not_278_out, not_279_out, not_280_out, not_281_out, not_282_out, not_283_out, F5, not_284_out, not_285_out, F2, F1, F0);
  and and_37 (and_37_out, not_286_out, not_287_out, not_288_out, not_289_out, not_290_out, not_291_out, F5, not_292_out, F3, not_293_out, F1, not_294_out);
  and and_38 (and_38_out, not_295_out, not_296_out, not_297_out, not_298_out, not_299_out, not_300_out, F5, not_301_out, F3, not_302_out, F1, F0);
  and and_39 (and_39_out, not_303_out, not_304_out, not_305_out, not_306_out, not_307_out, not_308_out, not_309_out, not_310_out, F3, F2, not_311_out, not_312_out);
  and and_40 (and_40_out, not_313_out, not_314_out, not_315_out, OP2, not_316_out, not_317_out);
  and and_41 (and_41_out, not_318_out, not_319_out, not_320_out, OP2, not_321_out, OP0);
  and and_42 (and_42_out, OP5, not_322_out, not_323_out, not_324_out, OP1, OP0);
  and and_43 (and_43_out, OP5, not_325_out, OP3, not_326_out, OP1, OP0);
  and and_44 (and_44_out, not_327_out, not_328_out, not_329_out, not_330_out, not_331_out, not_332_out, F5, not_333_out, not_334_out, not_335_out, F1, F0);
  and and_45 (and_45_out, not_336_out, not_337_out, not_338_out, not_339_out, not_340_out, not_341_out, F5, not_342_out, not_343_out, F2, F1, not_344_out);
  and and_46 (and_46_out, OP5, not_345_out, OP3, not_346_out, not_347_out, OP0);
  and and_47 (and_47_out, not_348_out, OP4, not_349_out, not_350_out, not_351_out, not_352_out);
  or or_1 (R1_Used, and_1_out, and_2_out, and_3_out, and_4_out, and_5_out, and_6_out, and_7_out, and_8_out, and_9_out, and_10_out, and_11_out, and_12_out, and_13_out, and_14_out, and_15_out, and_16_out, and_17_out, and_18_out, and_19_out, and_20_out, and_21_out, and_22_out, and_23_out, and_24_out, and_25_out, and_26_out, and_27_out);
  or or_2 (R2_Used, and_28_out, and_29_out, and_30_out, and_31_out, and_32_out, and_33_out, and_34_out, and_35_out, and_36_out, and_37_out, and_38_out, and_39_out, and_40_out, and_41_out, and_42_out, and_43_out, and_44_out, and_45_out, and_46_out, and_47_out);
endmodule
module \数据相关检测  (
  input  [5:0] OP,
  input  [4:0] EX_WriteReg_num,
  input  EX_RegWrite,
  input  EX_MemToReg,
  input  [4:0] MEM_WriteReg_num,
  input  MEM_RegWrite,
  input  MEM_MemToReg,
  input  [5:0] Func,
  input  [4:0] ID_R1_num,
  input  [4:0] ID_R2_num,
  output [1:0] ForwardR1,
  output [1:0] ForwardR2,
  output Load_Use,
  output \数据相关 
);

  wire and_1_out, and_2_out, and_3_out, and_4_out, and_7_out, and_8_out, and_9_out, and_10_out,
       comparator_1_eq, comparator_2_eq, comparator_3_eq, comparator_4_eq, comparator_5_eq, comparator_6_eq,
       comparator_7_eq, comparator_8_eq, comparator_9_eq, comparator_10_eq, comparator_11_eq,
       comparator_12_eq, comparator_13_eq, comparator_14_eq, comparator_15_eq, comparator_16_eq,
       comparator_17_eq, comparator_18_eq, not_1_out, not_2_out, not_3_out, not_4_out, not_5_out, not_6_out,
       not_7_out, not_8_out, not_9_out, not_10_out, or_1_out, or_2_out, or_4_out, R1_Used, \R1冲突 , R2_Used,
       \R2冲突 ;
  wire [1:0] multiplexer_1_out, multiplexer_2_out, multiplexer_3_out, multiplexer_4_out;

  \源寄存器使用情况  \u_源寄存器使用情况_1  (
    .OP0(OP[0]), .OP1(OP[1]), .OP2(OP[2]), .OP3(OP[3]), .OP4(OP[4]), .OP5(OP[5]), .F0(Func[0]), .F1(Func[1]),
    .F2(Func[2]), .F3(Func[3]), .F4(Func[4]), .F5(Func[5]), .R1_Used(R1_Used), .R2_Used(R2_Used));
  not not_1 (not_1_out, comparator_1_eq);
  Comparator #(.width(5)) comparator_1 (.a(MEM_WriteReg_num), .b({5{1'b0}}), .eq(comparator_1_eq));  // open: gt, lt
  Comparator #(.width(5)) comparator_2 (.a(MEM_WriteReg_num), .b(ID_R1_num), .eq(comparator_2_eq));  // open: gt, lt
  Comparator #(.width(5)) comparator_3 (.a(ID_R1_num), .b(EX_WriteReg_num), .eq(comparator_3_eq));  // open: gt, lt
  not not_2 (not_2_out, comparator_4_eq);
  Comparator #(.width(5)) comparator_4 (.a({5{1'b0}}), .b(EX_WriteReg_num), .eq(comparator_4_eq));  // open: gt, lt
  Comparator #(.width(5)) comparator_5 (.a(EX_WriteReg_num), .b({5{1'b0}}), .eq(comparator_5_eq));  // open: gt, lt
  not not_3 (not_3_out, comparator_5_eq);
  Comparator #(.width(5)) comparator_6 (.a(EX_WriteReg_num), .b(ID_R2_num), .eq(comparator_6_eq));  // open: gt, lt
  Comparator #(.width(5)) comparator_7 (.a(ID_R2_num), .b(MEM_WriteReg_num), .eq(comparator_7_eq));  // open: gt, lt
  not not_4 (not_4_out, comparator_8_eq);
  Comparator #(.width(5)) comparator_8 (.a({5{1'b0}}), .b(MEM_WriteReg_num), .eq(comparator_8_eq));  // open: gt, lt
  and and_1 (and_1_out, not_1_out, MEM_RegWrite, comparator_2_eq);
  and and_2 (and_2_out, comparator_3_eq, EX_RegWrite, not_2_out);
  and and_3 (and_3_out, not_3_out, EX_RegWrite, comparator_6_eq);
  and and_4 (and_4_out, comparator_7_eq, MEM_RegWrite, not_4_out);
  Comparator #(.width(5)) comparator_9 (.a(ID_R1_num), .b({5{1'b0}}), .eq(comparator_9_eq));  // open: gt, lt
  or or_1 (or_1_out, and_1_out, and_2_out);
  or or_2 (or_2_out, and_3_out, and_4_out);
  Comparator #(.width(5)) comparator_10 (.a(ID_R2_num), .b({5{1'b0}}), .eq(comparator_10_eq));  // open: gt, lt
  not not_5 (not_5_out, comparator_9_eq);
  not not_6 (not_6_out, comparator_10_eq);
  and and_5 (\R1冲突 , not_5_out, R1_Used, or_1_out);
  or or_3 (\数据相关 , \R1冲突 , \R2冲突 );
  and and_6 (\R2冲突 , or_2_out, R2_Used, not_6_out);
  Comparator #(.width(5)) comparator_11 (.a(ID_R1_num), .b(EX_WriteReg_num), .eq(comparator_11_eq));  // open: gt, lt
  Multiplexer #(.width(2), .enable("false")) multiplexer_1 (
    .in0(2'b01), .in1(2'b10), .out(multiplexer_1_out), .sel(MEM_MemToReg));
  Comparator #(.width(5)) comparator_12 (.a(ID_R2_num), .b(EX_WriteReg_num), .eq(comparator_12_eq));  // open: gt, lt
  Multiplexer #(.width(2), .enable("false")) multiplexer_2 (
    .in0(2'b01), .in1(2'b10), .out(multiplexer_2_out), .sel(MEM_MemToReg));
  Comparator #(.width(5)) comparator_13 (.a(ID_R1_num), .b({5{1'b0}}), .eq(comparator_13_eq));  // open: gt, lt
  not not_7 (not_7_out, comparator_13_eq);
  Comparator #(.width(5)) comparator_14 (.a(ID_R1_num), .b(EX_WriteReg_num), .eq(comparator_14_eq));  // open: gt, lt
  not not_8 (not_8_out, comparator_15_eq);
  Comparator #(.width(5)) comparator_15 (.a({5{1'b0}}), .b(EX_WriteReg_num), .eq(comparator_15_eq));  // open: gt, lt
  not not_9 (not_9_out, comparator_16_eq);
  Comparator #(.width(5)) comparator_16 (.a(EX_WriteReg_num), .b({5{1'b0}}), .eq(comparator_16_eq));  // open: gt, lt
  Comparator #(.width(5)) comparator_17 (.a(EX_WriteReg_num), .b(ID_R2_num), .eq(comparator_17_eq));  // open: gt, lt
  not not_10 (not_10_out, comparator_18_eq);
  Comparator #(.width(5)) comparator_18 (.a({5{1'b0}}), .b(ID_R2_num), .eq(comparator_18_eq));  // open: gt, lt
  Multiplexer #(.width(2), .enable("false")) multiplexer_3 (
    .in0(multiplexer_1_out), .in1(2'b11), .out(multiplexer_3_out), .sel(comparator_11_eq));
  Multiplexer #(.width(2), .enable("false")) multiplexer_4 (
    .in0(multiplexer_2_out), .in1(2'b11), .out(multiplexer_4_out), .sel(comparator_12_eq));
  and and_7 (and_7_out, comparator_14_eq, EX_RegWrite, not_8_out);
  and and_8 (and_8_out, not_9_out, EX_RegWrite, comparator_17_eq);
  Multiplexer #(.width(2), .enable("false")) multiplexer_5 (
    .in0(2'b00), .in1(multiplexer_3_out), .out(ForwardR1), .sel(\R1冲突 ));
  Multiplexer #(.width(2), .enable("false")) multiplexer_6 (
    .in0(2'b00), .in1(multiplexer_4_out), .out(ForwardR2), .sel(\R2冲突 ));
  and and_9 (and_9_out, not_7_out, R1_Used, and_7_out);
  and and_10 (and_10_out, and_8_out, R2_Used, not_10_out);
  or or_4 (or_4_out, and_9_out, and_10_out);
  and and_11 (Load_Use, EX_MemToReg, or_4_out);

  // Other names for the same wires on the sheet: OP_CODE[5:0] = OP
endmodule

module IF_ID (
  input  [31:0] Din_Ins,
  input  [31:0] Din_PC_4,
  input  [31:0] Din_PC,
  input  [1:0] Din_Status,
  input  [31:0] Din_Addr,
  input  Din_Miss,
  input  Din_Hit,
  input  \传输状态In_表明当前传输数据有效 ,
  input  CLK,
  input  \同步清零_气泡_高电平有效 ,
  input  \使能端_低电平有效_stall_高电平有效 ,
  output [31:0] Dout_Ins,
  output [31:0] Dout_PC_4,
  output [31:0] Dout_PC,
  output [1:0] Dout_Status,
  output [31:0] Dout_Addr,
  output Dout_Miss,
  output Dout_Hit,
  output \传输状态Out_表明当前传输数据有效 
);

  wire multiplexer_6_out, multiplexer_7_out, multiplexer_8_out, not_1_out;
  wire [1:0] multiplexer_4_out;
  wire [31:0] multiplexer_1_out, multiplexer_2_out, multiplexer_3_out, multiplexer_5_out;

  Multiplexer #(.width(32), .enable("false")) multiplexer_1 (
    .in0(Din_Ins), .in1({32{1'b0}}), .out(multiplexer_1_out), .sel(\同步清零_气泡_高电平有效 ));
  Multiplexer #(.width(32), .enable("false")) multiplexer_2 (
    .in0(Din_PC_4), .in1({32{1'b0}}), .out(multiplexer_2_out), .sel(\同步清零_气泡_高电平有效 ));
  Multiplexer #(.width(32), .enable("false")) multiplexer_3 (
    .in0(Din_PC), .in1({32{1'b0}}), .out(multiplexer_3_out), .sel(\同步清零_气泡_高电平有效 ));
  Multiplexer #(.width(2), .enable("false")) multiplexer_4 (
    .in0(Din_Status), .in1(2'b00), .out(multiplexer_4_out), .sel(\同步清零_气泡_高电平有效 ));
  Multiplexer #(.width(32), .enable("false")) multiplexer_5 (
    .in0(Din_Addr), .in1({32{1'b0}}), .out(multiplexer_5_out), .sel(\同步清零_气泡_高电平有效 ));
  Multiplexer #(.enable("false")) multiplexer_6 (
    .in0(Din_Miss), .in1(1'b0), .out(multiplexer_6_out), .sel(\同步清零_气泡_高电平有效 ));
  Multiplexer #(.enable("false")) multiplexer_7 (
    .in0(Din_Hit), .in1(1'b0), .out(multiplexer_7_out), .sel(\同步清零_气泡_高电平有效 ));
  Multiplexer #(.enable("false")) multiplexer_8 (
    .in0(\传输状态In_表明当前传输数据有效 ), .in1(1'b0), .out(multiplexer_8_out), .sel(\同步清零_气泡_高电平有效 ));
  Register #(.width(32)) register_1 (.D(multiplexer_1_out), .en(not_1_out), .Q(Dout_Ins), .clk(CLK));  // open: clr
  Register #(.width(32)) register_2 (.D(multiplexer_2_out), .en(not_1_out), .Q(Dout_PC_4), .clk(CLK));  // open: clr
  Register #(.width(32)) register_3 (.D(multiplexer_3_out), .en(not_1_out), .Q(Dout_PC), .clk(CLK));  // open: clr
  Register #(.width(2)) register_4 (.D(multiplexer_4_out), .en(not_1_out), .Q(Dout_Status), .clk(CLK));  // open: clr
  Register #(.width(32)) register_5 (.D(multiplexer_5_out), .en(not_1_out), .Q(Dout_Addr), .clk(CLK));  // open: clr
  Register #(.width(1)) register_6 (.D(multiplexer_6_out), .en(not_1_out), .Q(Dout_Miss), .clk(CLK));  // open: clr
  Register #(.width(1)) register_7 (.D(multiplexer_7_out), .en(not_1_out), .Q(Dout_Hit), .clk(CLK));  // open: clr
  Register #(.width(1)) register_8 (
    .D(multiplexer_8_out), .en(not_1_out), .Q(\传输状态Out_表明当前传输数据有效 ), .clk(CLK));  // open: clr
  not not_1 (not_1_out, \使能端_低电平有效_stall_高电平有效 );
endmodule

module ID_EX (
  input  [3:0] Din_4,
  input  [3:0] Din_4_2,
  input  [3:0] Din_4_3,
  input  [3:0] Din_4_4,
  input  [1:0] Din_2,
  input  [31:0] Din_32,
  input  [1:0] Din_2_2,
  input  [31:0] Din_32_2,
  input  [31:0] Din_32_3,
  input  [31:0] Din_32_4,
  input  [4:0] Din_5,
  input  [31:0] Din_32_5,
  input  [4:0] Din_5_2,
  input  [31:0] Din_32_6,
  input  [1:0] Din_2_3,
  input  [31:0] Din_32_7,
  input  Din_1,
  input  Din_1_2,
  input  \传输状态In_表明当前传输数据有效 ,
  input  CLK,
  input  \同步清零_气泡_高电平有效 ,
  input  \使能端_低电平有效_stall_高电平有效 ,
  output [3:0] Dout_4,
  output [3:0] Dout_4_2,
  output [3:0] Dout_4_3,
  output [3:0] Dout_4_4,
  output [1:0] Dout_2,
  output [31:0] Dout_32,
  output [1:0] Dout_2_2,
  output [31:0] Dout_32_2,
  output [31:0] Dout_32_3,
  output [31:0] Dout_32_4,
  output [4:0] Dout_5,
  output [31:0] Dout_32_5,
  output [4:0] Dout_5_2,
  output [31:0] Dout_32_6,
  output [1:0] Dout_2_3,
  output [31:0] Dout_32_7,
  output Dout_1,
  output Dout_1_2,
  output \传输状态Out_表明当前传输数据有效 
);

  wire multiplexer_17_out, multiplexer_18_out, multiplexer_19_out, not_1_out;
  wire [1:0] multiplexer_5_out, multiplexer_7_out, multiplexer_15_out;
  wire [3:0] multiplexer_1_out, multiplexer_2_out, multiplexer_3_out, multiplexer_4_out;
  wire [4:0] multiplexer_11_out, multiplexer_13_out;
  wire [31:0] multiplexer_6_out, multiplexer_8_out, multiplexer_9_out, multiplexer_10_out,
       multiplexer_12_out, multiplexer_14_out, multiplexer_16_out;

  Multiplexer #(.width(4), .enable("false")) multiplexer_1 (
    .in0(Din_4), .in1(4'b0000), .out(multiplexer_1_out), .sel(\同步清零_气泡_高电平有效 ));
  Multiplexer #(.width(4), .enable("false")) multiplexer_2 (
    .in0(Din_4_2), .in1(4'b0000), .out(multiplexer_2_out), .sel(\同步清零_气泡_高电平有效 ));
  Multiplexer #(.width(4), .enable("false")) multiplexer_3 (
    .in0(Din_4_3), .in1(4'b0000), .out(multiplexer_3_out), .sel(\同步清零_气泡_高电平有效 ));
  Multiplexer #(.width(4), .enable("false")) multiplexer_4 (
    .in0(Din_4_4), .in1(4'b0000), .out(multiplexer_4_out), .sel(\同步清零_气泡_高电平有效 ));
  Multiplexer #(.width(2), .enable("false")) multiplexer_5 (
    .in0(Din_2), .in1(2'b00), .out(multiplexer_5_out), .sel(\同步清零_气泡_高电平有效 ));
  Multiplexer #(.width(32), .enable("false")) multiplexer_6 (
    .in0(Din_32), .in1({32{1'b0}}), .out(multiplexer_6_out), .sel(\同步清零_气泡_高电平有效 ));
  Multiplexer #(.width(2), .enable("false")) multiplexer_7 (
    .in0(Din_2_2), .in1(2'b00), .out(multiplexer_7_out), .sel(\同步清零_气泡_高电平有效 ));
  Multiplexer #(.width(32), .enable("false")) multiplexer_8 (
    .in0(Din_32_2), .in1({32{1'b0}}), .out(multiplexer_8_out), .sel(\同步清零_气泡_高电平有效 ));
  Multiplexer #(.width(32), .enable("false")) multiplexer_9 (
    .in0(Din_32_3), .in1({32{1'b0}}), .out(multiplexer_9_out), .sel(\同步清零_气泡_高电平有效 ));
  Multiplexer #(.width(32), .enable("false")) multiplexer_10 (
    .in0(Din_32_4), .in1({32{1'b0}}), .out(multiplexer_10_out), .sel(\同步清零_气泡_高电平有效 ));
  Multiplexer #(.width(5), .enable("false")) multiplexer_11 (
    .in0(Din_5), .in1({5{1'b0}}), .out(multiplexer_11_out), .sel(\同步清零_气泡_高电平有效 ));
  Multiplexer #(.width(32), .enable("false")) multiplexer_12 (
    .in0(Din_32_5), .in1({32{1'b0}}), .out(multiplexer_12_out), .sel(\同步清零_气泡_高电平有效 ));
  Multiplexer #(.width(5), .enable("false")) multiplexer_13 (
    .in0(Din_5_2), .in1({5{1'b0}}), .out(multiplexer_13_out), .sel(\同步清零_气泡_高电平有效 ));
  Multiplexer #(.width(32), .enable("false")) multiplexer_14 (
    .in0(Din_32_6), .in1({32{1'b0}}), .out(multiplexer_14_out), .sel(\同步清零_气泡_高电平有效 ));
  Multiplexer #(.width(2), .enable("false")) multiplexer_15 (
    .in0(Din_2_3), .in1(2'b00), .out(multiplexer_15_out), .sel(\同步清零_气泡_高电平有效 ));
  Multiplexer #(.width(32), .enable("false")) multiplexer_16 (
    .in0(Din_32_7), .in1({32{1'b0}}), .out(multiplexer_16_out), .sel(\同步清零_气泡_高电平有效 ));
  Multiplexer #(.enable("false")) multiplexer_17 (
    .in0(Din_1), .in1(1'b0), .out(multiplexer_17_out), .sel(\同步清零_气泡_高电平有效 ));
  Multiplexer #(.enable("false")) multiplexer_18 (
    .in0(Din_1_2), .in1(1'b0), .out(multiplexer_18_out), .sel(\同步清零_气泡_高电平有效 ));
  Multiplexer #(.enable("false")) multiplexer_19 (
    .in0(\传输状态In_表明当前传输数据有效 ), .in1(1'b0), .out(multiplexer_19_out), .sel(\同步清零_气泡_高电平有效 ));
  Register #(.width(4)) register_1 (.D(multiplexer_1_out), .en(not_1_out), .Q(Dout_4), .clk(CLK));  // open: clr
  Register #(.width(4)) register_2 (.D(multiplexer_2_out), .en(not_1_out), .Q(Dout_4_2), .clk(CLK));  // open: clr
  Register #(.width(4)) register_3 (.D(multiplexer_3_out), .en(not_1_out), .Q(Dout_4_3), .clk(CLK));  // open: clr
  Register #(.width(4)) register_4 (.D(multiplexer_4_out), .en(not_1_out), .Q(Dout_4_4), .clk(CLK));  // open: clr
  Register #(.width(2)) register_5 (.D(multiplexer_5_out), .en(not_1_out), .Q(Dout_2), .clk(CLK));  // open: clr
  Register #(.width(32)) register_6 (.D(multiplexer_6_out), .en(not_1_out), .Q(Dout_32), .clk(CLK));  // open: clr
  Register #(.width(2)) register_7 (.D(multiplexer_7_out), .en(not_1_out), .Q(Dout_2_2), .clk(CLK));  // open: clr
  Register #(.width(32)) register_8 (.D(multiplexer_8_out), .en(not_1_out), .Q(Dout_32_2), .clk(CLK));  // open: clr
  Register #(.width(32)) register_9 (.D(multiplexer_9_out), .en(not_1_out), .Q(Dout_32_3), .clk(CLK));  // open: clr
  Register #(.width(32)) register_10 (.D(multiplexer_10_out), .en(not_1_out), .Q(Dout_32_4), .clk(CLK));  // open: clr
  Register #(.width(5)) register_11 (.D(multiplexer_11_out), .en(not_1_out), .Q(Dout_5), .clk(CLK));  // open: clr
  Register #(.width(32)) register_12 (.D(multiplexer_12_out), .en(not_1_out), .Q(Dout_32_5), .clk(CLK));  // open: clr
  Register #(.width(5)) register_13 (.D(multiplexer_13_out), .en(not_1_out), .Q(Dout_5_2), .clk(CLK));  // open: clr
  Register #(.width(32)) register_14 (.D(multiplexer_14_out), .en(not_1_out), .Q(Dout_32_6), .clk(CLK));  // open: clr
  Register #(.width(2)) register_15 (.D(multiplexer_15_out), .en(not_1_out), .Q(Dout_2_3), .clk(CLK));  // open: clr
  Register #(.width(32)) register_16 (.D(multiplexer_16_out), .en(not_1_out), .Q(Dout_32_7), .clk(CLK));  // open: clr
  Register #(.width(1)) register_17 (.D(multiplexer_17_out), .en(not_1_out), .Q(Dout_1), .clk(CLK));  // open: clr
  Register #(.width(1)) register_18 (.D(multiplexer_18_out), .en(not_1_out), .Q(Dout_1_2), .clk(CLK));  // open: clr
  Register #(.width(1)) register_19 (
    .D(multiplexer_19_out), .en(not_1_out), .Q(\传输状态Out_表明当前传输数据有效 ), .clk(CLK));  // open: clr
  not not_1 (not_1_out, \使能端_低电平有效_stall_高电平有效 );
endmodule

module EX_MEM (
  input  Din_1,
  input  Din_1_2,
  input  Din_1_3,
  input  Din_1_4,
  input  Din_1_5,
  input  Din_1_6,
  input  Din_1_7,
  input  [31:0] Din_32,
  input  [31:0] Din_32_2,
  input  [31:0] Din_32_3,
  input  [31:0] Din_32_4,
  input  [4:0] Din_5,
  input  [31:0] Din_32_5,
  input  Din_1_8,
  input  Din_1_9,
  input  [31:0] Din_32_6,
  input  [31:0] Din_32_7,
  input  Din_1_10,
  input  \传输状态In_表明当前传输数据有效 ,
  input  CLK,
  input  \同步清零_气泡_高电平有效 ,
  input  \使能端_低电平有效_stall_高电平有效 ,
  output Dout_1,
  output Dout_1_2,
  output Dout_1_3,
  output Dout_1_4,
  output Dout_1_5,
  output Dout_1_6,
  output Dout_1_7,
  output [31:0] Dout_32,
  output [31:0] Dout_32_2,
  output [31:0] Dout_32_3,
  output [31:0] Dout_32_4,
  output [4:0] Dout_5,
  output [31:0] Dout_32_5,
  output Dout_1_8,
  output Dout_1_9,
  output [31:0] Dout_32_6,
  output [31:0] Dout_32_7,
  output Dout_1_10,
  output \传输状态Out_表明当前传输数据有效 
);

  wire multiplexer_1_out, multiplexer_2_out, multiplexer_3_out, multiplexer_4_out, multiplexer_5_out,
       multiplexer_6_out, multiplexer_7_out, multiplexer_14_out, multiplexer_15_out, multiplexer_18_out,
       multiplexer_19_out, not_1_out;
  wire [4:0] multiplexer_12_out;
  wire [31:0] multiplexer_8_out, multiplexer_9_out, multiplexer_10_out, multiplexer_11_out,
       multiplexer_13_out, multiplexer_16_out, multiplexer_17_out;

  Multiplexer #(.enable("false")) multiplexer_1 (
    .in0(Din_1), .in1(1'b0), .out(multiplexer_1_out), .sel(\同步清零_气泡_高电平有效 ));
  Multiplexer #(.enable("false")) multiplexer_2 (
    .in0(Din_1_2), .in1(1'b0), .out(multiplexer_2_out), .sel(\同步清零_气泡_高电平有效 ));
  Multiplexer #(.enable("false")) multiplexer_3 (
    .in0(Din_1_3), .in1(1'b0), .out(multiplexer_3_out), .sel(\同步清零_气泡_高电平有效 ));
  Multiplexer #(.enable("false")) multiplexer_4 (
    .in0(Din_1_4), .in1(1'b0), .out(multiplexer_4_out), .sel(\同步清零_气泡_高电平有效 ));
  Multiplexer #(.enable("false")) multiplexer_5 (
    .in0(Din_1_5), .in1(1'b0), .out(multiplexer_5_out), .sel(\同步清零_气泡_高电平有效 ));
  Multiplexer #(.enable("false")) multiplexer_6 (
    .in0(Din_1_6), .in1(1'b0), .out(multiplexer_6_out), .sel(\同步清零_气泡_高电平有效 ));
  Multiplexer #(.enable("false")) multiplexer_7 (
    .in0(Din_1_7), .in1(1'b0), .out(multiplexer_7_out), .sel(\同步清零_气泡_高电平有效 ));
  Multiplexer #(.width(32), .enable("false")) multiplexer_8 (
    .in0(Din_32), .out(multiplexer_8_out), .sel(\同步清零_气泡_高电平有效 ));  // open: in1
  Multiplexer #(.width(32), .enable("false")) multiplexer_9 (
    .in0(Din_32_2), .in1({32{1'b0}}), .out(multiplexer_9_out), .sel(\同步清零_气泡_高电平有效 ));
  Multiplexer #(.width(32), .enable("false")) multiplexer_10 (
    .in0(Din_32_3), .in1({32{1'b0}}), .out(multiplexer_10_out), .sel(\同步清零_气泡_高电平有效 ));
  Multiplexer #(.width(32), .enable("false")) multiplexer_11 (
    .in0(Din_32_4), .in1({32{1'b0}}), .out(multiplexer_11_out), .sel(\同步清零_气泡_高电平有效 ));
  Multiplexer #(.width(5), .enable("false")) multiplexer_12 (
    .in0(Din_5), .in1({5{1'b0}}), .out(multiplexer_12_out), .sel(\同步清零_气泡_高电平有效 ));
  Multiplexer #(.width(32), .enable("false")) multiplexer_13 (
    .in0(Din_32_5), .out(multiplexer_13_out), .sel(\同步清零_气泡_高电平有效 ));  // open: in1
  Multiplexer #(.enable("false")) multiplexer_14 (
    .in0(Din_1_8), .in1(1'b0), .out(multiplexer_14_out), .sel(\同步清零_气泡_高电平有效 ));
  Multiplexer #(.enable("false")) multiplexer_15 (
    .in0(Din_1_9), .in1(1'b0), .out(multiplexer_15_out), .sel(\同步清零_气泡_高电平有效 ));
  Multiplexer #(.width(32), .enable("false")) multiplexer_16 (
    .in0(Din_32_6), .in1({32{1'b0}}), .out(multiplexer_16_out), .sel(\同步清零_气泡_高电平有效 ));
  Multiplexer #(.width(32), .enable("false")) multiplexer_17 (
    .in0(Din_32_7), .in1({32{1'b0}}), .out(multiplexer_17_out), .sel(\同步清零_气泡_高电平有效 ));
  Multiplexer #(.enable("false")) multiplexer_18 (
    .in0(Din_1_10), .in1(1'b0), .out(multiplexer_18_out), .sel(\同步清零_气泡_高电平有效 ));
  Multiplexer #(.enable("false")) multiplexer_19 (
    .in0(\传输状态In_表明当前传输数据有效 ), .in1(1'b0), .out(multiplexer_19_out), .sel(\同步清零_气泡_高电平有效 ));
  Register #(.width(1)) register_1 (.D(multiplexer_1_out), .en(not_1_out), .Q(Dout_1), .clk(CLK));  // open: clr
  Register #(.width(1)) register_2 (.D(multiplexer_2_out), .en(not_1_out), .Q(Dout_1_2), .clk(CLK));  // open: clr
  Register #(.width(1)) register_3 (.D(multiplexer_3_out), .en(not_1_out), .Q(Dout_1_3), .clk(CLK));  // open: clr
  Register #(.width(1)) register_4 (.D(multiplexer_4_out), .en(not_1_out), .Q(Dout_1_4), .clk(CLK));  // open: clr
  Register #(.width(1)) register_5 (.D(multiplexer_5_out), .en(not_1_out), .Q(Dout_1_5), .clk(CLK));  // open: clr
  Register #(.width(1)) register_6 (.D(multiplexer_6_out), .en(not_1_out), .Q(Dout_1_6), .clk(CLK));  // open: clr
  Register #(.width(1)) register_7 (.D(multiplexer_7_out), .Q(Dout_1_7), .clk(CLK));  // open: en, clr
  Register #(.width(32)) register_8 (.D(multiplexer_8_out), .en(not_1_out), .Q(Dout_32), .clk(CLK));  // open: clr
  Register #(.width(32)) register_9 (.D(multiplexer_9_out), .en(not_1_out), .Q(Dout_32_2), .clk(CLK));  // open: clr
  Register #(.width(32)) register_10 (.D(multiplexer_10_out), .en(not_1_out), .Q(Dout_32_3), .clk(CLK));  // open: clr
  Register #(.width(32)) register_11 (.D(multiplexer_11_out), .en(not_1_out), .Q(Dout_32_4), .clk(CLK));  // open: clr
  Register #(.width(5)) register_12 (.D(multiplexer_12_out), .en(not_1_out), .Q(Dout_5), .clk(CLK));  // open: clr
  Register #(.width(32)) register_13 (.D(multiplexer_13_out), .en(not_1_out), .Q(Dout_32_5), .clk(CLK));  // open: clr
  Register #(.width(1)) register_14 (.D(multiplexer_14_out), .en(not_1_out), .Q(Dout_1_8), .clk(CLK));  // open: clr
  Register #(.width(1)) register_15 (.D(multiplexer_15_out), .en(not_1_out), .Q(Dout_1_9), .clk(CLK));  // open: clr
  Register #(.width(32)) register_16 (.D(multiplexer_16_out), .en(not_1_out), .Q(Dout_32_6), .clk(CLK));  // open: clr
  Register #(.width(32)) register_17 (.D(multiplexer_17_out), .en(not_1_out), .Q(Dout_32_7), .clk(CLK));  // open: clr
  Register #(.width(1)) register_18 (.D(multiplexer_18_out), .en(not_1_out), .Q(Dout_1_10), .clk(CLK));  // open: clr
  Register #(.width(1)) register_19 (
    .D(multiplexer_19_out), .en(not_1_out), .Q(\传输状态Out_表明当前传输数据有效 ), .clk(CLK));  // open: clr
  not not_1 (not_1_out, \使能端_低电平有效_stall_高电平有效 );
endmodule

module MEM_WB (
  input  Din_1,
  input  Din_1_2,
  input  Din_1_3,
  input  Din_1_4,
  input  Din_1_5,
  input  [31:0] Din_32,
  input  [31:0] Din_32_2,
  input  [31:0] Din_32_3,
  input  [31:0] Din_32_4,
  input  [4:0] Din_5,
  input  [31:0] Din_32_5,
  input  Din_1_6,
  input  Din_1_7,
  input  [31:0] Din_32_6,
  input  [31:0] Din_32_7,
  input  Din_1_8,
  input  \传输状态In_表明当前传输数据有效 ,
  input  CLK,
  input  \同步清零_气泡_高电平有效 ,
  input  \使能端_低电平有效_stall_高电平有效 ,
  output Dout_1,
  output Dout_1_2,
  output Dout_1_3,
  output Dout_1_4,
  output Dout_1_5,
  output [31:0] Dout_32,
  output [31:0] Dout_32_2,
  output [31:0] Dout_32_3,
  output [31:0] Dout_32_4,
  output [4:0] Dout_5,
  output [31:0] Dout_32_5,
  output Dout_1_6,
  output Dout_1_7,
  output [31:0] Dout_32_6,
  output [31:0] Dout_32_7,
  output Dout_1_8,
  output \传输状态Out_表明当前传输数据有效 
);

  wire multiplexer_1_out, multiplexer_2_out, multiplexer_3_out, multiplexer_4_out, multiplexer_5_out,
       multiplexer_12_out, multiplexer_13_out, multiplexer_16_out, multiplexer_17_out, not_1_out;
  wire [4:0] multiplexer_10_out;
  wire [31:0] multiplexer_6_out, multiplexer_7_out, multiplexer_8_out, multiplexer_9_out, multiplexer_11_out,
       multiplexer_14_out, multiplexer_15_out;

  Multiplexer #(.enable("false")) multiplexer_1 (
    .in0(Din_1), .in1(1'b0), .out(multiplexer_1_out), .sel(\同步清零_气泡_高电平有效 ));
  Multiplexer #(.enable("false")) multiplexer_2 (
    .in0(Din_1_2), .in1(1'b0), .out(multiplexer_2_out), .sel(\同步清零_气泡_高电平有效 ));
  Multiplexer #(.enable("false")) multiplexer_3 (
    .in0(Din_1_3), .in1(1'b0), .out(multiplexer_3_out), .sel(\同步清零_气泡_高电平有效 ));
  Multiplexer #(.enable("false")) multiplexer_4 (
    .in0(Din_1_4), .in1(1'b0), .out(multiplexer_4_out), .sel(\同步清零_气泡_高电平有效 ));
  Multiplexer #(.enable("false")) multiplexer_5 (
    .in0(Din_1_5), .in1(1'b0), .out(multiplexer_5_out), .sel(\同步清零_气泡_高电平有效 ));
  Multiplexer #(.width(32), .enable("false")) multiplexer_6 (
    .in0(Din_32), .in1({32{1'b0}}), .out(multiplexer_6_out), .sel(\同步清零_气泡_高电平有效 ));
  Multiplexer #(.width(32), .enable("false")) multiplexer_7 (
    .in0(Din_32_2), .in1({32{1'b0}}), .out(multiplexer_7_out), .sel(\同步清零_气泡_高电平有效 ));
  Multiplexer #(.width(32), .enable("false")) multiplexer_8 (
    .in0(Din_32_3), .in1({32{1'b0}}), .out(multiplexer_8_out), .sel(\同步清零_气泡_高电平有效 ));
  Multiplexer #(.width(32), .enable("false")) multiplexer_9 (
    .in0(Din_32_4), .in1({32{1'b0}}), .out(multiplexer_9_out), .sel(\同步清零_气泡_高电平有效 ));
  Multiplexer #(.width(5), .enable("false")) multiplexer_10 (
    .in0(Din_5), .in1({5{1'b0}}), .out(multiplexer_10_out), .sel(\同步清零_气泡_高电平有效 ));
  Multiplexer #(.width(32), .enable("false")) multiplexer_11 (
    .in0(Din_32_5), .out(multiplexer_11_out), .sel(\同步清零_气泡_高电平有效 ));  // open: in1
  Multiplexer #(.enable("false")) multiplexer_12 (
    .in0(Din_1_6), .in1(1'b0), .out(multiplexer_12_out), .sel(\同步清零_气泡_高电平有效 ));
  Multiplexer #(.enable("false")) multiplexer_13 (
    .in0(Din_1_7), .in1(1'b0), .out(multiplexer_13_out), .sel(\同步清零_气泡_高电平有效 ));
  Multiplexer #(.width(32), .enable("false")) multiplexer_14 (
    .in0(Din_32_6), .in1({32{1'b0}}), .out(multiplexer_14_out), .sel(\同步清零_气泡_高电平有效 ));
  Multiplexer #(.width(32), .enable("false")) multiplexer_15 (
    .in0(Din_32_7), .in1({32{1'b0}}), .out(multiplexer_15_out), .sel(\同步清零_气泡_高电平有效 ));
  Multiplexer #(.enable("false")) multiplexer_16 (
    .in0(Din_1_8), .in1(1'b0), .out(multiplexer_16_out), .sel(\同步清零_气泡_高电平有效 ));
  Multiplexer #(.enable("false")) multiplexer_17 (
    .in0(\传输状态In_表明当前传输数据有效 ), .in1(1'b0), .out(multiplexer_17_out), .sel(\同步清零_气泡_高电平有效 ));
  not not_1 (not_1_out, \使能端_低电平有效_stall_高电平有效 );
  Register #(.width(1)) register_1 (.D(multiplexer_1_out), .en(not_1_out), .Q(Dout_1), .clk(CLK));  // open: clr
  Register #(.width(1)) register_2 (.D(multiplexer_2_out), .en(not_1_out), .Q(Dout_1_2), .clk(CLK));  // open: clr
  Register #(.width(1)) register_3 (.D(multiplexer_3_out), .en(not_1_out), .Q(Dout_1_3), .clk(CLK));  // open: clr
  Register #(.width(1)) register_4 (.D(multiplexer_4_out), .en(not_1_out), .Q(Dout_1_4), .clk(CLK));  // open: clr
  Register #(.width(1)) register_5 (.D(multiplexer_5_out), .en(not_1_out), .Q(Dout_1_5), .clk(CLK));  // open: clr
  Register #(.width(32)) register_6 (.D(multiplexer_6_out), .en(not_1_out), .Q(Dout_32), .clk(CLK));  // open: clr
  Register #(.width(32)) register_7 (.D(multiplexer_7_out), .en(not_1_out), .Q(Dout_32_2), .clk(CLK));  // open: clr
  Register #(.width(32)) register_8 (.D(multiplexer_8_out), .en(not_1_out), .Q(Dout_32_3), .clk(CLK));  // open: clr
  Register #(.width(32)) register_9 (.D(multiplexer_9_out), .en(not_1_out), .Q(Dout_32_4), .clk(CLK));  // open: clr
  Register #(.width(5)) register_10 (.D(multiplexer_10_out), .en(not_1_out), .Q(Dout_5), .clk(CLK));  // open: clr
  Register #(.width(32)) register_11 (.D(multiplexer_11_out), .en(not_1_out), .Q(Dout_32_5), .clk(CLK));  // open: clr
  Register #(.width(1)) register_12 (.D(multiplexer_12_out), .en(not_1_out), .Q(Dout_1_6), .clk(CLK));  // open: clr
  Register #(.width(1)) register_13 (.D(multiplexer_13_out), .en(not_1_out), .Q(Dout_1_7), .clk(CLK));  // open: clr
  Register #(.width(32)) register_14 (.D(multiplexer_14_out), .en(not_1_out), .Q(Dout_32_6), .clk(CLK));  // open: clr
  Register #(.width(32)) register_15 (.D(multiplexer_15_out), .en(not_1_out), .Q(Dout_32_7), .clk(CLK));  // open: clr
  Register #(.width(1)) register_16 (.D(multiplexer_16_out), .en(not_1_out), .Q(Dout_1_8), .clk(CLK));  // open: clr
  Register #(.width(1)) register_17 (
    .D(multiplexer_17_out), .en(not_1_out), .Q(\传输状态Out_表明当前传输数据有效 ), .clk(CLK));  // open: clr
endmodule

module \分支相关流水线  (
);

  wire and_1_out, and_2_out, and_3_out, and_4_out, and_5_out, Bench, CLK, comparator_1_eq, comparator_2_lt,
       ex_mem_1_dout_1, ex_mem_1_dout_1_2, ex_mem_1_dout_1_3, ex_mem_1_dout_1_4, ex_mem_1_dout_1_5,
       ex_mem_1_dout_1_6, ex_mem_1_dout_1_7, \ex_mem_1_传输状态out_表明当前传输数据有效 , Go, \id_ex_1_传输状态out_表明当前传输数据有效 ,
       \if_id_1_传输状态out_表明当前传输数据有效 , IR1, IR2, IR3, mem_wb_1_dout_1, mem_wb_1_dout_1_2, mem_wb_1_dout_1_3,
       mem_wb_1_dout_1_4, mem_wb_1_dout_1_5, mips_alu_1_equal, nor_1_out, not_1_out, not_2_out, not_3_out,
       not_4_out, not_5_out, or_1_out, or_2_out, register_1_q, RST, W1, W2, W3, \硬布线控制器_1_regdst ,
       \硬布线控制器_1_signedext ;
  wire [3:0] id_ex_1_dout_4, id_ex_1_dout_4_2, id_ex_1_dout_4_3, id_ex_1_dout_4_4, multiplexer_13_out,
       multiplexer_14_out, \硬布线控制器_1_alu_op , \硬布线控制器_1_alu_src , \硬布线控制器_1_beq , \硬布线控制器_1_bltz ;
  wire [4:0] ex_mem_1_dout_5, id_ex_1_dout_5, id_ex_1_dout_5_2, mem_wb_1_dout_5, multiplexer_2_out,
       multiplexer_3_out, multiplexer_4_out, multiplexer_6_out;
  wire [11:0] EX_PC, ID_PC, IF_PC, MEM_PC, WB_PC;
  wire [15:0] \LoadUse次数 , \总周期数 , \插入气泡数 , \无条件分支数 , \条件分支成功数 ;
  wire [31:0] adder_1_out, adder_2_out, bit_extender_1_out, bit_extender_2_out, bit_extender_3_out,
       ex_mem_1_dout_32, ex_mem_1_dout_32_2, ex_mem_1_dout_32_3, ex_mem_1_dout_32_4, id_ex_1_dout_32,
       id_ex_1_dout_32_2, id_ex_1_dout_32_3, id_ex_1_dout_32_4, id_ex_1_dout_32_5, if_id_1_dout_ins,
       if_id_1_dout_pc_4, LedData, mem_wb_1_dout_32_2, mem_wb_1_dout_32_3, mem_wb_1_dout_32_4,
       mips_alu_1_result, mips_ram_1_p8, mips_regifile_1_r1, mips_regifile_1_r2, multiplexer_1_out,
       multiplexer_5_out, multiplexer_7_out, multiplexer_8_out, multiplexer_9_out, multiplexer_10_out,
       multiplexer_11_out, multiplexer_12_out, multiplexer_15_out, multiplexer_16_out, PC_q, register_2_q,
       rom_1_data, shifter_1_out, shifter_2_out;

  Button \u_总复位  (.out(RST));
  Button _1 (.out(IR1));
  Button _2 (.out(IR2));
  Button _3 (.out(IR3));
  and and_1 (and_1_out, mem_wb_1_dout_1_2, not_1_out);
  not not_1 (not_1_out, mem_wb_1_dout_1);
  Button \u_继续运行  (.out(Go));
  LED led_1 (.in(W1));
  LED led_2 (.in(W2));
  LED led_3 (.in(W3));
  Counter #(.width(16), .max('hffff)) counter_1 (
    .count(not_2_out), .Q(\总周期数 ), .clk(CLK), .clr(RST));  // open: load, D, carry
  Register #(.width(32)) PC (.D(multiplexer_1_out), .en(not_2_out), .Q(PC_q), .clk(CLK), .clr(RST));
  Register #(.width(1)) register_1 (.D(mem_wb_1_dout_1_2), .en(and_1_out), .Q(register_1_q), .clk(CLK), .clr(or_1_out));
  or or_1 (or_1_out, Go, RST);
  Hex_Digit_Display hex_digit_display_1 (.value(LedData[31:28]));  // open: dp
  Adder #(.width(32)) adder_1 (.a(PC_q), .b(32'h4), .out(adder_1_out));  // open: cin, cout
  not not_2 (not_2_out, register_1_q);
  Multiplexer #(.width(32), .enable("false")) multiplexer_1 (
    .in0(adder_1_out), .in1(multiplexer_10_out), .out(multiplexer_1_out), .sel(Bench));
  Hex_Digit_Display hex_digit_display_2 (.value(LedData[27:24]));  // open: dp
  Hex_Digit_Display hex_digit_display_3 (.value(LedData[23:20]));  // open: dp
  Hex_Digit_Display hex_digit_display_4 (.value(LedData[15:12]));  // open: dp
  Hex_Digit_Display hex_digit_display_5 (.value(LedData[19:16]));  // open: dp
  IF_ID if_id_1 (
    .Din_Ins(rom_1_data), .Din_PC_4(adder_1_out), .\传输状态In_表明当前传输数据有效 (1'b1), .CLK(CLK),
    .Dout_Ins(if_id_1_dout_ins), .Dout_PC_4(if_id_1_dout_pc_4),
    .\传输状态Out_表明当前传输数据有效 (\if_id_1_传输状态out_表明当前传输数据有效 ), .\同步清零_气泡_高电平有效 (Bench),
    .\使能端_低电平有效_stall_高电平有效 (1'b0));  // open: Din_PC, Dout_PC, Din_Status, Dout_Status, Din_Addr, Dout_Addr, Din_Miss, Dout_Miss, Din_Hit, Dout_Hit
  ROM #(.addrWidth(10), .dataWidth(32)) rom_1 (.addr(PC_q[11:2]), .data(rom_1_data));  // open: sel
  Hex_Digit_Display hex_digit_display_6 (.value(LedData[11:8]));  // open: dp
  Hex_Digit_Display hex_digit_display_7 (.value(LedData[7:4]));  // open: dp
  Clock clock_1 (.out(CLK));
  Hex_Digit_Display hex_digit_display_8 (.value(LedData[3:0]));  // open: dp
  \硬布线控制器  \u_硬布线控制器_1  (
    .Func(if_id_1_dout_ins[5:0]), .OP(if_id_1_dout_ins[31:26]), .ALU_OP(\硬布线控制器_1_alu_op ),
    .MemToReg(\硬布线控制器_1_beq [2]), .MemWrite(\硬布线控制器_1_beq [3]), .ALU_SRC(\硬布线控制器_1_alu_src [0]),
    .RegWrite(\硬布线控制器_1_alu_src [1]), .SysCALL(\硬布线控制器_1_alu_src [3]), .SignedExt(\硬布线控制器_1_signedext ),
    .RegDst(\硬布线控制器_1_regdst ), .JR(\硬布线控制器_1_bltz [2]), .JMP(\硬布线控制器_1_bltz [3]), .Beq(\硬布线控制器_1_beq [0]),
    .JAL(\硬布线控制器_1_alu_src [2]), .Bne(\硬布线控制器_1_beq [1]), .SH(\硬布线控制器_1_bltz [1]), .BLTZ(\硬布线控制器_1_bltz [0]));  // open: ERET, MF, MFC0, MTC0
  Multiplexer #(.width(5), .enable("false")) multiplexer_2 (
    .in0(if_id_1_dout_ins[20:16]), .in1(if_id_1_dout_ins[15:11]), .out(multiplexer_2_out),
    .sel(\硬布线控制器_1_regdst ));
  assign bit_extender_1_out = {{16{1'b0}}, if_id_1_dout_ins[15:0]};  // Bit_Extender bit_extender_1
  assign bit_extender_2_out = {{16{if_id_1_dout_ins[15]}}, if_id_1_dout_ins[15:0]};  // Bit_Extender bit_extender_2
  assign bit_extender_3_out = {{6{if_id_1_dout_ins[25]}}, if_id_1_dout_ins[25:0]};  // Bit_Extender bit_extender_3
  Multiplexer #(.width(5), .enable("false")) multiplexer_3 (
    .in0(if_id_1_dout_ins[25:21]), .in1(5'b00100), .out(multiplexer_3_out), .sel(\硬布线控制器_1_alu_src [3]));
  Multiplexer #(.width(5), .enable("false")) multiplexer_4 (
    .in0(multiplexer_2_out), .in1({5{1'b1}}), .out(multiplexer_4_out), .sel(\硬布线控制器_1_alu_src [2]));
  Multiplexer #(.width(32), .enable("false")) multiplexer_5 (
    .in0(bit_extender_1_out), .in1(bit_extender_2_out), .out(multiplexer_5_out), .sel(\硬布线控制器_1_signedext ));
  // Probe on \总周期数 
  // Probe on \无条件分支数 
  // Probe on \条件分支成功数 
  // Probe on \插入气泡数 
  // Probe on \LoadUse次数 
  Multiplexer #(.width(5), .enable("false")) multiplexer_6 (
    .in0(if_id_1_dout_ins[20:16]), .in1(5'b00010), .out(multiplexer_6_out), .sel(\硬布线控制器_1_alu_src [3]));
  // Probe on IF_PC
  MIPS_Regifile mips_regifile_1 (
    .Din(multiplexer_16_out), .Clk(CLK), .R1(mips_regifile_1_r1), .R2(mips_regifile_1_r2),
    .WE(mem_wb_1_dout_1_4), .W_num(mem_wb_1_dout_5), .R1_num(multiplexer_3_out), .R2_num(multiplexer_6_out));
  // Probe on ID_PC
  ID_EX id_ex_1 (
    .Din_4(\硬布线控制器_1_bltz ), .Din_4_2(\硬布线控制器_1_beq ), .Din_4_3(\硬布线控制器_1_alu_op ),
    .Din_4_4(\硬布线控制器_1_alu_src ), .Din_32(mips_regifile_1_r1), .Din_32_2(mips_regifile_1_r2),
    .Din_32_3(multiplexer_5_out), .Din_32_4(bit_extender_3_out), .Din_5(if_id_1_dout_ins[10:6]),
    .Din_32_5(if_id_1_dout_pc_4), .\传输状态In_表明当前传输数据有效 (\if_id_1_传输状态out_表明当前传输数据有效 ), .CLK(CLK),
    .Dout_4(id_ex_1_dout_4), .Dout_4_2(id_ex_1_dout_4_2), .Dout_4_3(id_ex_1_dout_4_3),
    .Dout_4_4(id_ex_1_dout_4_4), .Dout_32(id_ex_1_dout_32), .Dout_32_2(id_ex_1_dout_32_2),
    .Dout_32_3(id_ex_1_dout_32_3), .Dout_32_4(id_ex_1_dout_32_4), .Dout_5(id_ex_1_dout_5),
    .Dout_32_5(id_ex_1_dout_32_5), .\传输状态Out_表明当前传输数据有效 (\id_ex_1_传输状态out_表明当前传输数据有效 ),
    .\同步清零_气泡_高电平有效 (Bench), .\使能端_低电平有效_stall_高电平有效 (1'b0), .Din_5_2(multiplexer_4_out),
    .Dout_5_2(id_ex_1_dout_5_2));  // open: Din_32_6, Dout_32_6, Din_2, Dout_2, Din_2_2, Dout_2_2, Din_2_3, Dout_2_3, Din_32_7, Dout_32_7, Din_1, Dout_1, Din_1_2, Dout_1_2
  // Probe on EX_PC
  // Probe on MEM_PC
  and and_2 (and_2_out, comparator_1_eq, id_ex_1_dout_4_4[3]);
  // Probe on WB_PC
  Register #(.width(32)) register_2 (.D(id_ex_1_dout_32), .en(and_2_out), .Q(register_2_q), .clk(CLK), .clr(RST));
  Comparator #(.width(32)) comparator_1 (.a(32'h22), .b(id_ex_1_dout_32_2), .eq(comparator_1_eq));  // open: gt, lt
  Multiplexer #(.width(32), .enable("false")) multiplexer_7 (
    .in0(id_ex_1_dout_32_2), .in1(id_ex_1_dout_32_3), .out(multiplexer_7_out), .sel(id_ex_1_dout_4_4[0]));
  Shifter #(.width(32)) shifter_1 (.in(id_ex_1_dout_32_3), .\dist (5'b00010), .out(shifter_1_out));
  Shifter #(.width(32)) shifter_2 (.in(id_ex_1_dout_32_4), .\dist (5'b00010), .out(shifter_2_out));
  MIPS_ALU mips_alu_1 (
    .X(id_ex_1_dout_32), .Y(multiplexer_7_out), .AluOP(id_ex_1_dout_4_3), .Equal(mips_alu_1_equal),
    .Result(mips_alu_1_result), .shamt(id_ex_1_dout_5));  // open: Result_2
  not not_3 (not_3_out, mips_alu_1_equal);
  Adder #(.width(32)) adder_2 (.a(shifter_1_out), .b(id_ex_1_dout_32_5), .out(adder_2_out));  // open: cin, cout
  and and_3 (and_3_out, id_ex_1_dout_4_2[0], mips_alu_1_equal);
  or or_2 (or_2_out, and_3_out, and_4_out);
  and and_4 (and_4_out, id_ex_1_dout_4_2[1], not_3_out);
  Comparator #(.width(32)) comparator_2 (.a(id_ex_1_dout_32), .b({32{1'b0}}), .lt(comparator_2_lt));  // open: gt, eq
  not not_4 (not_4_out, id_ex_1_dout_4[2]);
  and and_5 (and_5_out, id_ex_1_dout_4[0], comparator_2_lt);
  nor nor_1 (nor_1_out, and_5_out, or_2_out);
  Multiplexer #(.width(32), .enable("false")) multiplexer_8 (
    .in0(adder_2_out), .in1(id_ex_1_dout_32_5), .out(multiplexer_8_out), .sel(nor_1_out));
  not not_5 (not_5_out, id_ex_1_dout_4[3]);
  or or_3 (Bench, and_5_out, or_2_out, id_ex_1_dout_4[3]);
  Multiplexer #(.width(32), .enable("false")) multiplexer_9 (
    .in0(id_ex_1_dout_32), .in1(shifter_2_out), .out(multiplexer_9_out), .sel(not_4_out));
  Multiplexer #(.width(32), .enable("false")) multiplexer_10 (
    .in0(multiplexer_9_out), .in1(multiplexer_8_out), .out(multiplexer_10_out), .sel(not_5_out));
  EX_MEM ex_mem_1 (
    .Din_1_4(id_ex_1_dout_4_2[2]), .Din_1_5(id_ex_1_dout_4_2[3]), .Din_32_2(mips_alu_1_result),
    .Din_32_3(id_ex_1_dout_32_2), .Din_32_4(id_ex_1_dout_32_5),
    .\传输状态In_表明当前传输数据有效 (\id_ex_1_传输状态out_表明当前传输数据有效 ), .CLK(CLK), .Dout_1_4(ex_mem_1_dout_1_4),
    .Dout_1_5(ex_mem_1_dout_1_5), .Dout_32_2(ex_mem_1_dout_32_2), .Dout_32_3(ex_mem_1_dout_32_3),
    .Dout_32_4(ex_mem_1_dout_32_4), .\传输状态Out_表明当前传输数据有效 (\ex_mem_1_传输状态out_表明当前传输数据有效 ),
    .\同步清零_气泡_高电平有效 (1'b0), .\使能端_低电平有效_stall_高电平有效 (1'b0), .Din_1_6(id_ex_1_dout_4_4[1]),
    .Dout_1_6(ex_mem_1_dout_1_6), .Din_1_7(id_ex_1_dout_4_4[2]), .Dout_1_7(ex_mem_1_dout_1_7),
    .Din_32(register_2_q), .Dout_32(ex_mem_1_dout_32), .Dout_1_3(ex_mem_1_dout_1_3),
    .Din_1_3(id_ex_1_dout_4_4[3]), .Din_1_2(comparator_1_eq), .Dout_1_2(ex_mem_1_dout_1_2),
    .Din_1(id_ex_1_dout_4[1]), .Dout_1(ex_mem_1_dout_1), .Din_5(id_ex_1_dout_5_2), .Dout_5(ex_mem_1_dout_5));  // open: Din_32_5, Dout_32_5, Din_1_8, Dout_1_8, Din_1_9, Dout_1_9, Dout_32_6, Dout_32_7, Din_32_6, Din_32_7, Din_1_10, Dout_1_10
  Multiplexer #(.width(32), .enable("false")) multiplexer_11 (
    .in0(ex_mem_1_dout_32_3), .in1(multiplexer_12_out), .out(multiplexer_11_out), .sel(ex_mem_1_dout_1));
  Multiplexer #(.width(32), .enable("false")) multiplexer_12 (
    .in0({{16{1'b0}}, ex_mem_1_dout_32_3[15:0]}), .in1({ex_mem_1_dout_32_3[15:0], {16{1'b0}}}),
    .out(multiplexer_12_out), .sel(ex_mem_1_dout_32_2[1]));
  Multiplexer #(.width(4), .enable("false")) multiplexer_13 (
    .in0(4'b1111), .in1(multiplexer_14_out), .out(multiplexer_13_out), .sel(ex_mem_1_dout_1));
  Multiplexer #(.width(4), .enable("false")) multiplexer_14 (
    .in0(4'b0011), .in1(4'b1100), .out(multiplexer_14_out), .sel(ex_mem_1_dout_32_2[1]));
  MEM_WB mem_wb_1 (
    .Din_1_4(ex_mem_1_dout_1_6), .Din_1_5(ex_mem_1_dout_1_7), .Din_32(ex_mem_1_dout_32),
    .Din_32_3(mips_ram_1_p8), .Din_32_4(ex_mem_1_dout_32_4),
    .\传输状态In_表明当前传输数据有效 (\ex_mem_1_传输状态out_表明当前传输数据有效 ), .CLK(CLK), .Dout_1_4(mem_wb_1_dout_1_4),
    .Dout_1_5(mem_wb_1_dout_1_5), .Dout_32(LedData), .Dout_32_3(mem_wb_1_dout_32_3),
    .Dout_32_4(mem_wb_1_dout_32_4), .\同步清零_气泡_高电平有效 (1'b0), .\使能端_低电平有效_stall_高电平有效 (1'b0),
    .Dout_1(mem_wb_1_dout_1), .Dout_1_2(mem_wb_1_dout_1_2), .Din_1(ex_mem_1_dout_1_2),
    .Din_1_2(ex_mem_1_dout_1_3), .Din_5(ex_mem_1_dout_5), .Dout_5(mem_wb_1_dout_5),
    .Din_1_3(ex_mem_1_dout_1_4), .Dout_1_3(mem_wb_1_dout_1_3), .Din_32_2(ex_mem_1_dout_32_2),
    .Dout_32_2(mem_wb_1_dout_32_2));  // open: 传输状态Out_表明当前传输数据有效, Din_32_5, Dout_32_5, Din_1_6, Dout_1_6, Din_1_7, Dout_1_7, Din_32_6, Dout_32_6, Din_32_7, Dout_32_7, Din_1_8, Dout_1_8
  // MIPS_RAM mips_ram_1: pin names not known; wires that end beside it: ex_mem_1_dout_32_2[11:2], multiplexer_11_out, ex_mem_1_dout_1_5, multiplexer_13_out, CLK, 1'b1, RST, mips_ram_1_p8
  Multiplexer #(.width(32), .enable("false")) multiplexer_15 (
    .in0(mem_wb_1_dout_32_2), .in1(mem_wb_1_dout_32_3), .out(multiplexer_15_out), .sel(mem_wb_1_dout_1_3));
  Multiplexer #(.width(32), .enable("false")) multiplexer_16 (
    .in0(multiplexer_15_out), .in1(mem_wb_1_dout_32_4), .out(multiplexer_16_out), .sel(mem_wb_1_dout_1_5));

  // Notes on the sheet:
  //   中断源
  //   中断等待指示
  //   指令字
  //   指令存储器
  //   数码管输出
  //   IF/ID
  //   contents of rom_1 (hex, n*v repeats v):
  //   20110020 20020022 8000c06 20110000 20110000 2002000a 10000003 20110000 20110000 2002000a 14110003
  //   20110000 20110000 2002000a c000c14 2002000a 0 0 0 c 2231ffff 0 0 0 112020 0 0 0 c 1620fff6 3e00008
  //   JMP
  //   JR
  //   SH
  //   Bltz
  //   OP
  //   Func
  //   rs
  //   rt
  //   rd
  //   Beq
  //   Bne
  //   MemToReg
  //   MemWrite
  //   AluOP
  //   AluSrcB
  //   RegWrite
  //   JAL
  //   RegDst
  //   Syscall
  //   ID/EX
  //   流水调试日志用
  //   EX/MEM
  //   MEM/WB
endmodule

module \气泡流水线  (
);

  wire and_2_out, and_3_out, and_5_out, and_6_out, and_7_out, and_8_out, Bench, Benchif, CLK,
       comparator_1_eq, comparator_2_lt, Enable, ex_mem_1_dout_1, ex_mem_1_dout_1_2, ex_mem_1_dout_1_3,
       ex_mem_1_dout_1_4, ex_mem_1_dout_1_5, ex_mem_1_dout_1_6, ex_mem_1_dout_1_7,
       \ex_mem_1_传输状态out_表明当前传输数据有效 , Go, \id_ex_1_传输状态out_表明当前传输数据有效 , \if_id_1_传输状态out_表明当前传输数据有效 , IR1,
       IR2, IR3, JMP, mem_wb_1_dout_1, mem_wb_1_dout_1_2, mem_wb_1_dout_1_3, mem_wb_1_dout_1_4,
       mem_wb_1_dout_1_5, mips_alu_1_equal, nor_1_out, nor_2_out, not_1_out, not_2_out, not_4_out, not_5_out,
       not_6_out, not_7_out, not_8_out, or_1_out, or_2_out, or_3_out, or_4_out, register_1_q, RST, Run,
       Stop1, Stop2, W1, W2, W3, \数据相关 , \硬布线控制器_1_regdst , \硬布线控制器_1_signedext ;
  wire [2:0] id_ex_1_dout_4;
  wire [3:0] id_ex_1_dout_4_2, id_ex_1_dout_4_3, id_ex_1_dout_4_4, multiplexer_13_out, multiplexer_14_out,
       \硬布线控制器_1_alu_op , \硬布线控制器_1_alu_src , \硬布线控制器_1_beq , \硬布线控制器_1_bltz ;
  wire [4:0] ex_mem_1_dout_5, id_ex_1_dout_5, id_ex_1_dout_5_2, mem_wb_1_dout_5, multiplexer_2_out,
       multiplexer_3_out, multiplexer_4_out, multiplexer_6_out;
  wire [15:0] \LoadUse次数 , \总周期数 , \插入气泡数 , \无条件分支数 , \条件分支成功数 ;
  wire [31:0] adder_1_out, adder_2_out, bit_extender_1_out, bit_extender_2_out, bit_extender_3_out,
       ex_mem_1_dout_32, ex_mem_1_dout_32_2, ex_mem_1_dout_32_3, ex_mem_1_dout_32_4, EX_PC, id_ex_1_dout_32,
       id_ex_1_dout_32_2, id_ex_1_dout_32_3, id_ex_1_dout_32_4, id_ex_1_dout_32_5, ID_PC, if_id_1_dout_ins,
       if_id_1_dout_pc_4, IF_PC, LedData, MEM_PC, mem_wb_1_dout_32_2, mem_wb_1_dout_32_3, mem_wb_1_dout_32_4,
       mips_alu_1_result, mips_ram_1_p8, mips_regifile_1_r1, mips_regifile_1_r2, multiplexer_1_out,
       multiplexer_5_out, multiplexer_7_out, multiplexer_8_out, multiplexer_9_out, multiplexer_10_out,
       multiplexer_11_out, multiplexer_12_out, multiplexer_15_out, multiplexer_16_out, register_2_q,
       rom_1_data, shifter_1_out, shifter_2_out, WB_PC;

  Button \u_总复位  (.out(RST));
  Button _1 (.out(IR1));
  Button _2 (.out(IR2));
  Button _3 (.out(IR3));
  Button \u_继续运行  (.out(Go));
  LED led_1 (.in(W1));
  LED led_2 (.in(W2));
  LED led_3 (.in(W3));
  not not_1 (not_1_out, \数据相关 );
  and and_1 (Run, Enable, not_1_out);
  and and_2 (and_2_out, mem_wb_1_dout_1_2, not_2_out);
  not not_2 (not_2_out, mem_wb_1_dout_1);
  Hex_Digit_Display hex_digit_display_1 (.value(LedData[31:28]));  // open: dp
  Register #(.width(32)) PC (.D(multiplexer_1_out), .en(Run), .Q(IF_PC), .clk(CLK), .clr(RST));
  Adder #(.width(32)) adder_1 (.a(IF_PC), .b(32'h4), .out(adder_1_out));  // open: cin, cout
  not not_3 (Enable, register_1_q);
  Register #(.width(1)) register_1 (.D(mem_wb_1_dout_1_2), .en(and_2_out), .Q(register_1_q), .clk(CLK), .clr(or_1_out));
  or or_1 (or_1_out, Go, RST);
  Hex_Digit_Display hex_digit_display_2 (.value(LedData[23:20]));  // open: dp
  Hex_Digit_Display hex_digit_display_3 (.value(LedData[27:24]));  // open: dp
  Multiplexer #(.width(32), .enable("false")) multiplexer_1 (
    .in0(adder_1_out), .in1(multiplexer_10_out), .out(multiplexer_1_out), .sel(Bench));
  Hex_Digit_Display hex_digit_display_4 (.value(LedData[15:12]));  // open: dp
  Hex_Digit_Display hex_digit_display_5 (.value(LedData[19:16]));  // open: dp
  ROM #(.addrWidth(10), .dataWidth(32)) rom_1 (.addr(IF_PC[11:2]), .data(rom_1_data));  // open: sel
  or or_2 (or_2_out, \数据相关 , 1'b0);
  Hex_Digit_Display hex_digit_display_6 (.value(LedData[11:8]));  // open: dp
  Hex_Digit_Display hex_digit_display_7 (.value(LedData[7:4]));  // open: dp
  Clock clock_1 (.out(CLK));
  \数据相关检测  \u_数据相关检测_1  (
    .OP(if_id_1_dout_ins[31:26]), .EX_WriteReg_num(id_ex_1_dout_5_2), .EX_RegWrite(id_ex_1_dout_4_4[1]),
    .MEM_WriteReg_num(ex_mem_1_dout_5), .MEM_RegWrite(ex_mem_1_dout_1_6), .Func(if_id_1_dout_ins[5:0]),
    .ID_R1_num(multiplexer_3_out), .ID_R2_num(multiplexer_6_out), .\数据相关 (\数据相关 ));  // open: ForwardR1, ForwardR2, EX_MemToReg, MEM_MemToReg, Load_Use
  IF_ID if_id_1 (
    .Din_Ins(rom_1_data), .Din_PC_4(adder_1_out), .\传输状态In_表明当前传输数据有效 (1'b1), .CLK(CLK),
    .Dout_Ins(if_id_1_dout_ins), .Dout_PC_4(if_id_1_dout_pc_4),
    .\传输状态Out_表明当前传输数据有效 (\if_id_1_传输状态out_表明当前传输数据有效 ), .\同步清零_气泡_高电平有效 (Bench),
    .\使能端_低电平有效_stall_高电平有效 (or_2_out), .Din_PC(IF_PC), .Dout_PC(ID_PC));  // open: Din_Status, Dout_Status, Din_Addr, Dout_Addr, Din_Miss, Dout_Miss, Din_Hit, Dout_Hit
  Hex_Digit_Display hex_digit_display_8 (.value(LedData[3:0]));  // open: dp
  // Probe on \总周期数 
  // Probe on \无条件分支数 
  // Probe on \条件分支成功数 
  // Probe on \插入气泡数 
  // Probe on \LoadUse次数 
  \硬布线控制器  \u_硬布线控制器_1  (
    .Func(if_id_1_dout_ins[5:0]), .OP(if_id_1_dout_ins[31:26]), .ALU_OP(\硬布线控制器_1_alu_op ),
    .MemToReg(\硬布线控制器_1_beq [2]), .MemWrite(\硬布线控制器_1_beq [3]), .ALU_SRC(\硬布线控制器_1_alu_src [0]),
    .RegWrite(\硬布线控制器_1_alu_src [1]), .SysCALL(\硬布线控制器_1_alu_src [3]), .SignedExt(\硬布线控制器_1_signedext ),
    .RegDst(\硬布线控制器_1_regdst ), .JR(\硬布线控制器_1_bltz [2]), .JMP(\硬布线控制器_1_bltz [3]), .Beq(\硬布线控制器_1_beq [0]),
    .JAL(\硬布线控制器_1_alu_src [2]), .Bne(\硬布线控制器_1_beq [1]), .SH(\硬布线控制器_1_bltz [1]), .BLTZ(\硬布线控制器_1_bltz [0]));  // open: ERET, MF, MFC0, MTC0
  Multiplexer #(.width(5), .enable("false")) multiplexer_2 (
    .in0(if_id_1_dout_ins[20:16]), .in1(if_id_1_dout_ins[15:11]), .out(multiplexer_2_out),
    .sel(\硬布线控制器_1_regdst ));
  assign bit_extender_1_out = {{16{1'b0}}, if_id_1_dout_ins[15:0]};  // Bit_Extender bit_extender_1
  assign bit_extender_2_out = {{16{if_id_1_dout_ins[15]}}, if_id_1_dout_ins[15:0]};  // Bit_Extender bit_extender_2
  assign bit_extender_3_out = {{6{if_id_1_dout_ins[25]}}, if_id_1_dout_ins[25:0]};  // Bit_Extender bit_extender_3
  // Probe on IF_PC[11:0]
  Multiplexer #(.width(5), .enable("false")) multiplexer_3 (
    .in0(if_id_1_dout_ins[25:21]), .in1(5'b00100), .out(multiplexer_3_out), .sel(\硬布线控制器_1_alu_src [3]));
  Multiplexer #(.width(5), .enable("false")) multiplexer_4 (
    .in0(multiplexer_2_out), .in1({5{1'b1}}), .out(multiplexer_4_out), .sel(\硬布线控制器_1_alu_src [2]));
  Multiplexer #(.width(32), .enable("false")) multiplexer_5 (
    .in0(bit_extender_1_out), .in1(bit_extender_2_out), .out(multiplexer_5_out), .sel(\硬布线控制器_1_signedext ));
  // Probe on ID_PC[11:0]
  Multiplexer #(.width(5), .enable("false")) multiplexer_6 (
    .in0(if_id_1_dout_ins[20:16]), .in1(5'b00010), .out(multiplexer_6_out), .sel(\硬布线控制器_1_alu_src [3]));
  // Probe on MEM_PC[11:0]
  // Probe on EX_PC[11:0]
  MIPS_Regifile mips_regifile_1 (
    .Din(multiplexer_16_out), .Clk(CLK), .R1(mips_regifile_1_r1), .R2(mips_regifile_1_r2),
    .WE(mem_wb_1_dout_1_4), .W_num(mem_wb_1_dout_5), .R1_num(multiplexer_3_out), .R2_num(multiplexer_6_out));
  // Probe on WB_PC[11:0]
  or or_3 (or_3_out, Bench, \数据相关 );
  ID_EX id_ex_1 (
    .Din_4(\硬布线控制器_1_bltz ), .Din_4_2(\硬布线控制器_1_beq ), .Din_4_3(\硬布线控制器_1_alu_op ),
    .Din_4_4(\硬布线控制器_1_alu_src ), .Din_32(mips_regifile_1_r1), .Din_32_2(mips_regifile_1_r2),
    .Din_32_3(multiplexer_5_out), .Din_32_4(bit_extender_3_out), .Din_5(if_id_1_dout_ins[10:6]),
    .Din_32_5(if_id_1_dout_pc_4), .\传输状态In_表明当前传输数据有效 (\if_id_1_传输状态out_表明当前传输数据有效 ), .CLK(CLK),
    .Dout_4({JMP, id_ex_1_dout_4}), .Dout_4_2(id_ex_1_dout_4_2), .Dout_4_3(id_ex_1_dout_4_3),
    .Dout_4_4(id_ex_1_dout_4_4), .Dout_32(id_ex_1_dout_32), .Dout_32_2(id_ex_1_dout_32_2),
    .Dout_32_3(id_ex_1_dout_32_3), .Dout_32_4(id_ex_1_dout_32_4), .Dout_5(id_ex_1_dout_5),
    .Dout_32_5(id_ex_1_dout_32_5), .\传输状态Out_表明当前传输数据有效 (\id_ex_1_传输状态out_表明当前传输数据有效 ),
    .\同步清零_气泡_高电平有效 (or_3_out), .\使能端_低电平有效_stall_高电平有效 (1'b0), .Din_5_2(multiplexer_4_out),
    .Dout_5_2(id_ex_1_dout_5_2), .Din_32_6(ID_PC), .Dout_32_6(EX_PC));  // open: Din_2, Dout_2, Din_2_2, Dout_2_2, Din_2_3, Dout_2_3, Din_32_7, Dout_32_7, Din_1, Dout_1, Din_1_2, Dout_1_2
  and and_3 (and_3_out, comparator_1_eq, id_ex_1_dout_4_4[3]);
  not not_4 (not_4_out, comparator_1_eq);
  Counter #(.width(16), .max('hffff)) counter_1 (
    .count(Enable), .Q(\总周期数 ), .clk(CLK), .clr(RST));  // open: load, D, carry
  Register #(.width(32)) register_2 (.D(id_ex_1_dout_32), .en(and_3_out), .Q(register_2_q), .clk(CLK), .clr(RST));
  Comparator #(.width(32)) comparator_1 (.a(32'h22), .b(id_ex_1_dout_32_2), .eq(comparator_1_eq));  // open: gt, lt
  and and_4 (Stop1, not_4_out, id_ex_1_dout_4_4[3]);
  Counter #(.width(16), .max('hffff)) counter_2 (
    .count(JMP), .Q(\无条件分支数 ), .clk(CLK), .clr(RST));  // open: load, D, carry
  Multiplexer #(.width(32), .enable("false")) multiplexer_7 (
    .in0(id_ex_1_dout_32_2), .in1(id_ex_1_dout_32_3), .out(multiplexer_7_out), .sel(id_ex_1_dout_4_4[0]));
  Shifter #(.width(32)) shifter_1 (.in(id_ex_1_dout_32_3), .\dist (5'b00010), .out(shifter_1_out));
  Shifter #(.width(32)) shifter_2 (.in(id_ex_1_dout_32_4), .\dist (5'b00010), .out(shifter_2_out));
  not not_5 (not_5_out, mips_alu_1_equal);
  MIPS_ALU mips_alu_1 (
    .X(id_ex_1_dout_32), .Y(multiplexer_7_out), .AluOP(id_ex_1_dout_4_3), .Equal(mips_alu_1_equal),
    .Result(mips_alu_1_result), .shamt(id_ex_1_dout_5));  // open: Result_2
  Adder #(.width(32)) adder_2 (.a(shifter_1_out), .b(id_ex_1_dout_32_5), .out(adder_2_out));  // open: cin, cout
  and and_5 (and_5_out, id_ex_1_dout_4_2[0], mips_alu_1_equal);
  or or_4 (or_4_out, and_5_out, and_6_out);
  and and_6 (and_6_out, id_ex_1_dout_4_2[1], not_5_out);
  Counter #(.width(16), .max('hffff)) counter_3 (
    .count(Benchif), .Q(\条件分支成功数 ), .clk(CLK), .clr(RST));  // open: load, D, carry
  Comparator #(.width(32)) comparator_2 (.a(id_ex_1_dout_32), .b({32{1'b0}}), .lt(comparator_2_lt));  // open: gt, eq
  not not_6 (not_6_out, id_ex_1_dout_4[2]);
  and and_7 (and_7_out, id_ex_1_dout_4[0], comparator_2_lt);
  nor nor_1 (nor_1_out, and_7_out, or_4_out);
  Multiplexer #(.width(32), .enable("false")) multiplexer_8 (
    .in0(adder_2_out), .in1(id_ex_1_dout_32_5), .out(multiplexer_8_out), .sel(nor_1_out));
  nor nor_2 (nor_2_out, Stop2, Stop1);
  not not_7 (not_7_out, JMP);
  or or_5 (Benchif, and_7_out, or_4_out);
  or or_6 (Bench, and_7_out, or_4_out, JMP);
  Multiplexer #(.width(32), .enable("false")) multiplexer_9 (
    .in0(id_ex_1_dout_32), .in1(shifter_2_out), .out(multiplexer_9_out), .sel(not_6_out));
  Multiplexer #(.width(32), .enable("false")) multiplexer_10 (
    .in0(multiplexer_9_out), .in1(multiplexer_8_out), .out(multiplexer_10_out), .sel(not_7_out));
  Counter #(.width(16), .max('hffff)) counter_4 (
    .count(and_8_out), .Q(\插入气泡数 ), .clk(CLK), .clr(RST));  // open: load, D, carry
  and and_8 (and_8_out, nor_2_out, Enable, \数据相关 );
  EX_MEM ex_mem_1 (
    .Din_1_4(id_ex_1_dout_4_2[2]), .Din_1_5(id_ex_1_dout_4_2[3]), .Din_32_2(mips_alu_1_result),
    .Din_32_3(id_ex_1_dout_32_2), .Din_32_4(id_ex_1_dout_32_5),
    .\传输状态In_表明当前传输数据有效 (\id_ex_1_传输状态out_表明当前传输数据有效 ), .CLK(CLK), .Dout_1_4(ex_mem_1_dout_1_4),
    .Dout_1_5(ex_mem_1_dout_1_5), .Dout_32_2(ex_mem_1_dout_32_2), .Dout_32_3(ex_mem_1_dout_32_3),
    .Dout_32_4(ex_mem_1_dout_32_4), .\传输状态Out_表明当前传输数据有效 (\ex_mem_1_传输状态out_表明当前传输数据有效 ),
    .\同步清零_气泡_高电平有效 (1'b0), .\使能端_低电平有效_stall_高电平有效 (1'b0), .Din_1_6(id_ex_1_dout_4_4[1]),
    .Dout_1_6(ex_mem_1_dout_1_6), .Din_1_7(id_ex_1_dout_4_4[2]), .Dout_1_7(ex_mem_1_dout_1_7),
    .Din_32(register_2_q), .Dout_32(ex_mem_1_dout_32), .Dout_1_3(ex_mem_1_dout_1_3),
    .Din_1_3(id_ex_1_dout_4_4[3]), .Din_1_2(comparator_1_eq), .Dout_1_2(ex_mem_1_dout_1_2),
    .Din_1(id_ex_1_dout_4[1]), .Dout_1(ex_mem_1_dout_1), .Din_5(id_ex_1_dout_5_2), .Dout_5(ex_mem_1_dout_5),
    .Din_32_5(EX_PC), .Dout_32_5(MEM_PC));  // open: Din_1_8, Dout_1_8, Din_1_9, Dout_1_9, Dout_32_6, Dout_32_7, Din_32_6, Din_32_7, Din_1_10, Dout_1_10
  not not_8 (not_8_out, ex_mem_1_dout_1_2);
  and and_9 (Stop2, not_8_out, ex_mem_1_dout_1_3);
  Multiplexer #(.width(32), .enable("false")) multiplexer_11 (
    .in0({{16{1'b0}}, ex_mem_1_dout_32_3[15:0]}), .in1({ex_mem_1_dout_32_3[15:0], {16{1'b0}}}),
    .out(multiplexer_11_out), .sel(ex_mem_1_dout_32_2[1]));
  Multiplexer #(.width(32), .enable("false")) multiplexer_12 (
    .in0(ex_mem_1_dout_32_3), .in1(multiplexer_11_out), .out(multiplexer_12_out), .sel(ex_mem_1_dout_1));
  Multiplexer #(.width(4), .enable("false")) multiplexer_13 (
    .in0(4'b1111), .in1(multiplexer_14_out), .out(multiplexer_13_out), .sel(ex_mem_1_dout_1));
  Multiplexer #(.width(4), .enable("false")) multiplexer_14 (
    .in0(4'b0011), .in1(4'b1100), .out(multiplexer_14_out), .sel(ex_mem_1_dout_32_2[1]));
  // MIPS_RAM mips_ram_1: pin names not known; wires that end beside it: ex_mem_1_dout_32_2[11:2], multiplexer_12_out, ex_mem_1_dout_1_5, multiplexer_13_out, CLK, 1'b1, RST, mips_ram_1_p8
  MEM_WB mem_wb_1 (
    .Din_1_4(ex_mem_1_dout_1_6), .Din_1_5(ex_mem_1_dout_1_7), .Din_32(ex_mem_1_dout_32),
    .Din_32_3(mips_ram_1_p8), .Din_32_4(ex_mem_1_dout_32_4),
    .\传输状态In_表明当前传输数据有效 (\ex_mem_1_传输状态out_表明当前传输数据有效 ), .CLK(CLK), .Dout_1_4(mem_wb_1_dout_1_4),
    .Dout_1_5(mem_wb_1_dout_1_5), .Dout_32(LedData), .Dout_32_3(mem_wb_1_dout_32_3),
    .Dout_32_4(mem_wb_1_dout_32_4), .\同步清零_气泡_高电平有效 (1'b0), .\使能端_低电平有效_stall_高电平有效 (1'b0),
    .Dout_1(mem_wb_1_dout_1), .Dout_1_2(mem_wb_1_dout_1_2), .Din_1(ex_mem_1_dout_1_2),
    .Din_1_2(ex_mem_1_dout_1_3), .Din_5(ex_mem_1_dout_5), .Dout_5(mem_wb_1_dout_5), .Din_32_5(MEM_PC),
    .Dout_32_5(WB_PC), .Din_1_3(ex_mem_1_dout_1_4), .Dout_1_3(mem_wb_1_dout_1_3),
    .Din_32_2(ex_mem_1_dout_32_2), .Dout_32_2(mem_wb_1_dout_32_2));  // open: 传输状态Out_表明当前传输数据有效, Din_1_6, Dout_1_6, Din_1_7, Dout_1_7, Din_32_6, Dout_32_6, Din_32_7, Dout_32_7, Din_1_8, Dout_1_8
  Multiplexer #(.width(32), .enable("false")) multiplexer_15 (
    .in0(mem_wb_1_dout_32_2), .in1(mem_wb_1_dout_32_3), .out(multiplexer_15_out), .sel(mem_wb_1_dout_1_3));
  Multiplexer #(.width(32), .enable("false")) multiplexer_16 (
    .in0(multiplexer_15_out), .in1(mem_wb_1_dout_32_4), .out(multiplexer_16_out), .sel(mem_wb_1_dout_1_5));

  // Notes on the sheet:
  //   中断源
  //   中断等待指示
  //   指令存储器
  //   数码管输出
  //   IF/ID
  //   指令字
  //   contents of rom_1 (hex, n*v repeats v):
  //   2011fff1 112020 20020022 c 22310001 620fffb 2002000a c
  //   OP
  //   Func
  //   rs
  //   rt
  //   rd
  //   JMP
  //   JR
  //   SH
  //   Bltz
  //   Beq
  //   Bne
  //   MemToReg
  //   MemWrite
  //   AluOP
  //   AluSrcB
  //   RegWrite
  //   JAL
  //   RegDst
  //   Syscall
  //   流水调试日志用
  //   ID/EX
  //   统计
  //   EX/MEM
  //   MEM/WB
endmodule

module \重定向流水线  (
);

  wire and_2_out, and_3_out, and_5_out, and_6_out, and_7_out, and_8_out, Bench, Benchif, CLK,
       comparator_1_eq, comparator_2_lt, Enable, ex_mem_1_dout_1, ex_mem_1_dout_1_2, ex_mem_1_dout_1_3,
       ex_mem_1_dout_1_4, ex_mem_1_dout_1_5, ex_mem_1_dout_1_6, ex_mem_1_dout_1_7,
       \ex_mem_1_传输状态out_表明当前传输数据有效 , Go, \id_ex_1_传输状态out_表明当前传输数据有效 , \if_id_1_传输状态out_表明当前传输数据有效 , IR1,
       IR2, IR3, JMP, Load_use, mem_wb_1_dout_1, mem_wb_1_dout_1_2, mem_wb_1_dout_1_3, mem_wb_1_dout_1_4,
       mem_wb_1_dout_1_5, mips_alu_1_equal, nor_1_out, nor_2_out, not_1_out, not_2_out, not_4_out, not_5_out,
       not_6_out, not_7_out, not_8_out, or_1_out, or_2_out, or_3_out, or_4_out, or_5_out, or_8_out, or_9_out,
       register_1_q, RST, Run, Stop1, Stop2, W1, W2, W3, \硬布线控制器_1_regdst , \硬布线控制器_1_signedext ;
  wire [1:0] id_ex_1_dout_2, id_ex_1_dout_2_2, \数据相关检测_1_forwardr1 , \数据相关检测_1_forwardr2 ;
  wire [2:0] id_ex_1_dout_4;
  wire [3:0] id_ex_1_dout_4_2, id_ex_1_dout_4_3, id_ex_1_dout_4_4, multiplexer_15_out, multiplexer_16_out,
       \硬布线控制器_1_alu_op , \硬布线控制器_1_alu_src , \硬布线控制器_1_beq , \硬布线控制器_1_bltz ;
  wire [4:0] ex_mem_1_dout_5, id_ex_1_dout_5, id_ex_1_dout_5_2, mem_wb_1_dout_5, multiplexer_2_out,
       multiplexer_3_out, multiplexer_4_out, multiplexer_6_out;
  wire [15:0] \LoadUse次数 , \总周期数 , \无条件分支数 , \条件分支成功数 ;
  wire [31:0] adder_1_out, adder_2_out, bit_extender_1_out, bit_extender_2_out, bit_extender_3_out,
       ex_mem_1_dout_32, ex_mem_1_dout_32_2, ex_mem_1_dout_32_3, ex_mem_1_dout_32_4, EX_PC, id_ex_1_dout_32,
       id_ex_1_dout_32_2, id_ex_1_dout_32_3, id_ex_1_dout_32_4, id_ex_1_dout_32_5, ID_PC, if_id_1_dout_ins,
       if_id_1_dout_pc_4, IF_PC, LedData, MEM_PC, mem_wb_1_dout_32_2, mem_wb_1_dout_32_3, mem_wb_1_dout_32_4,
       mips_alu_1_result, mips_ram_1_p8, mips_regifile_1_r1, mips_regifile_1_r2, multiplexer_1_out,
       multiplexer_5_out, multiplexer_7_out, multiplexer_8_out, multiplexer_9_out, multiplexer_10_out,
       multiplexer_11_out, multiplexer_12_out, multiplexer_13_out, multiplexer_14_out, multiplexer_17_out,
       multiplexer_18_out, register_2_q, rom_1_data, shifter_1_out, shifter_2_out, WB_PC;

  Button \u_总复位  (.out(RST));
  Button _1 (.out(IR1));
  Button _2 (.out(IR2));
  Button _3 (.out(IR3));
  Button \u_继续运行  (.out(Go));
  LED led_1 (.in(W1));
  LED led_2 (.in(W2));
  LED led_3 (.in(W3));
  not not_1 (not_1_out, Load_use);
  and and_1 (Run, Enable, not_1_out);
  and and_2 (and_2_out, mem_wb_1_dout_1_2, not_2_out);
  not not_2 (not_2_out, mem_wb_1_dout_1);
  Hex_Digit_Display hex_digit_display_1 (.value(LedData[31:28]));  // open: dp
  Register #(.width(32)) PC (.D(multiplexer_1_out), .en(Run), .Q(IF_PC), .clk(CLK), .clr(RST));
  Adder #(.width(32)) adder_1 (.a(IF_PC), .b(32'h4), .out(adder_1_out));  // open: cin, cout
  not not_3 (Enable, register_1_q);
  Register #(.width(1)) register_1 (.D(mem_wb_1_dout_1_2), .en(and_2_out), .Q(register_1_q), .clk(CLK), .clr(or_1_out));
  or or_1 (or_1_out, Go, RST);
  Hex_Digit_Display hex_digit_display_2 (.value(LedData[27:24]));  // open: dp
  Hex_Digit_Display hex_digit_display_3 (.value(LedData[23:20]));  // open: dp
  Multiplexer #(.width(32), .enable("false")) multiplexer_1 (
    .in0(adder_1_out), .in1(multiplexer_12_out), .out(multiplexer_1_out), .sel(Bench));
  Hex_Digit_Display hex_digit_display_4 (.value(LedData[15:12]));  // open: dp
  Hex_Digit_Display hex_digit_display_5 (.value(LedData[19:16]));  // open: dp
  ROM #(.addrWidth(10), .dataWidth(32)) rom_1 (.addr(IF_PC[11:2]), .data(rom_1_data));  // open: sel
  or or_2 (or_2_out, Load_use, register_1_q, 1'b0);
  Hex_Digit_Display hex_digit_display_6 (.value(LedData[11:8]));  // open: dp
  Hex_Digit_Display hex_digit_display_7 (.value(LedData[7:4]));  // open: dp
  Clock clock_1 (.out(CLK));
  \数据相关检测  \u_数据相关检测_1  (
    .OP(if_id_1_dout_ins[31:26]), .EX_WriteReg_num(id_ex_1_dout_5_2), .EX_RegWrite(id_ex_1_dout_4_4[1]),
    .ForwardR1(\数据相关检测_1_forwardr1 ), .MEM_WriteReg_num(ex_mem_1_dout_5), .MEM_RegWrite(ex_mem_1_dout_1_6),
    .ForwardR2(\数据相关检测_1_forwardr2 ), .Func(if_id_1_dout_ins[5:0]), .ID_R1_num(multiplexer_3_out),
    .ID_R2_num(multiplexer_6_out), .EX_MemToReg(id_ex_1_dout_4_2[2]), .MEM_MemToReg(ex_mem_1_dout_1_4),
    .Load_Use(Load_use));  // open: 数据相关
  IF_ID if_id_1 (
    .Din_Ins(rom_1_data), .Din_PC_4(adder_1_out), .\传输状态In_表明当前传输数据有效 (1'b1), .CLK(CLK),
    .Dout_Ins(if_id_1_dout_ins), .Dout_PC_4(if_id_1_dout_pc_4),
    .\传输状态Out_表明当前传输数据有效 (\if_id_1_传输状态out_表明当前传输数据有效 ), .\同步清零_气泡_高电平有效 (Bench),
    .\使能端_低电平有效_stall_高电平有效 (or_2_out), .Din_PC(IF_PC), .Dout_PC(ID_PC));  // open: Din_Status, Dout_Status, Din_Addr, Dout_Addr, Din_Miss, Dout_Miss, Din_Hit, Dout_Hit
  Hex_Digit_Display hex_digit_display_8 (.value(LedData[3:0]));  // open: dp
  // Probe on \总周期数 
  // Probe on \无条件分支数 
  // Probe on \条件分支成功数 
  // Probe on \LoadUse次数 
  // Probe on \LoadUse次数 
  \硬布线控制器  \u_硬布线控制器_1  (
    .Func(if_id_1_dout_ins[5:0]), .OP(if_id_1_dout_ins[31:26]), .ALU_OP(\硬布线控制器_1_alu_op ),
    .MemToReg(\硬布线控制器_1_beq [2]), .MemWrite(\硬布线控制器_1_beq [3]), .ALU_SRC(\硬布线控制器_1_alu_src [0]),
    .RegWrite(\硬布线控制器_1_alu_src [1]), .SysCALL(\硬布线控制器_1_alu_src [3]), .SignedExt(\硬布线控制器_1_signedext ),
    .RegDst(\硬布线控制器_1_regdst ), .JR(\硬布线控制器_1_bltz [2]), .JMP(\硬布线控制器_1_bltz [3]), .Beq(\硬布线控制器_1_beq [0]),
    .JAL(\硬布线控制器_1_alu_src [2]), .Bne(\硬布线控制器_1_beq [1]), .SH(\硬布线控制器_1_bltz [1]), .BLTZ(\硬布线控制器_1_bltz [0]));  // open: ERET, MF, MFC0, MTC0
  Multiplexer #(.width(5), .enable("false")) multiplexer_2 (
    .in0(if_id_1_dout_ins[20:16]), .in1(if_id_1_dout_ins[15:11]), .out(multiplexer_2_out),
    .sel(\硬布线控制器_1_regdst ));
  assign bit_extender_1_out = {{16{1'b0}}, if_id_1_dout_ins[15:0]};  // Bit_Extender bit_extender_1
  assign bit_extender_2_out = {{16{if_id_1_dout_ins[15]}}, if_id_1_dout_ins[15:0]};  // Bit_Extender bit_extender_2
  assign bit_extender_3_out = {{6{if_id_1_dout_ins[25]}}, if_id_1_dout_ins[25:0]};  // Bit_Extender bit_extender_3
  // Probe on IF_PC[11:0]
  Multiplexer #(.width(5), .enable("false")) multiplexer_3 (
    .in0(if_id_1_dout_ins[25:21]), .in1(5'b00100), .out(multiplexer_3_out), .sel(\硬布线控制器_1_alu_src [3]));
  Multiplexer #(.width(5), .enable("false")) multiplexer_4 (
    .in0(multiplexer_2_out), .in1({5{1'b1}}), .out(multiplexer_4_out), .sel(\硬布线控制器_1_alu_src [2]));
  Multiplexer #(.width(32), .enable("false")) multiplexer_5 (
    .in0(bit_extender_1_out), .in1(bit_extender_2_out), .out(multiplexer_5_out), .sel(\硬布线控制器_1_signedext ));
  // Probe on ID_PC[11:0]
  Multiplexer #(.width(5), .enable("false")) multiplexer_6 (
    .in0(if_id_1_dout_ins[20:16]), .in1(5'b00010), .out(multiplexer_6_out), .sel(\硬布线控制器_1_alu_src [3]));
  // Probe on EX_PC[11:0]
  // Probe on MEM_PC[11:0]
  MIPS_Regifile mips_regifile_1 (
    .Din(multiplexer_18_out), .Clk(CLK), .R1(mips_regifile_1_r1), .R2(mips_regifile_1_r2),
    .WE(mem_wb_1_dout_1_4), .W_num(mem_wb_1_dout_5), .R1_num(multiplexer_3_out), .R2_num(multiplexer_6_out));
  // Probe on WB_PC[11:0]
  or or_3 (or_3_out, Bench, Load_use);
  ID_EX id_ex_1 (
    .Din_4(\硬布线控制器_1_bltz ), .Din_4_2(\硬布线控制器_1_beq ), .Din_4_3(\硬布线控制器_1_alu_op ),
    .Din_4_4(\硬布线控制器_1_alu_src ), .Din_32(mips_regifile_1_r1), .Din_32_2(mips_regifile_1_r2),
    .Din_32_3(multiplexer_5_out), .Din_32_4(bit_extender_3_out), .Din_5(if_id_1_dout_ins[10:6]),
    .Din_32_5(if_id_1_dout_pc_4), .\传输状态In_表明当前传输数据有效 (\if_id_1_传输状态out_表明当前传输数据有效 ), .CLK(CLK),
    .Dout_4({JMP, id_ex_1_dout_4}), .Dout_4_2(id_ex_1_dout_4_2), .Dout_4_3(id_ex_1_dout_4_3),
    .Dout_4_4(id_ex_1_dout_4_4), .Dout_32(id_ex_1_dout_32), .Dout_32_2(id_ex_1_dout_32_2),
    .Dout_32_3(id_ex_1_dout_32_3), .Dout_32_4(id_ex_1_dout_32_4), .Dout_5(id_ex_1_dout_5),
    .Dout_32_5(id_ex_1_dout_32_5), .\传输状态Out_表明当前传输数据有效 (\id_ex_1_传输状态out_表明当前传输数据有效 ),
    .\同步清零_气泡_高电平有效 (or_3_out), .\使能端_低电平有效_stall_高电平有效 (or_4_out), .Din_5_2(multiplexer_4_out),
    .Dout_5_2(id_ex_1_dout_5_2), .Din_32_6(ID_PC), .Dout_32_6(EX_PC), .Din_2(\数据相关检测_1_forwardr1 ),
    .Dout_2(id_ex_1_dout_2), .Din_2_2(\数据相关检测_1_forwardr2 ), .Dout_2_2(id_ex_1_dout_2_2));  // open: Din_2_3, Dout_2_3, Din_32_7, Dout_32_7, Din_1, Dout_1, Din_1_2, Dout_1_2
  or or_4 (or_4_out, register_1_q, 1'b0);
  Counter #(.width(16), .max('hffff)) counter_1 (
    .count(Enable), .Q(\总周期数 ), .clk(CLK), .clr(RST));  // open: load, D, carry
  Multiplexer #(.select(2), .width(32), .enable("false")) multiplexer_7 (
    .in0(id_ex_1_dout_32), .in1(mem_wb_1_dout_32_2), .in2(mem_wb_1_dout_32_3), .in3(ex_mem_1_dout_32_2),
    .out(multiplexer_7_out), .sel(id_ex_1_dout_2));
  Multiplexer #(.select(2), .width(32), .enable("false")) multiplexer_8 (
    .in0(id_ex_1_dout_32_2), .in1(mem_wb_1_dout_32_2), .in2(mem_wb_1_dout_32_3), .in3(ex_mem_1_dout_32_2),
    .out(multiplexer_8_out), .sel(id_ex_1_dout_2_2));
  Counter #(.width(16), .max('hffff)) counter_2 (
    .count(JMP), .Q(\无条件分支数 ), .clk(CLK), .clr(RST));  // open: load, D, carry
  and and_3 (and_3_out, comparator_1_eq, id_ex_1_dout_4_4[3]);
  not not_4 (not_4_out, comparator_1_eq);
  and and_4 (Stop1, not_4_out, id_ex_1_dout_4_4[3]);
  Register #(.width(32)) register_2 (.D(multiplexer_7_out), .en(and_3_out), .Q(register_2_q), .clk(CLK), .clr(RST));
  Comparator #(.width(32)) comparator_1 (.a(32'h22), .b(multiplexer_8_out), .eq(comparator_1_eq));  // open: gt, lt
  Multiplexer #(.width(32), .enable("false")) multiplexer_9 (
    .in0(multiplexer_8_out), .in1(id_ex_1_dout_32_3), .out(multiplexer_9_out), .sel(id_ex_1_dout_4_4[0]));
  Shifter #(.width(32)) shifter_1 (.in(id_ex_1_dout_32_3), .\dist (5'b00010), .out(shifter_1_out));
  Shifter #(.width(32)) shifter_2 (.in(id_ex_1_dout_32_4), .\dist (5'b00010), .out(shifter_2_out));
  Counter #(.width(16), .max('hffff)) counter_3 (
    .count(Benchif), .Q(\条件分支成功数 ), .clk(CLK), .clr(RST));  // open: load, D, carry
  MIPS_ALU mips_alu_1 (
    .X(multiplexer_7_out), .Y(multiplexer_9_out), .AluOP(id_ex_1_dout_4_3), .Equal(mips_alu_1_equal),
    .Result(mips_alu_1_result), .shamt(id_ex_1_dout_5));  // open: Result_2
  not not_5 (not_5_out, mips_alu_1_equal);
  Adder #(.width(32)) adder_2 (.a(shifter_1_out), .b(id_ex_1_dout_32_5), .out(adder_2_out));  // open: cin, cout
  and and_5 (and_5_out, id_ex_1_dout_4_2[0], mips_alu_1_equal);
  or or_5 (or_5_out, and_5_out, and_6_out);
  and and_6 (and_6_out, id_ex_1_dout_4_2[1], not_5_out);
  nor nor_1 (nor_1_out, Stop2, Stop1);
  Comparator #(.width(32)) comparator_2 (.a(multiplexer_7_out), .b({32{1'b0}}), .lt(comparator_2_lt));  // open: gt, eq
  Counter #(.width(16), .max('hffff)) counter_4 (
    .count(and_7_out), .Q(\LoadUse次数 ), .clk(CLK), .clr(RST));  // open: load, D, carry
  and and_7 (and_7_out, nor_1_out, Enable, Load_use);
  and and_8 (and_8_out, id_ex_1_dout_4[0], comparator_2_lt);
  not not_6 (not_6_out, id_ex_1_dout_4[2]);
  or or_6 (Benchif, and_8_out, or_5_out);
  nor nor_2 (nor_2_out, and_8_out, or_5_out);
  Multiplexer #(.width(32), .enable("false")) multiplexer_10 (
    .in0(multiplexer_7_out), .in1(shifter_2_out), .out(multiplexer_10_out), .sel(not_6_out));
  Multiplexer #(.width(32), .enable("false")) multiplexer_11 (
    .in0(adder_2_out), .in1(id_ex_1_dout_32_5), .out(multiplexer_11_out), .sel(nor_2_out));
  not not_7 (not_7_out, JMP);
  or or_7 (Bench, and_8_out, or_5_out, JMP);
  Multiplexer #(.width(32), .enable("false")) multiplexer_12 (
    .in0(multiplexer_10_out), .in1(multiplexer_11_out), .out(multiplexer_12_out), .sel(not_7_out));
  or or_8 (or_8_out, register_1_q, 1'b0);
  EX_MEM ex_mem_1 (
    .Din_1_4(id_ex_1_dout_4_2[2]), .Din_1_5(id_ex_1_dout_4_2[3]), .Din_32_2(mips_alu_1_result),
    .Din_32_3(multiplexer_8_out), .Din_32_4(id_ex_1_dout_32_5),
    .\传输状态In_表明当前传输数据有效 (\id_ex_1_传输状态out_表明当前传输数据有效 ), .CLK(CLK), .Dout_1_4(ex_mem_1_dout_1_4),
    .Dout_1_5(ex_mem_1_dout_1_5), .Dout_32_2(ex_mem_1_dout_32_2), .Dout_32_3(ex_mem_1_dout_32_3),
    .Dout_32_4(ex_mem_1_dout_32_4), .\传输状态Out_表明当前传输数据有效 (\ex_mem_1_传输状态out_表明当前传输数据有效 ),
    .\同步清零_气泡_高电平有效 (1'b0), .\使能端_低电平有效_stall_高电平有效 (or_8_out), .Din_1_6(id_ex_1_dout_4_4[1]),
    .Dout_1_6(ex_mem_1_dout_1_6), .Din_1_7(id_ex_1_dout_4_4[2]), .Dout_1_7(ex_mem_1_dout_1_7),
    .Din_32(register_2_q), .Dout_32(ex_mem_1_dout_32), .Dout_1_3(ex_mem_1_dout_1_3),
    .Din_1_3(id_ex_1_dout_4_4[3]), .Din_1_2(comparator_1_eq), .Dout_1_2(ex_mem_1_dout_1_2),
    .Din_1(id_ex_1_dout_4[1]), .Dout_1(ex_mem_1_dout_1), .Din_5(id_ex_1_dout_5_2), .Dout_5(ex_mem_1_dout_5),
    .Din_32_5(EX_PC), .Dout_32_5(MEM_PC));  // open: Din_1_8, Dout_1_8, Din_1_9, Dout_1_9, Dout_32_6, Dout_32_7, Din_32_6, Din_32_7, Din_1_10, Dout_1_10
  not not_8 (not_8_out, ex_mem_1_dout_1_2);
  and and_9 (Stop2, not_8_out, ex_mem_1_dout_1_3);
  Multiplexer #(.width(32), .enable("false")) multiplexer_13 (
    .in0({{16{1'b0}}, ex_mem_1_dout_32_3[15:0]}), .in1({ex_mem_1_dout_32_3[15:0], {16{1'b0}}}),
    .out(multiplexer_13_out), .sel(ex_mem_1_dout_32_2[1]));
  Multiplexer #(.width(32), .enable("false")) multiplexer_14 (
    .in0(ex_mem_1_dout_32_3), .in1(multiplexer_13_out), .out(multiplexer_14_out), .sel(ex_mem_1_dout_1));
  Multiplexer #(.width(4), .enable("false")) multiplexer_15 (
    .in0(4'b1111), .in1(multiplexer_16_out), .out(multiplexer_15_out), .sel(ex_mem_1_dout_1));
  Multiplexer #(.width(4), .enable("false")) multiplexer_16 (
    .in0(4'b0011), .in1(4'b1100), .out(multiplexer_16_out), .sel(ex_mem_1_dout_32_2[1]));
  // MIPS_RAM mips_ram_1: pin names not known; wires that end beside it: ex_mem_1_dout_32_2[11:2], multiplexer_14_out, ex_mem_1_dout_1_5, multiplexer_15_out, CLK, 1'b1, RST, mips_ram_1_p8
  MEM_WB mem_wb_1 (
    .Din_1_4(ex_mem_1_dout_1_6), .Din_1_5(ex_mem_1_dout_1_7), .Din_32(ex_mem_1_dout_32),
    .Din_32_3(mips_ram_1_p8), .Din_32_4(ex_mem_1_dout_32_4),
    .\传输状态In_表明当前传输数据有效 (\ex_mem_1_传输状态out_表明当前传输数据有效 ), .CLK(CLK), .Dout_1_4(mem_wb_1_dout_1_4),
    .Dout_1_5(mem_wb_1_dout_1_5), .Dout_32(LedData), .Dout_32_3(mem_wb_1_dout_32_3),
    .Dout_32_4(mem_wb_1_dout_32_4), .\同步清零_气泡_高电平有效 (1'b0), .\使能端_低电平有效_stall_高电平有效 (or_9_out),
    .Dout_1(mem_wb_1_dout_1), .Dout_1_2(mem_wb_1_dout_1_2), .Din_1(ex_mem_1_dout_1_2),
    .Din_1_2(ex_mem_1_dout_1_3), .Din_5(ex_mem_1_dout_5), .Dout_5(mem_wb_1_dout_5), .Din_32_5(MEM_PC),
    .Dout_32_5(WB_PC), .Din_1_3(ex_mem_1_dout_1_4), .Dout_1_3(mem_wb_1_dout_1_3),
    .Din_32_2(ex_mem_1_dout_32_2), .Dout_32_2(mem_wb_1_dout_32_2));  // open: 传输状态Out_表明当前传输数据有效, Din_1_6, Dout_1_6, Din_1_7, Dout_1_7, Din_32_6, Dout_32_6, Din_32_7, Dout_32_7, Din_1_8, Dout_1_8
  or or_9 (or_9_out, register_1_q, 1'b0);
  Multiplexer #(.width(32), .enable("false")) multiplexer_17 (
    .in0(mem_wb_1_dout_32_2), .in1(mem_wb_1_dout_32_3), .out(multiplexer_17_out), .sel(mem_wb_1_dout_1_3));
  Multiplexer #(.width(32), .enable("false")) multiplexer_18 (
    .in0(multiplexer_17_out), .in1(mem_wb_1_dout_32_4), .out(multiplexer_18_out), .sel(mem_wb_1_dout_1_5));

  // Other names for the same wires on the sheet: 插入气泡数[15:0] = \LoadUse次数 

  // Notes on the sheet:
  //   中断源
  //   中断等待指示
  //   指令存储器
  //   数码管输出
  //   IF/ID
  //   指令字
  //   contents of rom_1 (hex, n*v repeats v):
  //   20110001 8000c05 20110001 20120002 20130003 8000c09 20110001 20120002 20130003 8000c0d 20110001
  //   20120002 20130003 8000c11 20110001 20120002 20130003 c000cf5 20100001 20110001 118fc0 112020
  //   20020022 c 118882 12200001 8000c15 112020 20020022 c 20110001 118880 112020 20020022 c 12200001
  //   8000c1f 20110001 118fc0 112020 20020022 c 1188c3 112020 20020022 c 118903 112020 20020022 c 118903
  //   112020 20020022 c 118903 112020 20020022 c 118903 112020 20020022 c 118903 112020 20020022 c 118903
  //   112020 20020022 c 118903 112020 20020022 c 20100001 109fc0 139fc3 8021 2012000c 24160003 26100001
  //   3210000f 20080008 20090001 139900 2709825 132020 20020022 c 1094022 1500fff9 22100001 2018000f
  //   2188024 108700 20080008 20090001 139902 2709825 132021 20020022 c 1094022 1500fff9 108702 2c9b022
  //   12c00001 8000c50 4020 1084027 84400 3508ffff 82021 20020022 c 2010ffff 20110000 ae300000 22100001
  //   22310004 ae300000 22100001 22310004 ae300000 22100001 22310004 ae300000 22100001 22310004 ae300000
  //   22100001 22310004 ae300000 22100001 22310004 ae300000 22100001 22310004 ae300000 22100001 22310004
  //   ae300000 22100001 22310004 ae300000 22100001 22310004 ae300000 22100001 22310004 ae300000 22100001
  //   22310004 ae300000 22100001 22310004 ae300000 22100001 22310004 ae300000 22100001 22310004 ae300000
  //   22100001 22310004 22100001 8020 2011003c 8e130000 8e340000 274402a 11000002 ae330000 ae140000
  //   2231fffc 1611fff8 102020 20020022 c 22100004 2011003c 1611fff2 20020032 c 20080001 20110010 112020
  //   20020022 c 200b0020 2288823 112020 20020022 c 216bffff 1560fffa 2002000a c 2008ffff 20117777 112020
  //   20020022 c 200b0010 2288826 112020 20020022 c 216bffff 1560fffa 2002000a c 20090000 200b0020
  //   20110001 20120001 a5310000 112020 20020022 c 2328820 21290002 216bffff 1560fff8 200b0010 20090000
  //   8d310000 112020 20020022 c 21290004 216bffff 1560fff9 2002000a c 2011fff1 112020 20020022 c 22310001
  //   620fffb 2002000a c 2002000a c 20100000 22100001 102020 20020022 c 22100002 102020 20020022 c
  //   22100003 102020 20020022 c 22100004 102020 20020022 c 22100005 102020 20020022 c 22100006 102020
  //   20020022 c 22100007 102020 20020022 c 22100008 102020 20020022 20020022 c 3e00008
  //   OP
  //   Func
  //   rs
  //   rt
  //   rd
  //   JMP
  //   JR
  //   SH
  //   Bltz
  //   Beq
  //   Bne
  //   MemToReg
  //   MemWrite
  //   AluOP
  //   AluSrcB
  //   RegWrite
  //   JAL
  //   RegDst
  //   Syscall
  //   流水调试日志用
  //   ID/EX
  //   统计
  //   EX/MEM
  //   MEM/WB
endmodule

// 扩展信号生成
module \扩展信号控制器  (
  input  OP0,
  input  OP1,
  input  OP2,
  input  OP3,
  input  OP4,
  input  OP5,
  input  F0,
  input  F1,
  input  F2,
  input  F3,
  input  F4,
  input  F5,
  output SH,
  output BLTZ,
  output ERET
);

  wire not_1_out, not_2_out, not_3_out, not_4_out, not_5_out, not_6_out, not_7_out, not_8_out, not_9_out,
       not_10_out, not_11_out, not_12_out, not_13_out, not_14_out, not_15_out, not_16_out, not_17_out;

  not not_1 (not_1_out, OP4);
  not not_2 (not_2_out, OP2);
  not not_3 (not_3_out, OP1);
  not not_4 (not_4_out, OP5);
  not not_5 (not_5_out, OP4);
  not not_6 (not_6_out, OP3);
  not not_7 (not_7_out, OP2);
  not not_8 (not_8_out, OP1);
  not not_9 (not_9_out, OP5);
  not not_10 (not_10_out, OP3);
  not not_11 (not_11_out, OP2);
  not not_12 (not_12_out, OP1);
  not not_13 (not_13_out, OP0);
  not not_14 (not_14_out, F5);
  not not_15 (not_15_out, F2);
  not not_16 (not_16_out, F1);
  not not_17 (not_17_out, F0);
  and and_1 (SH, OP5, not_1_out, OP3, not_2_out, not_3_out, OP0);
  and and_2 (BLTZ, not_4_out, not_5_out, not_6_out, not_7_out, not_8_out, OP0);
  and and_3 (ERET, not_9_out, OP4, not_10_out, not_11_out, not_12_out, not_13_out, not_14_out, F4, F3, not_15_out, not_16_out, not_17_out);
endmodule

module \动态分支预测  (
);

  wire and_1_out, and_3_out, and_6_out, and_7_out, and_8_out, and_9_out, and_11_out, Bench, Benchif, CLK,
       comparator_1_eq, comparator_2_lt, Enable, ex_mem_1_dout_1, ex_mem_1_dout_1_2, ex_mem_1_dout_1_3,
       ex_mem_1_dout_1_4, ex_mem_1_dout_1_5, ex_mem_1_dout_1_6, ex_mem_1_dout_1_7,
       \ex_mem_1_传输状态out_表明当前传输数据有效 , Go, id_ex_1_dout_1, \id_ex_1_传输状态out_表明当前传输数据有效 , if_id_1_dout_hit,
       if_id_1_dout_miss, \if_id_1_传输状态out_表明当前传输数据有效 , IR1, IR2, IR3, J, JMP, Load_use, mem_wb_1_dout_1,
       mem_wb_1_dout_1_2, mem_wb_1_dout_1_3, mem_wb_1_dout_1_4, mem_wb_1_dout_1_5, mips_alu_1_equal, Miss,
       nor_1_out, nor_2_out, not_1_out, not_2_out, not_4_out, not_5_out, not_6_out, not_7_out, not_8_out,
       not_9_out, not_10_out, not_11_out, or_1_out, or_2_out, or_3_out, or_4_out, or_5_out, or_8_out,
       or_10_out, Pred, register_1_q, Replace, RST, Run, Stop1, Stop2, UpdateStat, W1, W2, W3, Wrong, \分支指令 ,
       \硬布线控制器_1_regdst , \硬布线控制器_1_signedext ;
  wire [1:0] id_ex_1_dout_2, id_ex_1_dout_2_2, id_ex_1_dout_2_3, if_id_1_dout_status, JMPStatus, JMPStatusIn,
       multiplexer_5_out, multiplexer_6_out, \数据相关检测_1_forwardr1 , \数据相关检测_1_forwardr2 ;
  wire [2:0] id_ex_1_dout_4;
  wire [3:0] id_ex_1_dout_4_2, id_ex_1_dout_4_3, id_ex_1_dout_4_4, multiplexer_21_out, multiplexer_22_out,
       \硬布线控制器_1_alu_op , \硬布线控制器_1_alu_src , \硬布线控制器_1_beq , \硬布线控制器_1_bltz ;
  wire [4:0] ex_mem_1_dout_5, id_ex_1_dout_5, id_ex_1_dout_5_2, mem_wb_1_dout_5, multiplexer_8_out,
       multiplexer_9_out, multiplexer_11_out, multiplexer_12_out;
  wire [15:0] adder_3_out, \LoadUse次数 , \不跳转数 , \分支指令数 , \总周期数 , \无条件分支数 , \条件分支成功数 , \预测失败次数 , \预测成功数 ;
  wire [31:0] adder_1_out, adder_2_out, bit_extender_1_out, bit_extender_2_out, bit_extender_3_out,
       ex_mem_1_dout_32, ex_mem_1_dout_32_2, ex_mem_1_dout_32_3, ex_mem_1_dout_32_4, EX_PC, id_ex_1_dout_32,
       id_ex_1_dout_32_2, id_ex_1_dout_32_3, id_ex_1_dout_32_4, id_ex_1_dout_32_5, id_ex_1_dout_32_7, ID_PC,
       if_id_1_dout_addr, if_id_1_dout_ins, if_id_1_dout_pc_4, IF_PC, Ins, JMPaddr, JMPaddrIn, JPC, LedData,
       MEM_PC, mem_wb_1_dout_32_2, mem_wb_1_dout_32_3, mem_wb_1_dout_32_4, mips_alu_1_result, mips_ram_1_p8,
       mips_regifile_1_r1, mips_regifile_1_r2, multiplexer_1_out, multiplexer_2_out, multiplexer_3_out,
       multiplexer_4_out, multiplexer_7_out, multiplexer_10_out, multiplexer_13_out, multiplexer_14_out,
       multiplexer_15_out, multiplexer_16_out, multiplexer_17_out, multiplexer_18_out, multiplexer_19_out,
       multiplexer_20_out, multiplexer_23_out, multiplexer_24_out, register_2_q, shifter_1_out,
       shifter_2_out, WB_PC;

  Button \u_总复位  (.out(RST));
  Button _1 (.out(IR1));
  Button _2 (.out(IR2));
  Button _3 (.out(IR3));
  Button \u_继续运行  (.out(Go));
  LED led_1 (.in(W1));
  LED led_2 (.in(W2));
  LED led_3 (.in(W3));
  and and_1 (and_1_out, mem_wb_1_dout_1_2, not_1_out);
  not not_1 (not_1_out, mem_wb_1_dout_1);
  Multiplexer #(.width(32), .enable("false")) multiplexer_1 (
    .in0(multiplexer_4_out), .in1(multiplexer_7_out), .out(multiplexer_1_out), .sel(Wrong));
  Hex_Digit_Display hex_digit_display_1 (.value(LedData[31:28]));  // open: dp
  \分支预测BHT  \u_分支预测bht_1  (
    .BlockDataIn(JMPaddrIn), .Addr1(IF_PC), .BlkDataReady(Replace), .CLK(CLK), .Bench(Pred),
    .JMPaddr(JMPaddr), .JMPStatusIn(JMPStatusIn), .JMPStatus(JMPStatus), .Miss(Miss),
    .UpdateStat(UpdateStat), .Addr2(EX_PC));
  \可计算出地址的跳转指令判断  \u_可计算出地址的跳转指令判断_1  (.J(J), .Instruction(Ins), .JMPPC(JPC), .PC(IF_PC));
  Register #(.width(32)) PC (.D(multiplexer_1_out), .en(Run), .Q(IF_PC), .clk(CLK), .clr(RST));
  Adder #(.width(32)) adder_1 (.a(IF_PC), .b(32'h4), .out(adder_1_out));  // open: cin, cout
  not not_2 (not_2_out, Load_use);
  and and_2 (Run, not_2_out, Enable);
  Register #(.width(1)) register_1 (.D(mem_wb_1_dout_1_2), .en(and_1_out), .Q(register_1_q), .clk(CLK), .clr(or_1_out));
  not not_3 (Enable, register_1_q);
  or or_1 (or_1_out, Go, RST);
  Multiplexer #(.width(32), .enable("false")) multiplexer_2 (
    .in0(JMPaddr), .in1(JPC), .out(multiplexer_2_out), .sel(J));
  Multiplexer #(.width(32), .enable("false")) multiplexer_3 (
    .in0(adder_1_out), .in1(JMPaddr), .out(multiplexer_3_out), .sel(Pred));
  Multiplexer #(.width(32), .enable("false")) multiplexer_4 (
    .in0(multiplexer_3_out), .in1(JPC), .out(multiplexer_4_out), .sel(J));
  Hex_Digit_Display hex_digit_display_2 (.value(LedData[23:20]));  // open: dp
  Hex_Digit_Display hex_digit_display_3 (.value(LedData[27:24]));  // open: dp
  Hex_Digit_Display hex_digit_display_4 (.value(LedData[15:12]));  // open: dp
  Hex_Digit_Display hex_digit_display_5 (.value(LedData[19:16]));  // open: dp
  ROM #(.addrWidth(10), .dataWidth(32)) rom_1 (.addr(IF_PC[11:2]), .data(Ins));  // open: sel
  Multiplexer #(.width(2), .enable("false")) multiplexer_5 (
    .in0(JMPStatus), .in1(2'b01), .out(multiplexer_5_out), .sel(Miss));
  or or_2 (or_2_out, Load_use, register_1_q, 1'b0);
  Hex_Digit_Display hex_digit_display_6 (.value(LedData[7:4]));  // open: dp
  Hex_Digit_Display hex_digit_display_7 (.value(LedData[11:8]));  // open: dp
  Clock clock_1 (.out(CLK));
  IF_ID if_id_1 (
    .Din_Ins(Ins), .Din_PC_4(adder_1_out), .\传输状态In_表明当前传输数据有效 (1'b1), .CLK(CLK),
    .Dout_Ins(if_id_1_dout_ins), .Dout_PC_4(if_id_1_dout_pc_4),
    .\传输状态Out_表明当前传输数据有效 (\if_id_1_传输状态out_表明当前传输数据有效 ), .\同步清零_气泡_高电平有效 (Wrong),
    .\使能端_低电平有效_stall_高电平有效 (or_2_out), .Din_PC(IF_PC), .Dout_PC(ID_PC), .Din_Status(multiplexer_6_out),
    .Dout_Status(if_id_1_dout_status), .Din_Addr(multiplexer_2_out), .Dout_Addr(if_id_1_dout_addr),
    .Din_Miss(Miss), .Dout_Miss(if_id_1_dout_miss), .Din_Hit(not_4_out), .Dout_Hit(if_id_1_dout_hit));
  Multiplexer #(.width(2), .enable("false")) multiplexer_6 (
    .in0(multiplexer_5_out), .in1(2'b11), .out(multiplexer_6_out), .sel(J));
  not not_4 (not_4_out, Miss);
  not not_5 (not_5_out, Bench);
  Multiplexer #(.width(32), .enable("false")) multiplexer_7 (
    .in0(JMPaddrIn), .in1(id_ex_1_dout_32_5), .out(multiplexer_7_out), .sel(not_5_out));
  Hex_Digit_Display hex_digit_display_8 (.value(LedData[3:0]));  // open: dp
  \数据相关检测  \u_数据相关检测_1  (
    .OP(if_id_1_dout_ins[31:26]), .EX_WriteReg_num(id_ex_1_dout_5_2), .EX_RegWrite(id_ex_1_dout_4_4[1]),
    .ForwardR1(\数据相关检测_1_forwardr1 ), .MEM_WriteReg_num(ex_mem_1_dout_5), .MEM_RegWrite(ex_mem_1_dout_1_6),
    .ForwardR2(\数据相关检测_1_forwardr2 ), .Func(if_id_1_dout_ins[5:0]), .ID_R1_num(multiplexer_8_out),
    .ID_R2_num(multiplexer_11_out), .EX_MemToReg(id_ex_1_dout_4_2[2]), .MEM_MemToReg(ex_mem_1_dout_1_4),
    .Load_Use(Load_use));  // open: 数据相关
  // Probe on \总周期数 
  // Probe on \无条件分支数 
  // Probe on \条件分支成功数 
  // Probe on \LoadUse次数 
  // Probe on \预测成功数 
  // Probe on \预测失败次数 
  \硬布线控制器  \u_硬布线控制器_1  (
    .Func(if_id_1_dout_ins[5:0]), .OP(if_id_1_dout_ins[31:26]), .ALU_OP(\硬布线控制器_1_alu_op ),
    .MemToReg(\硬布线控制器_1_beq [2]), .MemWrite(\硬布线控制器_1_beq [3]), .ALU_SRC(\硬布线控制器_1_alu_src [0]),
    .RegWrite(\硬布线控制器_1_alu_src [1]), .SysCALL(\硬布线控制器_1_alu_src [3]), .SignedExt(\硬布线控制器_1_signedext ),
    .RegDst(\硬布线控制器_1_regdst ), .JR(\硬布线控制器_1_bltz [2]), .JMP(\硬布线控制器_1_bltz [3]), .Beq(\硬布线控制器_1_beq [0]),
    .JAL(\硬布线控制器_1_alu_src [2]), .Bne(\硬布线控制器_1_beq [1]), .SH(\硬布线控制器_1_bltz [1]), .BLTZ(\硬布线控制器_1_bltz [0]));  // open: ERET, MF, MFC0, MTC0
  // Probe on IF_PC[11:0]
  Multiplexer #(.width(5), .enable("false")) multiplexer_8 (
    .in0(if_id_1_dout_ins[25:21]), .in1(5'b00100), .out(multiplexer_8_out), .sel(\硬布线控制器_1_alu_src [3]));
  Multiplexer #(.width(5), .enable("false")) multiplexer_9 (
    .in0(if_id_1_dout_ins[20:16]), .in1(if_id_1_dout_ins[15:11]), .out(multiplexer_9_out),
    .sel(\硬布线控制器_1_regdst ));
  assign bit_extender_1_out = {{16{1'b0}}, if_id_1_dout_ins[15:0]};  // Bit_Extender bit_extender_1
  Multiplexer #(.width(32), .enable("false")) multiplexer_10 (
    .in0(bit_extender_1_out), .in1(bit_extender_2_out), .out(multiplexer_10_out), .sel(\硬布线控制器_1_signedext ));
  assign bit_extender_2_out = {{16{if_id_1_dout_ins[15]}}, if_id_1_dout_ins[15:0]};  // Bit_Extender bit_extender_2
  assign bit_extender_3_out = {{6{if_id_1_dout_ins[25]}}, if_id_1_dout_ins[25:0]};  // Bit_Extender bit_extender_3
  // Probe on ID_PC[11:0]
  Multiplexer #(.width(5), .enable("false")) multiplexer_11 (
    .in0(if_id_1_dout_ins[20:16]), .in1(5'b00010), .out(multiplexer_11_out), .sel(\硬布线控制器_1_alu_src [3]));
  Multiplexer #(.width(5), .enable("false")) multiplexer_12 (
    .in0(multiplexer_9_out), .in1({5{1'b1}}), .out(multiplexer_12_out), .sel(\硬布线控制器_1_alu_src [2]));
  // Probe on EX_PC[11:0]
  // Probe on MEM_PC[11:0]
  // Probe on WB_PC[11:0]
  MIPS_Regifile mips_regifile_1 (
    .Din(multiplexer_24_out), .Clk(CLK), .R1(mips_regifile_1_r1), .R2(mips_regifile_1_r2),
    .WE(mem_wb_1_dout_1_4), .W_num(mem_wb_1_dout_5), .R1_num(multiplexer_8_out), .R2_num(multiplexer_11_out));
  or or_3 (or_3_out, Wrong, Load_use);
  ID_EX id_ex_1 (
    .Din_4(\硬布线控制器_1_bltz ), .Din_4_2(\硬布线控制器_1_beq ), .Din_4_3(\硬布线控制器_1_alu_op ),
    .Din_4_4(\硬布线控制器_1_alu_src ), .Din_32(mips_regifile_1_r1), .Din_32_2(mips_regifile_1_r2),
    .Din_32_3(multiplexer_10_out), .Din_32_4(bit_extender_3_out), .Din_5(if_id_1_dout_ins[10:6]),
    .Din_32_5(if_id_1_dout_pc_4), .\传输状态In_表明当前传输数据有效 (\if_id_1_传输状态out_表明当前传输数据有效 ), .CLK(CLK),
    .Dout_4({JMP, id_ex_1_dout_4}), .Dout_4_2(id_ex_1_dout_4_2), .Dout_4_3(id_ex_1_dout_4_3),
    .Dout_4_4(id_ex_1_dout_4_4), .Dout_32(id_ex_1_dout_32), .Dout_32_2(id_ex_1_dout_32_2),
    .Dout_32_3(id_ex_1_dout_32_3), .Dout_32_4(id_ex_1_dout_32_4), .Dout_5(id_ex_1_dout_5),
    .Dout_32_5(id_ex_1_dout_32_5), .\传输状态Out_表明当前传输数据有效 (\id_ex_1_传输状态out_表明当前传输数据有效 ),
    .\同步清零_气泡_高电平有效 (or_3_out), .\使能端_低电平有效_stall_高电平有效 (or_4_out), .Din_5_2(multiplexer_12_out),
    .Dout_5_2(id_ex_1_dout_5_2), .Din_32_6(ID_PC), .Dout_32_6(EX_PC), .Din_2(\数据相关检测_1_forwardr1 ),
    .Dout_2(id_ex_1_dout_2), .Din_2_2(\数据相关检测_1_forwardr2 ), .Dout_2_2(id_ex_1_dout_2_2),
    .Din_2_3(if_id_1_dout_status), .Dout_2_3(id_ex_1_dout_2_3), .Din_32_7(if_id_1_dout_addr),
    .Dout_32_7(id_ex_1_dout_32_7), .Din_1(if_id_1_dout_miss), .Dout_1(id_ex_1_dout_1),
    .Din_1_2(if_id_1_dout_hit), .Dout_1_2(UpdateStat));
  or or_4 (or_4_out, register_1_q, 1'b0);
  Counter #(.width(16), .max('hffff)) counter_1 (
    .count(Enable), .Q(\总周期数 ), .clk(CLK), .clr(RST));  // open: load, D, carry
  Multiplexer #(.select(2), .width(32), .enable("false")) multiplexer_13 (
    .in0(id_ex_1_dout_32), .in1(mem_wb_1_dout_32_2), .in2(mem_wb_1_dout_32_3), .in3(ex_mem_1_dout_32_2),
    .out(multiplexer_13_out), .sel(id_ex_1_dout_2));
  Multiplexer #(.select(2), .width(32), .enable("false")) multiplexer_14 (
    .in0(id_ex_1_dout_32_2), .in1(mem_wb_1_dout_32_2), .in2(mem_wb_1_dout_32_3), .in3(ex_mem_1_dout_32_2),
    .out(multiplexer_14_out), .sel(id_ex_1_dout_2_2));
  Counter #(.width(16), .max('hffff)) counter_2 (
    .count(JMP), .Q(\无条件分支数 ), .clk(CLK), .clr(RST));  // open: load, D, carry
  not not_6 (not_6_out, comparator_1_eq);
  Register #(.width(32)) register_2 (.D(multiplexer_13_out), .en(and_3_out), .Q(register_2_q), .clk(CLK), .clr(RST));
  and and_3 (and_3_out, comparator_1_eq, id_ex_1_dout_4_4[3]);
  Comparator #(.width(32)) comparator_1 (.a(32'h22), .b(multiplexer_14_out), .eq(comparator_1_eq));  // open: gt, lt
  and and_4 (Stop1, not_6_out, id_ex_1_dout_4_4[3]);
  Counter #(.width(16), .max('hffff)) counter_3 (
    .count(Benchif), .Q(\条件分支成功数 ), .clk(CLK), .clr(RST));  // open: load, D, carry
  Multiplexer #(.width(32), .enable("false")) multiplexer_15 (
    .in0(multiplexer_14_out), .in1(id_ex_1_dout_32_3), .out(multiplexer_15_out), .sel(id_ex_1_dout_4_4[0]));
  Shifter #(.width(32)) shifter_1 (.in(id_ex_1_dout_32_3), .\dist (5'b00010), .out(shifter_1_out));
  Shifter #(.width(32)) shifter_2 (.in(id_ex_1_dout_32_4), .\dist (5'b00010), .out(shifter_2_out));
  and and_5 (Replace, id_ex_1_dout_1, \分支指令 );
  not not_7 (not_7_out, mips_alu_1_equal);
  MIPS_ALU mips_alu_1 (
    .X(multiplexer_13_out), .Y(multiplexer_15_out), .AluOP(id_ex_1_dout_4_3), .Equal(mips_alu_1_equal),
    .Result(mips_alu_1_result), .shamt(id_ex_1_dout_5));  // open: Result_2
  Adder #(.width(32)) adder_2 (.a(shifter_1_out), .b(id_ex_1_dout_32_5), .out(adder_2_out));  // open: cin, cout
  and and_6 (and_6_out, id_ex_1_dout_4_2[0], mips_alu_1_equal);
  and and_7 (and_7_out, id_ex_1_dout_4_2[1], not_7_out);
  nor nor_1 (nor_1_out, Stop2, Stop1);
  or or_5 (or_5_out, and_6_out, and_7_out);
  Counter #(.width(16), .max('hffff)) counter_4 (
    .count(and_8_out), .Q(\LoadUse次数 ), .clk(CLK), .clr(RST));  // open: load, D, carry
  and and_8 (and_8_out, nor_1_out, Enable, Load_use);
  Comparator #(.width(32)) comparator_2 (.a(multiplexer_13_out), .b({32{1'b0}}), .lt(comparator_2_lt));  // open: gt, eq
  and and_9 (and_9_out, id_ex_1_dout_4[0], comparator_2_lt);
  nor nor_2 (nor_2_out, and_9_out, or_5_out);
  Multiplexer #(.width(32), .enable("false")) multiplexer_16 (
    .in0(adder_2_out), .in1(id_ex_1_dout_32_5), .out(multiplexer_16_out), .sel(nor_2_out));
  or or_6 (\分支指令 , id_ex_1_dout_4_2[1], id_ex_1_dout_4_2[0], id_ex_1_dout_4[0], JMP);
  not not_8 (not_8_out, id_ex_1_dout_4[2]);
  not not_9 (not_9_out, JMP);
  or or_7 (Benchif, and_9_out, or_5_out);
  Multiplexer #(.width(32), .enable("false")) multiplexer_17 (
    .in0(multiplexer_13_out), .in1(shifter_2_out), .out(multiplexer_17_out), .sel(not_8_out));
  Multiplexer #(.width(32), .enable("false")) multiplexer_18 (
    .in0(multiplexer_17_out), .in1(multiplexer_16_out), .out(multiplexer_18_out), .sel(not_9_out));
  or or_8 (or_8_out, register_1_q, 1'b0);
  Counter #(.width(16), .max('hffff)) counter_5 (
    .count(Wrong), .Q(\预测失败次数 ), .clk(CLK), .clr(RST));  // open: load, D, carry
  or or_9 (Bench, and_9_out, or_5_out, JMP);
  \分支预测状态转换  \u_分支预测状态转换_1  (
    .bench(Bench), .Status_out1(JMPStatusIn[1]), .Status_in1(id_ex_1_dout_2_3[1]),
    .Status_in0(id_ex_1_dout_2_3[0]), .Status_out0(JMPStatusIn[0]), .Wrong(Wrong),
    .Pre_addr(id_ex_1_dout_32_7), .Addr_out(JMPaddrIn), .Addr_in0(multiplexer_18_out));
  EX_MEM ex_mem_1 (
    .Din_1_4(id_ex_1_dout_4_2[2]), .Din_1_5(id_ex_1_dout_4_2[3]), .Din_32_2(mips_alu_1_result),
    .Din_32_3(multiplexer_14_out), .Din_32_4(id_ex_1_dout_32_5),
    .\传输状态In_表明当前传输数据有效 (\id_ex_1_传输状态out_表明当前传输数据有效 ), .CLK(CLK), .Dout_1_4(ex_mem_1_dout_1_4),
    .Dout_1_5(ex_mem_1_dout_1_5), .Dout_32_2(ex_mem_1_dout_32_2), .Dout_32_3(ex_mem_1_dout_32_3),
    .Dout_32_4(ex_mem_1_dout_32_4), .\传输状态Out_表明当前传输数据有效 (\ex_mem_1_传输状态out_表明当前传输数据有效 ),
    .\同步清零_气泡_高电平有效 (1'b0), .\使能端_低电平有效_stall_高电平有效 (or_8_out), .Din_1_6(id_ex_1_dout_4_4[1]),
    .Dout_1_6(ex_mem_1_dout_1_6), .Din_1_7(id_ex_1_dout_4_4[2]), .Dout_1_7(ex_mem_1_dout_1_7),
    .Din_32(register_2_q), .Dout_32(ex_mem_1_dout_32), .Dout_1_3(ex_mem_1_dout_1_3),
    .Din_1_3(id_ex_1_dout_4_4[3]), .Din_1_2(comparator_1_eq), .Dout_1_2(ex_mem_1_dout_1_2),
    .Din_1(id_ex_1_dout_4[1]), .Dout_1(ex_mem_1_dout_1), .Din_5(id_ex_1_dout_5_2), .Dout_5(ex_mem_1_dout_5),
    .Din_32_5(EX_PC), .Dout_32_5(MEM_PC));  // open: Din_1_8, Dout_1_8, Din_1_9, Dout_1_9, Dout_32_6, Dout_32_7, Din_32_6, Din_32_7, Din_1_10, Dout_1_10
  not not_10 (not_10_out, ex_mem_1_dout_1_2);
  and and_10 (Stop2, not_10_out, ex_mem_1_dout_1_3);
  Counter #(.width(16), .max('hffff)) counter_6 (
    .count(\分支指令 ), .Q(\分支指令数 ), .clk(CLK), .clr(RST));  // open: load, D, carry
  Multiplexer #(.width(32), .enable("false")) multiplexer_19 (
    .in0({{16{1'b0}}, ex_mem_1_dout_32_3[15:0]}), .in1({ex_mem_1_dout_32_3[15:0], {16{1'b0}}}),
    .out(multiplexer_19_out), .sel(ex_mem_1_dout_32_2[1]));
  Multiplexer #(.width(32), .enable("false")) multiplexer_20 (
    .in0(ex_mem_1_dout_32_3), .in1(multiplexer_19_out), .out(multiplexer_20_out), .sel(ex_mem_1_dout_1));
  not not_11 (not_11_out, Bench);
  Multiplexer #(.width(4), .enable("false")) multiplexer_21 (
    .in0(4'b1111), .in1(multiplexer_22_out), .out(multiplexer_21_out), .sel(ex_mem_1_dout_1));
  Multiplexer #(.width(4), .enable("false")) multiplexer_22 (
    .in0(4'b0011), .in1(4'b1100), .out(multiplexer_22_out), .sel(ex_mem_1_dout_32_2[1]));
  Counter #(.width(16), .max('hffff)) counter_7 (
    .count(and_11_out), .Q(\不跳转数 ), .clk(CLK), .clr(RST));  // open: load, D, carry
  and and_11 (and_11_out, not_11_out, \分支指令 );
  // MIPS_RAM mips_ram_1: pin names not known; wires that end beside it: ex_mem_1_dout_32_2[11:2], multiplexer_20_out, ex_mem_1_dout_1_5, multiplexer_21_out, CLK, 1'b1, RST, mips_ram_1_p8
  MEM_WB mem_wb_1 (
    .Din_1_4(ex_mem_1_dout_1_6), .Din_1_5(ex_mem_1_dout_1_7), .Din_32(ex_mem_1_dout_32),
    .Din_32_3(mips_ram_1_p8), .Din_32_4(ex_mem_1_dout_32_4),
    .\传输状态In_表明当前传输数据有效 (\ex_mem_1_传输状态out_表明当前传输数据有效 ), .CLK(CLK), .Dout_1_4(mem_wb_1_dout_1_4),
    .Dout_1_5(mem_wb_1_dout_1_5), .Dout_32(LedData), .Dout_32_3(mem_wb_1_dout_32_3),
    .Dout_32_4(mem_wb_1_dout_32_4), .\同步清零_气泡_高电平有效 (1'b0), .\使能端_低电平有效_stall_高电平有效 (or_10_out),
    .Dout_1(mem_wb_1_dout_1), .Dout_1_2(mem_wb_1_dout_1_2), .Din_1(ex_mem_1_dout_1_2),
    .Din_1_2(ex_mem_1_dout_1_3), .Din_5(ex_mem_1_dout_5), .Dout_5(mem_wb_1_dout_5), .Din_32_5(MEM_PC),
    .Dout_32_5(WB_PC), .Din_1_3(ex_mem_1_dout_1_4), .Dout_1_3(mem_wb_1_dout_1_3),
    .Din_32_2(ex_mem_1_dout_32_2), .Dout_32_2(mem_wb_1_dout_32_2));  // open: 传输状态Out_表明当前传输数据有效, Din_1_6, Dout_1_6, Din_1_7, Dout_1_7, Din_32_6, Dout_32_6, Din_32_7, Dout_32_7, Din_1_8, Dout_1_8
  or or_10 (or_10_out, register_1_q, 1'b0);
  Multiplexer #(.width(32), .enable("false")) multiplexer_23 (
    .in0(mem_wb_1_dout_32_2), .in1(mem_wb_1_dout_32_3), .out(multiplexer_23_out), .sel(mem_wb_1_dout_1_3));
  Adder #(.width(16)) adder_3 (.a(\不跳转数 ), .b(\预测失败次数 ), .out(adder_3_out));  // open: cin, cout
  Multiplexer #(.width(32), .enable("false")) multiplexer_24 (
    .in0(multiplexer_23_out), .in1(mem_wb_1_dout_32_4), .out(multiplexer_24_out), .sel(mem_wb_1_dout_1_5));
  Subtractor #(.width(16)) subtractor_1 (.a(\分支指令数 ), .b(adder_3_out), .out(\预测成功数 ));  // open: bin, bout

  // Notes on the sheet:
  //   中断源
  //   中断等待指示
  //   分支预测BHT
  //   分支地址提前计算
  //   指令存储器
  //   数码管输出
  //   指令字
  //   contents of rom_1 (hex, n*v repeats v):
  //   20110001 8000c05 20110001 20120002 20130003 8000c09 20110001 20120002 20130003 8000c0d 20110001
  //   20120002 20130003 8000c11 20110001 20120002 20130003 c000cf5 20100001 20110001 118fc0 112020
  //   20020022 c 118882 12200001 8000c15 112020 20020022 c 20110001 118880 112020 20020022 c 12200001
  //   8000c1f 20110001 118fc0 112020 20020022 c 1188c3 112020 20020022 c 118903 112020 20020022 c 118903
  //   112020 20020022 c 118903 112020 20020022 c 118903 112020 20020022 c 118903 112020 20020022 c 118903
  //   112020 20020022 c 118903 112020 20020022 c 20100001 109fc0 139fc3 8021 2012000c 24160003 26100001
  //   3210000f 20080008 20090001 139900 2709825 132020 20020022 c 1094022 1500fff9 22100001 2018000f
  //   2188024 108700 20080008 20090001 139902 2709825 132021 20020022 c 1094022 1500fff9 108702 2c9b022
  //   12c00001 8000c50 4020 1084027 84400 3508ffff 82021 20020022 c 2010ffff 20110000 ae300000 22100001
  //   22310004 ae300000 22100001 22310004 ae300000 22100001 22310004 ae300000 22100001 22310004 ae300000
  //   22100001 22310004 ae300000 22100001 22310004 ae300000 22100001 22310004 ae300000 22100001 22310004
  //   ae300000 22100001 22310004 ae300000 22100001 22310004 ae300000 22100001 22310004 ae300000 22100001
  //   22310004 ae300000 22100001 22310004 ae300000 22100001 22310004 ae300000 22100001 22310004 ae300000
  //   22100001 22310004 22100001 8020 2011003c 8e130000 8e340000 274402a 11000002 ae330000 ae140000
  //   2231fffc 1611fff8 102020 20020022 c 22100004 2011003c 1611fff2 20020032 c 20080001 20110010 112020
  //   20020022 c 200b0020 2288823 112020 20020022 c 216bffff 1560fffa 2002000a c 2008ffff 20117777 112020
  //   20020022 c 200b0010 2288826 112020 20020022 c 216bffff 1560fffa 2002000a c 20090000 200b0020
  //   20110001 20120001 a5310000 112020 20020022 c 2328820 21290002 216bffff 1560fff8 200b0010 20090000
  //   8d310000 112020 20020022 c 21290004 216bffff 1560fff9 2002000a c 2011fff1 112020 20020022 c 22310001
  //   620fffb 2002000a c 2002000a c 20100000 22100001 102020 20020022 c 22100002 102020 20020022 c
  //   22100003 102020 20020022 c 22100004 102020 20020022 c 22100005 102020 20020022 c 22100006 102020
  //   20020022 c 22100007 102020 20020022 c 22100008 102020 20020022 20020022 c 3e00008
  //   IF/ID
  //   OP
  //   Func
  //   rs
  //   rt
  //   rd
  //   JMP
  //   Beq
  //   JR
  //   Bne
  //   SH
  //   Bltz
  //   JAL
  //   Syscall
  //   MemToReg
  //   MemWrite
  //   AluOP
  //   AluSrcB
  //   RegWrite
  //   RegDst
  //   流水调试日志用
  //   ID/EX
  //   统计流水线各类数据
  //   EX/MEM
  //   MEM/WB
endmodule
// 分支预测BHT
module \分支预测BHT  (
  input  [31:0] Addr1,
  input  [31:0] Addr2,
  input  [31:0] BlockDataIn,
  input  [1:0] JMPStatusIn,
  input  CLK,
  input  BlkDataReady,
  input  UpdateStat,
  output Bench,
  output Miss,
  output [31:0] JMPaddr,
  output [1:0] JMPStatus
);

  wire and_26_out, and_27_out, and_28_out, and_29_out, and_30_out, and_31_out, and_32_out, and_33_out,
       comparator_1_eq, comparator_2_eq, comparator_3_eq, comparator_4_eq, comparator_5_eq, comparator_6_eq,
       comparator_7_eq, comparator_8_eq, comparator_9_eq, comparator_10_eq, comparator_11_eq,
       comparator_12_eq, comparator_13_eq, comparator_14_eq, comparator_15_eq, comparator_16_eq,
       decoder_1_out0, decoder_1_out1, decoder_1_out2, decoder_1_out3, decoder_1_out4, decoder_1_out5,
       decoder_1_out6, decoder_1_out7, Hit, L0, L1, L2, L3, L4, L5, L6, L7, nand_1_out, not_1_out, not_2_out,
       not_3_out, not_4_out, not_5_out, not_6_out, not_7_out, not_8_out, or_1_out, or_2_out, or_3_out,
       or_4_out, or_5_out, or_6_out, or_7_out, or_8_out, R0, R1, R2, R3, R4, R5, R6, R7, Up0, Up1, Up2, Up3,
       Up4, Up5, Up6, Up7, V0, V1, V2, V3, V4, V5, V6, V7;
  wire [1:0] StatData0, StatData1, StatData2, StatData3, StatData4, StatData5, StatData6, StatData7,
       \分支预测状态_2_q , \分支预测状态_3_q , \分支预测状态_4_q , \分支预测状态_5_q , \分支预测状态_6_q , \分支预测状态_7_q , \分支预测状态_8_q ,
       \分支预测状态_q ;
  wire [2:0] max3_1_max_num, max3_2_max_num, max3_3_max_num, max3_4_max_num, max3_5_max_num, max3_6_max_num,
       max3_7_max_num, multiplexer_1_out, not_9_out, priority_encoder_1_out, Select;
  wire [15:0] C0, C1, C2, C3, C4, C5, C6, C7, max3_1_max, max3_2_max, max3_3_max, max3_4_max, max3_5_max,
       max3_6_max;
  wire [31:0] SlotData0, SlotData1, SlotData2, SlotData3, SlotData4, SlotData5, SlotData6, SlotData7, Tag0,
       Tag1, Tag2, Tag3, Tag4, Tag5, Tag6, Tag7, \数据块副本_2_q , \数据块副本_3_q , \数据块副本_4_q , \数据块副本_5_q ,
       \数据块副本_6_q , \数据块副本_7_q , \数据块副本_8_q , \数据块副本_q ;

  Comparator #(.width(32)) comparator_1 (.a(Addr1), .b(Tag0), .eq(comparator_1_eq));  // open: gt, lt
  Comparator #(.width(32)) comparator_2 (.a(Addr1), .b(Tag2), .eq(comparator_2_eq));  // open: gt, lt
  Comparator #(.width(32)) comparator_3 (.a(Addr1), .b(Tag4), .eq(comparator_3_eq));  // open: gt, lt
  Comparator #(.width(32)) comparator_4 (.a(Addr1), .b(Tag6), .eq(comparator_4_eq));  // open: gt, lt
  Comparator #(.width(32)) comparator_5 (.a(Addr2), .b(Tag0), .eq(comparator_5_eq));  // open: gt, lt
  Comparator #(.width(32)) comparator_6 (.a(Addr2), .b(Tag2), .eq(comparator_6_eq));  // open: gt, lt
  Comparator #(.width(32)) comparator_7 (.a(Addr2), .b(Tag4), .eq(comparator_7_eq));  // open: gt, lt
  Comparator #(.width(32)) comparator_8 (.a(Addr2), .b(Tag6), .eq(comparator_8_eq));  // open: gt, lt
  Max3 max3_1 (.Y(C1), .X(C0), .Y_num(3'b001), .X_num(3'b000), .MAX(max3_1_max), .Max_num(max3_1_max_num));
  Max3 max3_2 (.Y(C3), .X(C2), .Y_num(3'b011), .X_num(3'b010), .MAX(max3_2_max), .Max_num(max3_2_max_num));
  Max3 max3_3 (.Y(C5), .X(C4), .Y_num(3'b101), .X_num(3'b100), .MAX(max3_3_max), .Max_num(max3_3_max_num));
  Max3 max3_4 (.Y(C7), .X(C6), .Y_num(3'b111), .X_num(3'b110), .MAX(max3_4_max), .Max_num(max3_4_max_num));
  and and_1 (L0, V0, comparator_1_eq);
  and and_2 (L2, V2, comparator_2_eq);
  and and_3 (L4, V4, comparator_3_eq);
  and and_4 (L6, V6, comparator_4_eq);
  and and_5 (Up0, V0, comparator_5_eq);
  and and_6 (Up2, V2, comparator_6_eq);
  and and_7 (Up4, V4, comparator_7_eq);
  and and_8 (Up6, V6, comparator_8_eq);
  Max3 max3_5 (
    .Y(max3_2_max), .X(max3_1_max), .Y_num(max3_2_max_num), .X_num(max3_1_max_num), .MAX(max3_5_max),
    .Max_num(max3_5_max_num));
  Max3 max3_6 (
    .Y(max3_4_max), .X(max3_3_max), .Y_num(max3_4_max_num), .X_num(max3_3_max_num), .MAX(max3_6_max),
    .Max_num(max3_6_max_num));
  not not_1 (not_1_out, V7);
  not not_2 (not_2_out, V6);
  not not_3 (not_3_out, V5);
  not not_4 (not_4_out, V4);
  not not_5 (not_5_out, V3);
  not not_6 (not_6_out, V2);
  not not_7 (not_7_out, V1);
  not not_8 (not_8_out, V0);
  Max3 max3_7 (
    .Y(max3_6_max), .X(max3_5_max), .Y_num(max3_6_max_num), .X_num(max3_5_max_num), .Max_num(max3_7_max_num));  // open: MAX
  Priority_Encoder priority_encoder_1 (
    .in0(not_1_out), .in1(not_2_out), .in2(not_3_out), .in3(not_4_out), .in4(not_5_out), .in5(not_6_out),
    .in6(not_7_out), .in7(not_8_out), .out(priority_encoder_1_out));  // open: en_in, gs, en_out
  assign not_9_out = ~priority_encoder_1_out;  // NOT_Gate not_9, 3 bits wide
  Comparator #(.width(32)) comparator_9 (.a(Addr1), .b(Tag1), .eq(comparator_9_eq));  // open: gt, lt
  Comparator #(.width(32)) comparator_10 (.a(Addr1), .b(Tag3), .eq(comparator_10_eq));  // open: gt, lt
  Comparator #(.width(32)) comparator_11 (.a(Addr1), .b(Tag5), .eq(comparator_11_eq));  // open: gt, lt
  Comparator #(.width(32)) comparator_12 (.a(Addr1), .b(Tag7), .eq(comparator_12_eq));  // open: gt, lt
  Comparator #(.width(32)) comparator_13 (.a(Addr2), .b(Tag1), .eq(comparator_13_eq));  // open: gt, lt
  Comparator #(.width(32)) comparator_14 (.a(Addr2), .b(Tag3), .eq(comparator_14_eq));  // open: gt, lt
  Comparator #(.width(32)) comparator_15 (.a(Addr2), .b(Tag5), .eq(comparator_15_eq));  // open: gt, lt
  Comparator #(.width(32)) comparator_16 (.a(Addr2), .b(Tag7), .eq(comparator_16_eq));  // open: gt, lt
  Decoder #(.select(3), .enable("false")) decoder_1 (
    .out0(decoder_1_out0), .out1(decoder_1_out1), .out2(decoder_1_out2), .out3(decoder_1_out3),
    .out4(decoder_1_out4), .out5(decoder_1_out5), .out6(decoder_1_out6), .out7(decoder_1_out7),
    .sel(multiplexer_1_out));
  Multiplexer #(.width(3), .enable("false")) multiplexer_1 (
    .in0(max3_7_max_num), .in1(not_9_out), .out(multiplexer_1_out), .sel(nand_1_out));
  nand nand_1 (nand_1_out, V7, V6, V5, V4, V3, V2, V1, V0);
  and and_9 (L1, V1, comparator_9_eq);
  and and_10 (L3, V3, comparator_10_eq);
  and and_11 (L5, V5, comparator_11_eq);
  and and_12 (L7, V7, comparator_12_eq);
  and and_13 (Up1, V1, comparator_13_eq);
  and and_14 (Up3, V3, comparator_14_eq);
  and and_15 (Up5, V5, comparator_15_eq);
  and and_16 (Up7, V7, comparator_16_eq);
  nor nor_1 (Miss, L1, L0, L3, L2, L4, L5, L6, L7);
  not not_10 (Hit, Miss);
  and and_17 (R0, decoder_1_out0, BlkDataReady);
  and and_18 (R1, decoder_1_out1, BlkDataReady);
  and and_19 (R2, decoder_1_out2, BlkDataReady);
  and and_20 (R3, decoder_1_out3, BlkDataReady);
  and and_21 (R4, decoder_1_out4, BlkDataReady);
  and and_22 (R5, decoder_1_out5, BlkDataReady);
  and and_23 (R6, decoder_1_out6, BlkDataReady);
  and and_24 (R7, decoder_1_out7, BlkDataReady);
  Register #(.width(1)) vaild (.D(1'b1), .en(R0), .Q(V0), .clk(CLK));  // open: clr
  Register #(.width(1)) vaild_2 (.D(1'b1), .en(R1), .Q(V1), .clk(CLK));  // open: clr
  Register #(.width(1)) vaild_3 (.D(1'b1), .en(R2), .Q(V2), .clk(CLK));  // open: clr
  Register #(.width(1)) vaild_4 (.D(1'b1), .en(R3), .Q(V3), .clk(CLK));  // open: clr
  Register #(.width(1)) vaild_5 (.D(1'b1), .en(R4), .Q(V4), .clk(CLK));  // open: clr
  Register #(.width(1)) vaild_6 (.D(1'b1), .en(R5), .Q(V5), .clk(CLK));  // open: clr
  Register #(.width(1)) vaild_7 (.D(1'b1), .en(R6), .Q(V6), .clk(CLK));  // open: clr
  Register #(.width(1)) vaild_8 (.D(1'b1), .en(R7), .Q(V7), .clk(CLK));  // open: clr
  and and_25 (Bench, Hit, JMPStatus[1]);
  Register #(.width(32)) \u_标记位  (.D(Addr2), .en(R0), .Q(Tag0), .clk(CLK));  // open: clr
  Register #(.width(32)) \u_标记位_2  (.D(Addr2), .en(R1), .Q(Tag1), .clk(CLK));  // open: clr
  Register #(.width(32)) \u_标记位_3  (.D(Addr2), .en(R2), .Q(Tag2), .clk(CLK));  // open: clr
  Register #(.width(32)) \u_标记位_4  (.D(Addr2), .en(R3), .Q(Tag3), .clk(CLK));  // open: clr
  Register #(.width(32)) \u_标记位_5  (.D(Addr2), .en(R4), .Q(Tag4), .clk(CLK));  // open: clr
  Register #(.width(32)) \u_标记位_6  (.D(Addr2), .en(R5), .Q(Tag5), .clk(CLK));  // open: clr
  Register #(.width(32)) \u_标记位_7  (.D(Addr2), .en(R6), .Q(Tag6), .clk(CLK));  // open: clr
  Register #(.width(32)) \u_标记位_8  (.D(Addr2), .en(R7), .Q(Tag7), .clk(CLK));  // open: clr
  Priority_Encoder priority_encoder_2 (
    .in0(L0), .in1(L1), .in2(L2), .in3(L3), .in4(L4), .in5(L5), .in6(L6), .in7(L7), .out(Select));  // open: en_in, gs, en_out
  Counter #(.width(16), .max('hffff)) \u_淘汰标志位  (
    .load(R0), .D({16{1'b0}}), .count(Hit), .Q(C0), .clk(CLK), .clr(L0));  // open: carry
  Counter #(.width(16), .max('hffff)) \u_淘汰标志位_2  (
    .load(R1), .D({16{1'b0}}), .count(Hit), .Q(C1), .clk(CLK), .clr(L1));  // open: carry
  Counter #(.width(16), .max('hffff)) \u_淘汰标志位_3  (
    .load(R2), .D({16{1'b0}}), .count(Hit), .Q(C2), .clk(CLK), .clr(L2));  // open: carry
  Counter #(.width(16), .max('hffff)) \u_淘汰标志位_4  (
    .load(R3), .D({16{1'b0}}), .count(Hit), .Q(C3), .clk(CLK), .clr(L3));  // open: carry
  Counter #(.width(16), .max('hffff)) \u_淘汰标志位_5  (
    .load(R4), .D({16{1'b0}}), .count(Hit), .Q(C4), .clk(CLK), .clr(L4));  // open: carry
  Counter #(.width(16), .max('hffff)) \u_淘汰标志位_6  (
    .load(R5), .D({16{1'b0}}), .count(Hit), .Q(C5), .clk(CLK), .clr(L5));  // open: carry
  Counter #(.width(16), .max('hffff)) \u_淘汰标志位_7  (
    .load(R6), .D({16{1'b0}}), .count(Hit), .Q(C6), .clk(CLK), .clr(L6));  // open: carry
  Counter #(.width(16), .max('hffff)) \u_淘汰标志位_8  (
    .load(R7), .D({16{1'b0}}), .count(Hit), .Q(C7), .clk(CLK), .clr(L7));  // open: carry
  Register #(.width(32)) \u_数据块副本  (.D(BlockDataIn), .en(R0), .Q(\数据块副本_q ), .clk(CLK));  // open: clr
  Register #(.width(32)) \u_数据块副本_2  (.D(BlockDataIn), .en(R1), .Q(\数据块副本_2_q ), .clk(CLK));  // open: clr
  Register #(.width(32)) \u_数据块副本_3  (.D(BlockDataIn), .en(R2), .Q(\数据块副本_3_q ), .clk(CLK));  // open: clr
  Register #(.width(32)) \u_数据块副本_4  (.D(BlockDataIn), .en(R3), .Q(\数据块副本_4_q ), .clk(CLK));  // open: clr
  Register #(.width(32)) \u_数据块副本_5  (.D(BlockDataIn), .en(R4), .Q(\数据块副本_5_q ), .clk(CLK));  // open: clr
  Register #(.width(32)) \u_数据块副本_6  (.D(BlockDataIn), .en(R5), .Q(\数据块副本_6_q ), .clk(CLK));  // open: clr
  Register #(.width(32)) \u_数据块副本_7  (.D(BlockDataIn), .en(R6), .Q(\数据块副本_7_q ), .clk(CLK));  // open: clr
  Register #(.width(32)) \u_数据块副本_8  (.D(BlockDataIn), .en(R7), .Q(\数据块副本_8_q ), .clk(CLK));  // open: clr
  assign SlotData0 = L0 ? \数据块副本_q  : 32'bz;  // Controlled_Buffer controlled_buffer_1
  assign SlotData1 = L1 ? \数据块副本_2_q  : 32'bz;  // Controlled_Buffer controlled_buffer_2
  assign SlotData2 = L2 ? \数据块副本_3_q  : 32'bz;  // Controlled_Buffer controlled_buffer_3
  assign SlotData3 = L3 ? \数据块副本_4_q  : 32'bz;  // Controlled_Buffer controlled_buffer_4
  assign SlotData4 = L4 ? \数据块副本_5_q  : 32'bz;  // Controlled_Buffer controlled_buffer_5
  assign SlotData5 = L5 ? \数据块副本_6_q  : 32'bz;  // Controlled_Buffer controlled_buffer_6
  assign SlotData6 = L6 ? \数据块副本_7_q  : 32'bz;  // Controlled_Buffer controlled_buffer_7
  assign SlotData7 = L7 ? \数据块副本_8_q  : 32'bz;  // Controlled_Buffer controlled_buffer_8
  Multiplexer #(.select(3), .width(32), .enable("false")) multiplexer_2 (
    .in0(SlotData0), .in1(SlotData1), .in2(SlotData2), .in3(SlotData3), .in4(SlotData4), .in5(SlotData5),
    .in6(SlotData6), .in7(SlotData7), .out(JMPaddr), .sel(Select));
  and and_26 (and_26_out, UpdateStat, Up0);
  or or_1 (or_1_out, and_26_out, R0);
  and and_27 (and_27_out, UpdateStat, Up1);
  or or_2 (or_2_out, and_27_out, R1);
  and and_28 (and_28_out, UpdateStat, Up2);
  or or_3 (or_3_out, and_28_out, R2);
  and and_29 (and_29_out, UpdateStat, Up3);
  or or_4 (or_4_out, and_29_out, R3);
  and and_30 (and_30_out, UpdateStat, Up4);
  or or_5 (or_5_out, and_30_out, R4);
  and and_31 (and_31_out, UpdateStat, Up5);
  or or_6 (or_6_out, and_31_out, R5);
  and and_32 (and_32_out, UpdateStat, Up6);
  or or_7 (or_7_out, and_32_out, R6);
  and and_33 (and_33_out, UpdateStat, Up7);
  or or_8 (or_8_out, and_33_out, R7);
  Register #(.width(2)) \u_分支预测状态  (.D(JMPStatusIn), .en(or_1_out), .Q(\分支预测状态_q ), .clk(CLK));  // open: clr
  assign StatData0 = L0 ? \分支预测状态_q  : 2'bz;  // Controlled_Buffer controlled_buffer_9
  Register #(.width(2)) \u_分支预测状态_2  (.D(JMPStatusIn), .en(or_2_out), .Q(\分支预测状态_2_q ), .clk(CLK));  // open: clr
  assign StatData1 = L1 ? \分支预测状态_2_q  : 2'bz;  // Controlled_Buffer controlled_buffer_10
  Register #(.width(2)) \u_分支预测状态_3  (.D(JMPStatusIn), .en(or_3_out), .Q(\分支预测状态_3_q ), .clk(CLK));  // open: clr
  assign StatData2 = L2 ? \分支预测状态_3_q  : 2'bz;  // Controlled_Buffer controlled_buffer_11
  assign StatData3 = L3 ? \分支预测状态_4_q  : 2'bz;  // Controlled_Buffer controlled_buffer_12
  Register #(.width(2)) \u_分支预测状态_4  (.D(JMPStatusIn), .en(or_4_out), .Q(\分支预测状态_4_q ), .clk(CLK));  // open: clr
  Register #(.width(2)) \u_分支预测状态_5  (.D(JMPStatusIn), .en(or_5_out), .Q(\分支预测状态_5_q ), .clk(CLK));  // open: clr
  assign StatData4 = L4 ? \分支预测状态_5_q  : 2'bz;  // Controlled_Buffer controlled_buffer_13
  Register #(.width(2)) \u_分支预测状态_6  (.D(JMPStatusIn), .en(or_6_out), .Q(\分支预测状态_6_q ), .clk(CLK));  // open: clr
  assign StatData5 = L5 ? \分支预测状态_6_q  : 2'bz;  // Controlled_Buffer controlled_buffer_14
  Register #(.width(2)) \u_分支预测状态_7  (.D(JMPStatusIn), .en(or_7_out), .Q(\分支预测状态_7_q ), .clk(CLK));  // open: clr
  assign StatData6 = L6 ? \分支预测状态_7_q  : 2'bz;  // Controlled_Buffer controlled_buffer_15
  assign StatData7 = L7 ? \分支预测状态_8_q  : 2'bz;  // Controlled_Buffer controlled_buffer_16
  Register #(.width(2)) \u_分支预测状态_8  (.D(JMPStatusIn), .en(or_8_out), .Q(\分支预测状态_8_q ), .clk(CLK));  // open: clr
  Multiplexer #(.select(3), .width(2), .enable("false")) multiplexer_3 (
    .in0(StatData0), .in1(StatData1), .in2(StatData2), .in3(StatData3), .in4(StatData4), .in5(StatData5),
    .in6(StatData6), .in7(StatData7), .out(JMPStatus), .sel(Select));

  // Other names for the same wires on the sheet: Blk[31:0] = BlockDataIn; BlkReady = BlkDataReady;
  //   DataOut1[31:0] = JMPaddr; DataOut2[1:0] = JMPStatus; Stat[1:0] = JMPStatusIn; Tag[31:0] = Addr1;
  //   Upstat[31:0] = Addr2

  // Notes on the sheet:
  //   输入引脚区
  //   请勿增改引脚，请勿修改子电路封装
  //   电路功能：利用上面给定的隧道构建8行的Cache，cache映射方式自选
  //   Tag命中比较
  //   LRU替换算法
  //   输出引脚区
  //   请在下方利用上方输入输出引脚的隧道信号构建电路，ctrl+d复制选择部件
  //   执行预测
  //   选择信号
  //   Cache槽实现
  //   选择输出结果
endmodule

// Max3
module Max3 (
  input  [15:0] Y,
  input  [15:0] X,
  input  [2:0] Y_num,
  input  [2:0] X_num,
  output [15:0] MAX,
  output [2:0] Max_num
);

  wire comparator_1_eq, comparator_1_gt, or_1_out;

  Multiplexer #(.width(16), .enable("false")) multiplexer_1 (.in0(Y), .in1(X), .out(MAX), .sel(or_1_out));
  Comparator #(.width(16), .mode("unsigned")) comparator_1 (
    .a(X), .b(Y), .gt(comparator_1_gt), .eq(comparator_1_eq));  // open: lt
  or or_1 (or_1_out, comparator_1_gt, comparator_1_eq);
  Multiplexer #(.width(3), .enable("false")) multiplexer_2 (.in0(Y_num), .in1(X_num), .out(Max_num), .sel(or_1_out));

  // Notes on the sheet:
  //   输出两个输入中的较大值，并输出较大值的3位编号
endmodule

module \分支预测状态转换  (
  input  bench,
  input  Status_in1,
  input  Status_in0,
  input  [31:0] Pre_addr,
  input  [31:0] Addr_in0,
  output Status_out1,
  output Status_out0,
  output Wrong,
  output [31:0] Addr_out
);

  wire and_1_out, and_2_out, and_3_out, and_4_out, and_5_out, and_6_out, and_7_out, comparator_1_eq,
       not_1_out, not_2_out, not_3_out, not_4_out, not_5_out, not_6_out, not_7_out, not_8_out;

  not not_1 (not_1_out, Status_in0);
  not not_2 (not_2_out, bench);
  not not_3 (not_3_out, Status_in0);
  not not_4 (not_4_out, Status_in1);
  not not_5 (not_5_out, Status_in0);
  not not_6 (not_6_out, bench);
  not not_7 (not_7_out, Status_in1);
  not not_8 (not_8_out, comparator_1_eq);
  Comparator #(.width(32)) comparator_1 (.a(Pre_addr), .b(Addr_in0), .eq(comparator_1_eq));  // open: gt, lt
  and and_1 (and_1_out, Status_in1, not_1_out);
  and and_2 (and_2_out, bench, Status_in0);
  and and_3 (and_3_out, not_2_out, Status_in1, not_3_out);
  and and_4 (and_4_out, bench, not_4_out, not_5_out);
  and and_5 (and_5_out, not_6_out, Status_in1);
  and and_6 (and_6_out, bench, not_7_out);
  and and_7 (and_7_out, bench, not_8_out);
  or or_1 (Status_out1, and_1_out, and_2_out);
  or or_2 (Status_out0, and_3_out, and_4_out);
  or or_3 (Wrong, and_5_out, and_6_out, and_7_out);
  Multiplexer #(.width(32), .enable("false")) multiplexer_1 (
    .in0(Pre_addr), .in1(Addr_in0), .out(Addr_out), .sel(Wrong));
endmodule

// Bench
module \可计算出地址的跳转指令判断  (
  input  [31:0] Instruction,
  input  [31:0] PC,
  output J,
  output [31:0] JMPPC
);

  wire and_1_out, not_1_out, or_1_out, \硬布线控制器_1_beq , \硬布线控制器_1_bne , \硬布线控制器_1_jmp , \硬布线控制器_1_jr ;
  wire [31:0] adder_1_out, adder_2_out, bit_extender_1_out, bit_extender_2_out, shifter_1_out, shifter_2_out;

  and and_1 (and_1_out, \硬布线控制器_1_jmp , not_1_out);
  not not_1 (not_1_out, \硬布线控制器_1_jr );
  \硬布线控制器  \u_硬布线控制器_1  (
    .Func(Instruction[5:0]), .OP(Instruction[31:26]), .JR(\硬布线控制器_1_jr ), .JMP(\硬布线控制器_1_jmp ),
    .Beq(\硬布线控制器_1_beq ), .Bne(\硬布线控制器_1_bne ));  // open: ALU_OP, MemToReg, MemWrite, ALU_SRC, RegWrite, SysCALL, SignedExt, RegDst, JAL, SH, BLTZ, ERET, MF, MFC0, MTC0
  assign bit_extender_1_out = {{6{Instruction[25]}}, Instruction[25:0]};  // Bit_Extender bit_extender_1
  assign bit_extender_2_out = {{16{Instruction[15]}}, Instruction[15:0]};  // Bit_Extender bit_extender_2
  Adder #(.width(32)) adder_1 (.a(PC), .b(32'h4), .out(adder_1_out));  // open: cin, cout
  or or_1 (or_1_out, \硬布线控制器_1_beq , \硬布线控制器_1_bne );
  Shifter #(.width(32)) shifter_1 (.in(bit_extender_1_out), .\dist (5'b00010), .out(shifter_1_out));
  Shifter #(.width(32)) shifter_2 (.in(bit_extender_2_out), .\dist (5'b00010), .out(shifter_2_out));
  or or_2 (J, and_1_out, or_1_out);
  Adder #(.width(32)) adder_2 (.a(shifter_2_out), .b(adder_1_out), .out(adder_2_out));  // open: cin, cout
  Multiplexer #(.width(32), .enable("false")) multiplexer_1 (
    .in0(shifter_1_out), .in1(adder_2_out), .out(JMPPC), .sel(or_1_out));

  // Notes on the sheet:
  //   JMP
  //   JR
  //   OP
  //   Func
endmodule

module \单级中断  (
);

  wire and_1_out, and_2_out, and_3_out, and_4_out, and_5_out, and_7_out, and_11_out, and_12_out, Bench, BLTZ,
       CLK, comparator_1_lt, d_ff_1_q, d_ff_2_q, d_ff_3_q, decoder_1_out1, decoder_1_out2, decoder_1_out3,
       Do, Do1, Do2, Do3, Enable, ERET, Go, heigh, IE_q, IR, IR1, IR2, IR3, JMP, mips_alu_1_equal, not_1_out,
       not_3_out, not_4_out, or_5_out, or_6_out, or_7_out, or_8_out, or_9_out, or_10_out, register_1_q, RST,
       rst1, rst2, rst3, SH, Show, SignedExt, W1, W2, W3, \硬布线控制器_1_alu_src , \硬布线控制器_1_beq , \硬布线控制器_1_bne ,
       \硬布线控制器_1_jal , \硬布线控制器_1_jr , \硬布线控制器_1_memtoreg , \硬布线控制器_1_memwrite , \硬布线控制器_1_regdst ,
       \硬布线控制器_1_regwrite , \硬布线控制器_1_syscall ;
  wire [1:0] priority_encoder_1_out, \中断号_q ;
  wire [3:0] multiplexer_17_out, multiplexer_18_out, \硬布线控制器_1_alu_op ;
  wire [4:0] multiplexer_7_out, multiplexer_8_out, multiplexer_9_out, multiplexer_11_out, rom_1_data_2;
  wire [11:0] EX_PC, ID_PC, IF_PC, MEM_PC, WB_PC;
  wire [15:0] \LoadUse次数 , \总周期数 , \插入气泡数 , \无条件分支数 , \条件分支成功数 ;
  wire [31:0] adder_1_out, adder_2_out, bit_extender_1_out, bit_extender_2_out, bit_extender_3_out, EPC,
       LedData, mips_alu_1_result, mips_ram_1_p8, mips_regifile_1_r1, mips_regifile_1_r2, multiplexer_1_out,
       multiplexer_2_out, multiplexer_3_out, multiplexer_4_out, multiplexer_5_out, multiplexer_6_out,
       multiplexer_12_out, multiplexer_13_out, multiplexer_14_out, multiplexer_15_out, multiplexer_16_out,
       multiplexer_19_out, PC, rom_1_data, shifter_1_out, shifter_2_out, \中断程序入口地址 ;

  Button \u_总复位  (.out(RST));
  Button _1 (.out(IR1));
  Button _2 (.out(IR2));
  Button _3 (.out(IR3));
  Button \u_继续运行  (.out(Go));
  LED led_1 (.in(W1));
  LED led_2 (.in(W2));
  LED led_3 (.in(W3));
  Comparator #(.width(32)) comparator_1 (.a(mips_regifile_1_r1), .b({32{1'b0}}), .lt(comparator_1_lt));  // open: gt, eq
  or or_1 (Bench, or_10_out, and_1_out);
  Multiplexer #(.width(32), .enable("false")) multiplexer_1 (
    .in0(adder_1_out), .in1(adder_2_out), .out(multiplexer_1_out), .sel(or_10_out));
  or or_2 (W1, Do1, d_ff_1_q);
  or or_3 (W2, Do2, d_ff_2_q);
  or or_4 (W3, Do3, d_ff_3_q);
  Hex_Digit_Display hex_digit_display_1 (.value(LedData[31:28]));  // open: dp
  and and_1 (and_1_out, comparator_1_lt, BLTZ);
  Multiplexer #(.width(32), .enable("false")) multiplexer_2 (
    .in0(multiplexer_1_out), .in1(adder_2_out), .out(multiplexer_2_out), .sel(and_1_out));
  D_Flip_Flop d_ff_1 (.clk(IR1), .D(1'b1), .Q(d_ff_1_q), .reset(Do1));  // open: Qn, preset, en
  D_Flip_Flop d_ff_2 (.clk(IR2), .D(1'b1), .Q(d_ff_2_q), .reset(Do2));  // open: Qn, preset, en
  D_Flip_Flop d_ff_3 (.clk(IR3), .D(1'b1), .Q(d_ff_3_q), .reset(Do3));  // open: Qn, preset, en
  Hex_Digit_Display hex_digit_display_2 (.value(LedData[23:20]));  // open: dp
  Hex_Digit_Display hex_digit_display_3 (.value(LedData[27:24]));  // open: dp
  Multiplexer #(.width(32), .enable("false")) multiplexer_3 (
    .in0(multiplexer_2_out), .in1(multiplexer_6_out), .out(multiplexer_3_out), .sel(JMP));
  Multiplexer #(.width(32), .enable("false")) multiplexer_4 (
    .in0(multiplexer_3_out), .in1(\中断程序入口地址 ), .out(multiplexer_4_out), .sel(IR));
  or or_5 (or_5_out, d_ff_1_q, Do1);
  or or_6 (or_6_out, d_ff_2_q, Do2);
  or or_7 (or_7_out, d_ff_3_q, Do3);
  Hex_Digit_Display hex_digit_display_4 (.value(LedData[19:16]));  // open: dp
  Hex_Digit_Display hex_digit_display_5 (.value(LedData[15:12]));  // open: dp
  not not_1 (not_1_out, Show);
  Multiplexer #(.width(32), .enable("false")) multiplexer_5 (
    .in0(multiplexer_4_out), .in1(EPC), .out(multiplexer_5_out), .sel(ERET));
  Multiplexer #(.width(32), .enable("false")) multiplexer_6 (
    .in0(shifter_2_out), .in1(mips_regifile_1_r1), .out(multiplexer_6_out), .sel(\硬布线控制器_1_jr ));
  and and_2 (and_2_out, or_5_out, ~rst1);  // AND_Gate
  and and_3 (and_3_out, or_6_out, ~rst2);  // AND_Gate
  and and_4 (and_4_out, or_7_out, ~rst3);  // AND_Gate
  Hex_Digit_Display hex_digit_display_6 (.value(LedData[11:8]));  // open: dp
  Hex_Digit_Display hex_digit_display_7 (.value(LedData[7:4]));  // open: dp
  Clock clock_1 (.out(CLK));
  and and_5 (and_5_out, not_1_out, \硬布线控制器_1_syscall );
  D_Flip_Flop u_IR1 (.clk(CLK), .D(and_2_out), .Q(Do1));  // open: Qn, preset, en, reset
  D_Flip_Flop u_IR2 (.clk(CLK), .D(and_3_out), .Q(Do2));  // open: Qn, preset, en, reset
  D_Flip_Flop u_IR3 (.clk(CLK), .D(and_4_out), .Q(Do3));  // open: Qn, preset, en, reset
  Hex_Digit_Display hex_digit_display_8 (.value(LedData[3:0]));  // open: dp
  not not_2 (Enable, register_1_q);
  Register #(.width(1)) register_1 (
    .D(\硬布线控制器_1_syscall ), .en(and_5_out), .Q(register_1_q), .clk(CLK), .clr(or_8_out));
  or or_8 (or_8_out, Go, RST);
  Register #(.width(32)) u_PC (.D(multiplexer_5_out), .en(Enable), .Q(PC), .clk(CLK), .clr(RST));
  // Probe on \总周期数 
  // Probe on \无条件分支数 
  // Probe on \条件分支成功数 
  // Probe on \插入气泡数 
  // Probe on \LoadUse次数 
  ROM #(.addrWidth(10), .dataWidth(32)) rom_1 (
    .addr(PC[11:2]), .data({rom_1_data[31:11], rom_1_data_2, rom_1_data[5:0]}));  // open: sel
  Adder #(.width(32)) adder_1 (.a(PC), .b(32'h4), .out(adder_1_out));  // open: cin, cout
  // Probe on IF_PC
  Priority_Encoder #(.select(2)) priority_encoder_1 (
    .in0(1'b0), .in1(Do1), .in2(Do2), .in3(Do3), .out(priority_encoder_1_out), .gs(Do));  // open: en_out, en_in
  // Probe on ID_PC
  \硬布线控制器  \u_硬布线控制器_1  (
    .Func(rom_1_data[5:0]), .OP(rom_1_data[31:26]), .ALU_OP(\硬布线控制器_1_alu_op ),
    .MemToReg(\硬布线控制器_1_memtoreg ), .MemWrite(\硬布线控制器_1_memwrite ), .ALU_SRC(\硬布线控制器_1_alu_src ),
    .RegWrite(\硬布线控制器_1_regwrite ), .SysCALL(\硬布线控制器_1_syscall ), .SignedExt(SignedExt),
    .RegDst(\硬布线控制器_1_regdst ), .JR(\硬布线控制器_1_jr ), .JMP(JMP), .Beq(\硬布线控制器_1_beq ), .JAL(\硬布线控制器_1_jal ),
    .Bne(\硬布线控制器_1_bne ), .SH(SH), .BLTZ(BLTZ), .ERET(ERET));  // open: MF, MFC0, MTC0
  or or_9 (or_9_out, IR, ERET);
  // Probe on EX_PC
  // Probe on MEM_PC
  Multiplexer #(.width(5), .enable("false")) multiplexer_7 (
    .in0(rom_1_data[25:21]), .in1(5'b00100), .out(multiplexer_7_out), .sel(\硬布线控制器_1_syscall ));
  Multiplexer #(.width(5), .enable("false")) multiplexer_8 (
    .in0(rom_1_data[20:16]), .in1(rom_1_data[15:11]), .out(multiplexer_8_out), .sel(\硬布线控制器_1_regdst ));
  Multiplexer #(.width(5), .enable("false")) multiplexer_9 (
    .in0(multiplexer_8_out), .in1({5{1'b1}}), .out(multiplexer_9_out), .sel(\硬布线控制器_1_jal ));
  Register #(.width(32)) u_EPC (.D(PC), .en(IR), .Q(EPC), .clk(CLK));  // open: clr
  Register #(.width(1)) IE (.D(IR), .en(or_9_out), .Q(IE_q), .clk(CLK));  // open: clr
  Multiplexer #(.select(2), .width(32), .enable("false")) multiplexer_10 (
    .in1(32'h4), .in2(32'h1c8), .in3(32'h38c), .out(\中断程序入口地址 ), .sel(priority_encoder_1_out));  // open: in0
  // Probe on WB_PC
  Multiplexer #(.width(5), .enable("false")) multiplexer_11 (
    .in0(rom_1_data[20:16]), .in1(5'b00010), .out(multiplexer_11_out), .sel(\硬布线控制器_1_syscall ));
  Multiplexer #(.width(32), .enable("false")) multiplexer_12 (
    .in0(multiplexer_19_out), .in1(adder_1_out), .out(multiplexer_12_out), .sel(\硬布线控制器_1_jal ));
  not not_3 (not_3_out, IE_q);
  and and_6 (IR, not_3_out, Do);
  assign bit_extender_1_out = {{16{1'b0}}, {rom_1_data[15:11], rom_1_data_2, rom_1_data[5:0]}};  // Bit_Extender bit_extender_1
  assign bit_extender_2_out = {{16{rom_1_data[15]}}, {rom_1_data[15:11], rom_1_data_2, rom_1_data[5:0]}};  // Bit_Extender bit_extender_2
  assign bit_extender_3_out = {{6{rom_1_data[25]}}, {rom_1_data[25:11], rom_1_data_2, rom_1_data[5:0]}};  // Bit_Extender bit_extender_3
  Register #(.width(2)) \u_中断号  (.D(priority_encoder_1_out), .en(IR), .Q(\中断号_q ), .clk(CLK));  // open: clr
  Counter #(.width(16), .max('hffff)) counter_1 (
    .count(Enable), .Q(\总周期数 ), .clk(CLK), .clr(RST));  // open: load, D, carry
  and and_7 (and_7_out, Show, \硬布线控制器_1_syscall );
  MIPS_Regifile mips_regifile_1 (
    .Din(multiplexer_12_out), .Clk(CLK), .R1(mips_regifile_1_r1), .R2(mips_regifile_1_r2),
    .WE(\硬布线控制器_1_regwrite ), .W_num(multiplexer_9_out), .R1_num(multiplexer_7_out),
    .R2_num(multiplexer_11_out));
  Multiplexer #(.width(32), .enable("false")) multiplexer_13 (
    .in0(bit_extender_1_out), .in1(bit_extender_2_out), .out(multiplexer_13_out), .sel(SignedExt));
  Decoder #(.select(2), .enable("false")) decoder_1 (
    .out1(decoder_1_out1), .out2(decoder_1_out2), .out3(decoder_1_out3), .sel(\中断号_q ));  // open: out0
  Register #(.width(32)) register_2 (.D(mips_regifile_1_r1), .en(and_7_out), .Q(LedData), .clk(CLK), .clr(RST));
  Comparator #(.width(32)) comparator_2 (.a(32'h22), .b(mips_regifile_1_r2), .eq(Show));  // open: gt, lt
  and and_8 (rst1, decoder_1_out1, ERET);
  and and_9 (rst2, decoder_1_out2, ERET);
  and and_10 (rst3, decoder_1_out3, ERET);
  Multiplexer #(.width(32), .enable("false")) multiplexer_14 (
    .in0(mips_regifile_1_r2), .in1(multiplexer_13_out), .out(multiplexer_14_out), .sel(\硬布线控制器_1_alu_src ));
  Shifter #(.width(32)) shifter_1 (.in(multiplexer_13_out), .\dist (5'b00010), .out(shifter_1_out));
  Shifter #(.width(32)) shifter_2 (.in(bit_extender_3_out), .\dist (5'b00010), .out(shifter_2_out));
  Counter #(.width(16), .max('hffff)) counter_2 (
    .count(JMP), .Q(\无条件分支数 ), .clk(CLK), .clr(RST));  // open: load, D, carry
  MIPS_ALU mips_alu_1 (
    .X(mips_regifile_1_r1), .Y(multiplexer_14_out), .AluOP(\硬布线控制器_1_alu_op ), .Equal(mips_alu_1_equal),
    .Result({mips_alu_1_result[31:2], heigh, mips_alu_1_result[0]}), .shamt(rom_1_data_2));  // open: Result_2
  not not_4 (not_4_out, mips_alu_1_equal);
  Multiplexer #(.width(32), .enable("false")) multiplexer_15 (
    .in0(mips_regifile_1_r2), .in1(multiplexer_16_out), .out(multiplexer_15_out), .sel(SH));
  Multiplexer #(.width(32), .enable("false")) multiplexer_16 (
    .in0({{16{1'b0}}, mips_regifile_1_r2[15:0]}), .in1({mips_regifile_1_r2[15:0], {16{1'b0}}}),
    .out(multiplexer_16_out), .sel(heigh));
  Adder #(.width(32)) adder_2 (.a(shifter_1_out), .b(adder_1_out), .out(adder_2_out));  // open: cin, cout
  and and_11 (and_11_out, \硬布线控制器_1_beq , mips_alu_1_equal);
  or or_10 (or_10_out, and_11_out, and_12_out);
  and and_12 (and_12_out, \硬布线控制器_1_bne , not_4_out);
  Multiplexer #(.width(4), .enable("false")) multiplexer_17 (
    .in0(4'b1111), .in1(multiplexer_18_out), .out(multiplexer_17_out), .sel(SH));
  Counter #(.width(16), .max('hffff)) counter_3 (
    .count(Bench), .Q(\条件分支成功数 ), .clk(CLK), .clr(RST));  // open: load, D, carry
  Multiplexer #(.width(4), .enable("false")) multiplexer_18 (
    .in0(4'b0011), .in1(4'b1100), .out(multiplexer_18_out), .sel(heigh));
  Multiplexer #(.width(32), .enable("false")) multiplexer_19 (
    .in0({mips_alu_1_result[31:2], heigh, mips_alu_1_result[0]}), .in1(mips_ram_1_p8),
    .out(multiplexer_19_out), .sel(\硬布线控制器_1_memtoreg ));
  // MIPS_RAM mips_ram_1: pin names not known; wires that end beside it: mips_alu_1_result[11:2], multiplexer_15_out, \硬布线控制器_1_memwrite , multiplexer_17_out, CLK, 1'b1, RST, mips_ram_1_p8

  // Notes on the sheet:
  //   中断源
  //   中断等待指示
  //   中断按键信号产生
  //   数码管输出
  //   Reset 
  //   Reset 
  //   Reset 
  //   指令存储器
  //   指令字
  //   contents of rom_1 (hex, n*v repeats v):
  //   8000d54 23bdfffc afa10000 23bdfffc afa20000 23bdfffc afa30000 23bdfffc afa40000 23bdfffc afa50000
  //   23bdfffc afa60000 23bdfffc afa70000 23bdfffc afa80000 23bdfffc afa90000 23bdfffc afaa0000 23bdfffc
  //   afab0000 23bdfffc afac0000 23bdfffc afad0000 23bdfffc afae0000 23bdfffc afaf0000 23bdfffc afb00000
  //   23bdfffc afb10000 23bdfffc afb20000 23bdfffc afb30000 23bdfffc afb40000 23bdfffc afb50000 23bdfffc
  //   afb60000 23bdfffc afb70000 23bdfffc afb80000 23bdfffc afb90000 20160001 20140006 20150001 168020
  //   108100 2149825 132020 20020022 c 1600fffa 295a022 1680fff7 8fb90000 23bd0004 8fb80000 23bd0004
  //   8fb70000 23bd0004 8fb60000 23bd0004 8fb50000 23bd0004 8fb40000 23bd0004 8fb30000 23bd0004 8fb20000
  //   23bd0004 8fb10000 23bd0004 8fb00000 23bd0004 8faf0000 23bd0004 8fae0000 23bd0004 8fad0000 23bd0004
  //   8fac0000 23bd0004 8fab0000 23bd0004 8faa0000 23bd0004 8fa90000 23bd0004 8fa80000 23bd0004 8fa70000
  //   23bd0004 8fa60000 23bd0004 8fa50000 23bd0004 8fa40000 23bd0004 8fa30000 23bd0004 8fa20000 23bd0004
  //   8fa10000 23bd0004 42000018 23bdfffc afa10000 23bdfffc afa20000 23bdfffc afa30000 23bdfffc afa40000
  //   23bdfffc afa50000 23bdfffc afa60000 23bdfffc afa70000 23bdfffc afa80000 23bdfffc afa90000 23bdfffc
  //   afaa0000 23bdfffc afab0000 23bdfffc afac0000 23bdfffc afad0000 23bdfffc afae0000 23bdfffc afaf0000
  //   23bdfffc afb00000 23bdfffc afb10000 23bdfffc afb20000 23bdfffc afb30000 23bdfffc afb40000 23bdfffc
  //   afb50000 23bdfffc afb60000 23bdfffc afb70000 23bdfffc afb80000 23bdfffc afb90000 20160002 20140006
  //   20150001 168020 108100 2149825 132020 20020022 c 1600fffa 295a022 1680fff7 8fb90000 23bd0004
  //   8fb80000 23bd0004 8fb70000 23bd0004 8fb60000 23bd0004 8fb50000 23bd0004 8fb40000 23bd0004 8fb30000
  //   23bd0004 8fb20000 23bd0004 8fb10000 23bd0004 8fb00000 23bd0004 8faf0000 23bd0004 8fae0000 23bd0004
  //   8fad0000 23bd0004 8fac0000 23bd0004 8fab0000 23bd0004 8faa0000 23bd0004 8fa90000 23bd0004 8fa80000
  //   23bd0004 8fa70000 23bd0004 8fa60000 23bd0004 8fa50000 23bd0004 8fa40000 23bd0004 8fa30000 23bd0004
  //   8fa20000 23bd0004 8fa10000 23bd0004 42000018 23bdfffc afa10000 23bdfffc afa20000 23bdfffc afa30000
  //   23bdfffc afa40000 23bdfffc afa50000 23bdfffc afa60000 23bdfffc afa70000 23bdfffc afa80000 23bdfffc
  //   afa90000 23bdfffc afaa0000 23bdfffc afab0000 23bdfffc afac0000 23bdfffc afad0000 23bdfffc afae0000
  //   23bdfffc afaf0000 23bdfffc afb00000 23bdfffc afb10000 23bdfffc afb20000 23bdfffc afb30000 23bdfffc
  //   afb40000 23bdfffc afb50000 23bdfffc afb60000 23bdfffc afb70000 23bdfffc afb80000 23bdfffc afb90000
  //   20160003 20140006 20150001 168020 108100 2149825 132020 20020022 c 1600fffa 295a022 1680fff7
  //   8fb90000 23bd0004 8fb80000 23bd0004 8fb70000 23bd0004 8fb60000 23bd0004 8fb50000 23bd0004 8fb40000
  //   23bd0004 8fb30000 23bd0004 8fb20000 23bd0004 8fb10000 23bd0004 8fb00000 23bd0004 8faf0000 23bd0004
  //   8fae0000 23bd0004 8fad0000 23bd0004 8fac0000 23bd0004 8fab0000 23bd0004 8faa0000 23bd0004 8fa90000
  //   23bd0004 8fa80000 23bd0004 8fa70000 23bd0004 8fa60000 23bd0004 8fa50000 23bd0004 8fa40000 23bd0004
  //   8fa30000 23bd0004 8fa20000 23bd0004 8fa10000 23bd0004 42000018 20110200 20020022 112020 c 2231ffff
  //   1620fffc 20020032 c 2002000a c
  //   JMP
  //   JR
  //   OP
  //   OP
  //   Func
  //   Func
  //   rs
  //   rt
  //   rd
  //   Beq
  //   Bne
  //   MemToReg
  //   MemWrite
  //   AluOP
  //   AluSrcB
  //   RegWrite
  //   JAL
  //   RegDst
  //   Syscall
  //   流水调试日志用
  //   COP0模拟
  //   中断服务程序进入和返回处理
  //   周期数计算
endmodule

module \多级中断  (
);

  wire and_1_out, and_2_out, and_3_out, and_4_out, and_5_out, and_6_out, and_7_out, and_9_out, and_10_out,
       and_11_out, and_12_out, and_13_out, and_17_out, and_18_out, and_19_out, Bench, BLTZ, CLK,
       comparator_1_lt, comparator_2_eq, comparator_3_eq, comparator_4_eq, d_ff_1_q, d_ff_2_q, d_ff_3_q,
       d_ff_4_qn, d_ff_5_qn, d_ff_6_qn, d_ff_7_qn, decoder_1_out1, decoder_1_out2, decoder_1_out3, Do, Do1,
       Do2, Do3, Enable, ERET, Go, heigh, IE_q, IR, IR1, IR2, IR3, JMP, MFC0, mips_alu_1_equal, MTC0,
       multiplexer_6_out, multiplexer_9_out, multiplexer_10_out, multiplexer_11_out, multiplexer_12_out,
       not_1_out, not_2_out, not_3_out, not_5_out, not_6_out, not_7_out, or_5_out, or_6_out, or_7_out,
       or_8_out, or_9_out, or_10_out, or_11_out, register_1_q, RST, rst1, rst2, rst3, SH, Show, SignedExt,
       W1, W2, W3, \硬布线控制器_1_alu_src , \硬布线控制器_1_beq , \硬布线控制器_1_bne , \硬布线控制器_1_jal , \硬布线控制器_1_jr ,
       \硬布线控制器_1_memtoreg , \硬布线控制器_1_memwrite , \硬布线控制器_1_regdst , \硬布线控制器_1_regwrite , \硬布线控制器_1_syscall ;
  wire [1:0] priority_encoder_1_out, priority_encoder_2_out;
  wire [3:0] multiplexer_26_out, multiplexer_27_out, \中断屏蔽字 , \硬布线控制器_1_alu_op ;
  wire [4:0] multiplexer_13_out, multiplexer_14_out, multiplexer_15_out, multiplexer_17_out, rd,
       rom_1_data_2, rt;
  wire [11:0] EX_PC, ID_PC, IF_PC, MEM_PC, WB_PC;
  wire [15:0] \LoadUse次数 , \总周期数 , \插入气泡数 , \无条件分支数 , \条件分支成功数 ;
  wire [31:0] adder_1_out, adder_2_out, bit_extender_1_out, bit_extender_2_out, bit_extender_3_out, EPC,
       EPC_out, IE_out, LedData, MFC0Data, mips_alu_1_result, mips_ram_1_p8, mips_regifile_1_r1,
       mips_regifile_1_r2, MTC0Data, multiplexer_1_out, multiplexer_2_out, multiplexer_3_out,
       multiplexer_4_out, multiplexer_5_out, multiplexer_7_out, multiplexer_8_out, multiplexer_18_out,
       multiplexer_19_out, multiplexer_20_out, multiplexer_23_out, multiplexer_24_out, multiplexer_25_out,
       multiplexer_28_out, PC, rom_1_data, shifter_1_out, shifter_2_out, \中断屏蔽字_out , \中断程序入口地址 ;

  Button \u_总复位  (.out(RST));
  Button _1 (.out(IR1));
  Button _2 (.out(IR2));
  Button _3 (.out(IR3));
  Button \u_继续运行  (.out(Go));
  LED led_1 (.in(W1));
  LED led_2 (.in(W2));
  LED led_3 (.in(W3));
  Comparator #(.width(32)) comparator_1 (.a(mips_regifile_1_r1), .b({32{1'b0}}), .lt(comparator_1_lt));  // open: gt, eq
  or or_1 (Bench, or_11_out, and_1_out);
  Multiplexer #(.width(32), .enable("false")) multiplexer_1 (
    .in0(adder_1_out), .in1(adder_2_out), .out(multiplexer_1_out), .sel(or_11_out));
  or or_2 (W1, Do1, d_ff_1_q);
  or or_3 (W2, Do2, d_ff_2_q);
  or or_4 (W3, Do3, d_ff_3_q);
  Hex_Digit_Display hex_digit_display_1 (.value(LedData[31:28]));  // open: dp
  and and_1 (and_1_out, comparator_1_lt, BLTZ);
  Multiplexer #(.width(32), .enable("false")) multiplexer_2 (
    .in0(multiplexer_1_out), .in1(adder_2_out), .out(multiplexer_2_out), .sel(and_1_out));
  D_Flip_Flop d_ff_1 (.clk(IR1), .D(1'b1), .Q(d_ff_1_q), .reset(Do1));  // open: Qn, preset, en
  D_Flip_Flop d_ff_2 (.clk(IR2), .D(1'b1), .Q(d_ff_2_q), .reset(Do2));  // open: Qn, preset, en
  D_Flip_Flop d_ff_3 (.clk(IR3), .D(1'b1), .Q(d_ff_3_q), .reset(Do3));  // open: Qn, preset, en
  Comparator #(.width(5)) comparator_2 (.a(rd), .b(5'b00010), .eq(comparator_2_eq));  // open: gt, lt
  not not_1 (not_1_out, IE_out[0]);
  Comparator #(.width(5)) comparator_3 (.a(rd), .b(5'b00011), .eq(comparator_3_eq));  // open: gt, lt
  and and_2 (and_2_out, comparator_3_eq, MTC0);
  Hex_Digit_Display hex_digit_display_2 (.value(LedData[23:20]));  // open: dp
  Hex_Digit_Display hex_digit_display_3 (.value(LedData[27:24]));  // open: dp
  Multiplexer #(.width(32), .enable("false")) multiplexer_3 (
    .in0(multiplexer_2_out), .in1(multiplexer_8_out), .out(multiplexer_3_out), .sel(JMP));
  Multiplexer #(.width(32), .enable("false")) multiplexer_4 (
    .in0(multiplexer_3_out), .in1(\中断程序入口地址 ), .out(multiplexer_4_out), .sel(IR));
  or or_5 (or_5_out, d_ff_1_q, Do1);
  or or_6 (or_6_out, d_ff_2_q, Do2);
  or or_7 (or_7_out, d_ff_3_q, Do3);
  and and_3 (and_3_out, MTC0, comparator_2_eq);
  Multiplexer #(.width(32), .enable("false")) multiplexer_5 (
    .in0(PC), .in1(EPC_out), .out(multiplexer_5_out), .sel(and_3_out));
  or or_8 (or_8_out, IR, and_3_out);
  Multiplexer #(.enable("false")) multiplexer_6 (.in0(IR), .in1(not_1_out), .out(multiplexer_6_out), .sel(and_2_out));
  or or_9 (or_9_out, IR, and_2_out, ERET);
  Hex_Digit_Display hex_digit_display_4 (.value(LedData[19:16]));  // open: dp
  Hex_Digit_Display hex_digit_display_5 (.value(LedData[15:12]));  // open: dp
  not not_2 (not_2_out, Show);
  Multiplexer #(.width(32), .enable("false")) multiplexer_7 (
    .in0(multiplexer_4_out), .in1(EPC), .out(multiplexer_7_out), .sel(ERET));
  Multiplexer #(.width(32), .enable("false")) multiplexer_8 (
    .in0(shifter_2_out), .in1(mips_regifile_1_r1), .out(multiplexer_8_out), .sel(\硬布线控制器_1_jr ));
  and and_4 (and_4_out, or_5_out, ~rst1);  // AND_Gate
  and and_5 (and_5_out, or_6_out, ~rst2);  // AND_Gate
  and and_6 (and_6_out, or_7_out, ~rst3);  // AND_Gate
  Register #(.width(32)) u_EPC (.D(multiplexer_5_out), .en(or_8_out), .Q(EPC), .clk(CLK));  // open: clr
  Register #(.width(1)) IE (.D(multiplexer_6_out), .en(or_9_out), .Q(IE_q), .clk(CLK));  // open: clr
  Hex_Digit_Display hex_digit_display_6 (.value(LedData[11:8]));  // open: dp
  Hex_Digit_Display hex_digit_display_7 (.value(LedData[7:4]));  // open: dp
  Clock clock_1 (.out(CLK));
  and and_7 (and_7_out, not_2_out, \硬布线控制器_1_syscall );
  D_Flip_Flop u_IR1 (.clk(CLK), .D(and_4_out), .Q(Do1));  // open: Qn, preset, en, reset
  D_Flip_Flop u_IR2 (.clk(CLK), .D(and_5_out), .Q(Do2));  // open: Qn, preset, en, reset
  D_Flip_Flop u_IR3 (.clk(CLK), .D(and_6_out), .Q(Do3));  // open: Qn, preset, en, reset
  not not_3 (not_3_out, IE_q);
  and and_8 (IR, not_3_out, Do);
  Hex_Digit_Display hex_digit_display_8 (.value(LedData[3:0]));  // open: dp
  Register #(.width(1)) register_1 (
    .D(\硬布线控制器_1_syscall ), .en(and_7_out), .Q(register_1_q), .clk(CLK), .clr(or_10_out));
  not not_4 (Enable, register_1_q);
  or or_10 (or_10_out, Go, RST);
  Register #(.width(32)) u_PC (.D(multiplexer_7_out), .en(Enable), .Q(PC), .clk(CLK), .clr(RST));
  // Probe on \总周期数 
  // Probe on \无条件分支数 
  // Probe on \条件分支成功数 
  // Probe on \插入气泡数 
  // Probe on \LoadUse次数 
  ROM #(.addrWidth(10), .dataWidth(32)) rom_1 (
    .addr(PC[11:2]), .data({rom_1_data[31:21], rt, rd, rom_1_data_2, rom_1_data[5:0]}));  // open: sel
  Adder #(.width(32)) adder_1 (.a(PC), .b(32'h4), .out(adder_1_out));  // open: cin, cout
  Comparator #(.width(5)) comparator_4 (.a(rd), .b(5'b00001), .eq(comparator_4_eq));  // open: gt, lt
  // Probe on IF_PC
  and and_9 (and_9_out, MTC0, comparator_4_eq);
  // Probe on ID_PC
  \硬布线控制器  \u_硬布线控制器_1  (
    .Func(rom_1_data[5:0]), .OP(rom_1_data[31:26]), .ALU_OP(\硬布线控制器_1_alu_op ),
    .MemToReg(\硬布线控制器_1_memtoreg ), .MemWrite(\硬布线控制器_1_memwrite ), .ALU_SRC(\硬布线控制器_1_alu_src ),
    .RegWrite(\硬布线控制器_1_regwrite ), .SysCALL(\硬布线控制器_1_syscall ), .SignedExt(SignedExt),
    .RegDst(\硬布线控制器_1_regdst ), .JR(\硬布线控制器_1_jr ), .JMP(JMP), .Beq(\硬布线控制器_1_beq ), .JAL(\硬布线控制器_1_jal ),
    .Bne(\硬布线控制器_1_bne ), .SH(SH), .BLTZ(BLTZ), .ERET(ERET), .MF(rom_1_data[25:21]), .MFC0(MFC0), .MTC0(MTC0));
  Multiplexer #(.enable("false")) multiplexer_9 (
    .in0(1'b0), .in1(\中断屏蔽字_out [0]), .out(multiplexer_9_out), .sel(and_9_out));
  Multiplexer #(.enable("false")) multiplexer_10 (
    .in0(1'b0), .in1(\中断屏蔽字_out [1]), .out(multiplexer_10_out), .sel(and_9_out));
  Multiplexer #(.enable("false")) multiplexer_11 (
    .in0(1'b0), .in1(\中断屏蔽字_out [2]), .out(multiplexer_11_out), .sel(and_9_out));
  Multiplexer #(.enable("false")) multiplexer_12 (
    .in0(1'b0), .in1(\中断屏蔽字_out [3]), .out(multiplexer_12_out), .sel(and_9_out));
  // Probe on MEM_PC
  // Probe on EX_PC
  Multiplexer #(.width(5), .enable("false")) multiplexer_13 (
    .in0(rom_1_data[25:21]), .in1(5'b00100), .out(multiplexer_13_out), .sel(\硬布线控制器_1_syscall ));
  Multiplexer #(.width(5), .enable("false")) multiplexer_14 (
    .in0(rt), .in1(rd), .out(multiplexer_14_out), .sel(\硬布线控制器_1_regdst ));
  Multiplexer #(.width(5), .enable("false")) multiplexer_15 (
    .in0(multiplexer_14_out), .in1({5{1'b1}}), .out(multiplexer_15_out), .sel(\硬布线控制器_1_jal ));
  D_Flip_Flop d_ff_4 (
    .clk(CLK), .D(multiplexer_9_out), .Q(\中断屏蔽字 [0]), .Qn(d_ff_4_qn), .en(and_9_out));  // open: preset, reset
  D_Flip_Flop d_ff_5 (
    .clk(CLK), .D(multiplexer_10_out), .Q(\中断屏蔽字 [1]), .Qn(d_ff_5_qn), .en(and_9_out));  // open: preset, reset
  D_Flip_Flop d_ff_6 (
    .clk(CLK), .D(multiplexer_11_out), .Q(\中断屏蔽字 [2]), .Qn(d_ff_6_qn), .en(and_9_out));  // open: preset, reset
  D_Flip_Flop d_ff_7 (
    .clk(CLK), .D(multiplexer_12_out), .Q(\中断屏蔽字 [3]), .Qn(d_ff_7_qn), .en(and_9_out));  // open: preset, reset
  Multiplexer #(.select(2), .width(32), .enable("false")) multiplexer_16 (
    .in1({{28{1'b0}}, \中断屏蔽字 }), .in2(EPC), .out(MFC0Data), .sel(rd[1:0]));  // open: in0, in3
  Demultiplexer #(.select(2), .width(32), .enable("false")) demultiplexer_1 (
    .out1(\中断屏蔽字_out ), .out2(EPC_out), .out3(IE_out), .in(MTC0Data), .sel(rd[1:0]));  // open: out0
  // Probe on WB_PC
  Multiplexer #(.width(5), .enable("false")) multiplexer_17 (
    .in0(rt), .in1(5'b00010), .out(multiplexer_17_out), .sel(\硬布线控制器_1_syscall ));
  Multiplexer #(.width(32), .enable("false")) multiplexer_18 (
    .in0(multiplexer_28_out), .in1(adder_1_out), .out(multiplexer_18_out), .sel(\硬布线控制器_1_jal ));
  and and_10 (and_10_out, 1'b0, d_ff_4_qn);
  and and_11 (and_11_out, Do1, d_ff_5_qn);
  and and_12 (and_12_out, Do2, d_ff_6_qn);
  and and_13 (and_13_out, Do3, d_ff_7_qn);
  Priority_Encoder #(.select(2)) priority_encoder_1 (
    .in0(1'b0), .in1(Do1), .in2(Do2), .in3(Do3), .out(priority_encoder_1_out));  // open: gs, en_out, en_in
  Decoder #(.select(2), .enable("false")) decoder_1 (
    .out1(decoder_1_out1), .out2(decoder_1_out2), .out3(decoder_1_out3), .sel(priority_encoder_1_out));  // open: out0
  not not_5 (not_5_out, MFC0);
  Multiplexer #(.width(32), .enable("false")) multiplexer_19 (
    .in0(MFC0Data), .in1(multiplexer_18_out), .out(multiplexer_19_out), .sel(not_5_out));
  Priority_Encoder #(.select(2)) priority_encoder_2 (
    .in0(and_10_out), .in1(and_11_out), .in2(and_12_out), .in3(and_13_out), .out(priority_encoder_2_out),
    .gs(Do));  // open: en_out, en_in
  Counter #(.width(16), .max('hffff)) counter_1 (
    .count(Enable), .Q(\总周期数 ), .clk(CLK), .clr(RST));  // open: load, D, carry
  assign bit_extender_1_out = {{16{1'b0}}, {rd, rom_1_data_2, rom_1_data[5:0]}};  // Bit_Extender bit_extender_1
  assign bit_extender_2_out = {{16{rd[4]}}, {rd, rom_1_data_2, rom_1_data[5:0]}};  // Bit_Extender bit_extender_2
  assign bit_extender_3_out = {{6{rom_1_data[25]}}, {rom_1_data[25:21], rt, rd, rom_1_data_2, rom_1_data[5:0]}};  // Bit_Extender bit_extender_3
  and and_14 (rst1, decoder_1_out1, ERET);
  and and_15 (rst2, decoder_1_out2, ERET);
  and and_16 (rst3, decoder_1_out3, ERET);
  MIPS_Regifile mips_regifile_1 (
    .Din(multiplexer_19_out), .Clk(CLK), .R1(mips_regifile_1_r1), .R2(mips_regifile_1_r2),
    .WE(\硬布线控制器_1_regwrite ), .W_num(multiplexer_15_out), .R1_num(multiplexer_13_out),
    .R2_num(multiplexer_17_out));
  Multiplexer #(.width(32), .enable("false")) multiplexer_20 (
    .in0(bit_extender_1_out), .in1(bit_extender_2_out), .out(multiplexer_20_out), .sel(SignedExt));
  not not_6 (not_6_out, MTC0);
  Multiplexer #(.select(2), .width(32), .enable("false")) multiplexer_21 (
    .in1(32'h4), .in2(32'h20c), .in3(32'h414), .out(\中断程序入口地址 ), .sel(priority_encoder_2_out));  // open: in0
  Counter #(.width(16), .max('hffff)) counter_2 (
    .count(JMP), .Q(\无条件分支数 ), .clk(CLK), .clr(RST));  // open: load, D, carry
  Register #(.width(32)) register_2 (.D(mips_regifile_1_r1), .en(and_17_out), .Q(LedData), .clk(CLK), .clr(RST));
  and and_17 (and_17_out, Show, \硬布线控制器_1_syscall );
  Multiplexer #(.width(32), .enable("false")) multiplexer_22 (
    .in0(mips_regifile_1_r2), .in1({32{1'b0}}), .out(MTC0Data), .sel(not_6_out));
  Comparator #(.width(32)) comparator_5 (.a(32'h22), .b(mips_regifile_1_r2), .eq(Show));  // open: gt, lt
  Multiplexer #(.width(32), .enable("false")) multiplexer_23 (
    .in0(mips_regifile_1_r2), .in1(multiplexer_20_out), .out(multiplexer_23_out), .sel(\硬布线控制器_1_alu_src ));
  Shifter #(.width(32)) shifter_1 (.in(multiplexer_20_out), .\dist (5'b00010), .out(shifter_1_out));
  Shifter #(.width(32)) shifter_2 (.in(bit_extender_3_out), .\dist (5'b00010), .out(shifter_2_out));
  Counter #(.width(16), .max('hffff)) counter_3 (
    .count(Bench), .Q(\条件分支成功数 ), .clk(CLK), .clr(RST));  // open: load, D, carry
  MIPS_ALU mips_alu_1 (
    .X(mips_regifile_1_r1), .Y(multiplexer_23_out), .AluOP(\硬布线控制器_1_alu_op ), .Equal(mips_alu_1_equal),
    .Result({mips_alu_1_result[31:2], heigh, mips_alu_1_result[0]}), .shamt(rom_1_data_2));  // open: Result_2
  Multiplexer #(.width(32), .enable("false")) multiplexer_24 (
    .in0({{16{1'b0}}, mips_regifile_1_r2[15:0]}), .in1({mips_regifile_1_r2[15:0], {16{1'b0}}}),
    .out(multiplexer_24_out), .sel(heigh));
  Adder #(.width(32)) adder_2 (.a(shifter_1_out), .b(adder_1_out), .out(adder_2_out));  // open: cin, cout
  and and_18 (and_18_out, \硬布线控制器_1_beq , mips_alu_1_equal);
  and and_19 (and_19_out, \硬布线控制器_1_bne , not_7_out);
  not not_7 (not_7_out, mips_alu_1_equal);
  Multiplexer #(.width(32), .enable("false")) multiplexer_25 (
    .in0(mips_regifile_1_r2), .in1(multiplexer_24_out), .out(multiplexer_25_out), .sel(SH));
  or or_11 (or_11_out, and_18_out, and_19_out);
  Multiplexer #(.width(4), .enable("false")) multiplexer_26 (
    .in0(4'b1111), .in1(multiplexer_27_out), .out(multiplexer_26_out), .sel(SH));
  Multiplexer #(.width(4), .enable("false")) multiplexer_27 (
    .in0(4'b0011), .in1(4'b1100), .out(multiplexer_27_out), .sel(heigh));
  // MIPS_RAM mips_ram_1: pin names not known; wires that end beside it: mips_alu_1_result[11:2], multiplexer_25_out, \硬布线控制器_1_memwrite , multiplexer_26_out, CLK, 1'b1, RST, mips_ram_1_p8
  Multiplexer #(.width(32), .enable("false")) multiplexer_28 (
    .in0({mips_alu_1_result[31:2], heigh, mips_alu_1_result[0]}), .in1(mips_ram_1_p8),
    .out(multiplexer_28_out), .sel(\硬布线控制器_1_memtoreg ));

  // Notes on the sheet:
  //   中断源
  //   中断等待指示
  //   中断按键信号产生
  //   COP0模拟
  //   数码管输出
  //   Reset 
  //   Reset 
  //   Reset 
  //   指令存储器
  //   指令字
  //   contents of rom_1 (hex, n*v repeats v):
  //   8000d87 23bdfffc afa10000 23bdfffc afa20000 23bdfffc afa30000 23bdfffc afa40000 23bdfffc afa50000
  //   23bdfffc afa60000 23bdfffc afa70000 23bdfffc afa80000 23bdfffc afa90000 23bdfffc afaa0000 23bdfffc
  //   afab0000 23bdfffc afac0000 23bdfffc afad0000 23bdfffc afae0000 23bdfffc afaf0000 23bdfffc afb00000
  //   23bdfffc afb10000 23bdfffc afb20000 23bdfffc afb30000 23bdfffc afb40000 23bdfffc afb50000 23bdfffc
  //   afb60000 23bdfffc afb70000 23bdfffc afb80000 23bdfffc afb90000 40010800 40021000 23bdfffc afa10000
  //   23bdfffc afa20000 20010003 40810800 20030001 40831800 20160001 20140006 20150001 168020 108100
  //   2149825 132020 20020022 c 1600fffa 295a022 1680fff7 40801800 8fa20000 23bd0004 8fa10000 23bd0004
  //   40821000 40810800 8fb90000 23bd0004 8fb80000 23bd0004 8fb70000 23bd0004 8fb60000 23bd0004 8fb50000
  //   23bd0004 8fb40000 23bd0004 8fb30000 23bd0004 8fb20000 23bd0004 8fb10000 23bd0004 8fb00000 23bd0004
  //   8faf0000 23bd0004 8fae0000 23bd0004 8fad0000 23bd0004 8fac0000 23bd0004 8fab0000 23bd0004 8faa0000
  //   23bd0004 8fa90000 23bd0004 8fa80000 23bd0004 8fa70000 23bd0004 8fa60000 23bd0004 8fa50000 23bd0004
  //   8fa40000 23bd0004 8fa30000 23bd0004 8fa20000 23bd0004 8fa10000 23bd0004 42000018 23bdfffc afa10000
  //   23bdfffc afa20000 23bdfffc afa30000 23bdfffc afa40000 23bdfffc afa50000 23bdfffc afa60000 23bdfffc
  //   afa70000 23bdfffc afa80000 23bdfffc afa90000 23bdfffc afaa0000 23bdfffc afab0000 23bdfffc afac0000
  //   23bdfffc afad0000 23bdfffc afae0000 23bdfffc afaf0000 23bdfffc afb00000 23bdfffc afb10000 23bdfffc
  //   afb20000 23bdfffc afb30000 23bdfffc afb40000 23bdfffc afb50000 23bdfffc afb60000 23bdfffc afb70000
  //   23bdfffc afb80000 23bdfffc afb90000 40010800 40021000 23bdfffc afa10000 23bdfffc afa20000 20010007
  //   40810800 20030001 40831800 20160002 20140006 20150001 168020 108100 2149825 132020 20020022 c
  //   1600fffa 295a022 1680fff7 40801800 8fa20000 23bd0004 8fa10000 23bd0004 40821000 40810800 8fb90000
  //   23bd0004 8fb80000 23bd0004 8fb70000 23bd0004 8fb60000 23bd0004 8fb50000 23bd0004 8fb40000 23bd0004
  //   8fb30000 23bd0004 8fb20000 23bd0004 8fb10000 23bd0004 8fb00000 23bd0004 8faf0000 23bd0004 8fae0000
  //   23bd0004 8fad0000 23bd0004 8fac0000 23bd0004 8fab0000 23bd0004 8faa0000 23bd0004 8fa90000 23bd0004
  //   8fa80000 23bd0004 8fa70000 23bd0004 8fa60000 23bd0004 8fa50000 23bd0004 8fa40000 23bd0004 8fa30000
  //   23bd0004 8fa20000 23bd0004 8fa10000 23bd0004 42000018 23bdfffc afa10000 23bdfffc afa20000 23bdfffc
  //   afa30000 23bdfffc afa40000 23bdfffc afa50000 23bdfffc afa60000 23bdfffc afa70000 23bdfffc afa80000
  //   23bdfffc afa90000 23bdfffc afaa0000 23bdfffc afab0000 23bdfffc afac0000 23bdfffc afad0000 23bdfffc
  //   afae0000 23bdfffc afaf0000 23bdfffc afb00000 23bdfffc afb10000 23bdfffc afb20000 23bdfffc afb30000
  //   23bdfffc afb40000 23bdfffc afb50000 23bdfffc afb60000 23bdfffc afb70000 23bdfffc afb80000 23bdfffc
  //   afb90000 40010800 40021000 23bdfffc afa10000 23bdfffc afa20000 2001000f 40810800 20030001 40831800
  //   20160003 20140006 20150001 168020 108100 2149825 132020 20020022 c 1600fffa 295a022 1680fff7
  //   40801800 8fa20000 23bd0004 8fa10000 23bd0004 40821000 40810800 8fb90000 23bd0004 8fb80000 23bd0004
  //   8fb70000 23bd0004 8fb60000 23bd0004 8fb50000 23bd0004 8fb40000 23bd0004 8fb30000 23bd0004 8fb20000
  //   23bd0004 8fb10000 23bd0004 8fb00000 23bd0004 8faf0000 23bd0004 8fae0000 23bd0004 8fad0000 23bd0004
  //   8fac0000 23bd0004 8fab0000 23bd0004 8faa0000 23bd0004 8fa90000 23bd0004 8fa80000 23bd0004 8fa70000
  //   23bd0004 8fa60000 23bd0004 8fa50000 23bd0004 8fa40000 23bd0004 8fa30000 23bd0004 8fa20000 23bd0004
  //   8fa10000 23bd0004 42000018 20110200 20020022 112020 c 2231ffff 1620fffc 20020032 c 2002000a c
  //   JMP
  //   JR
  //   OP
  //   OP
  //   Func
  //   Func
  //   rs
  //   rt
  //   rd
  //   Beq
  //   Bne
  //   MemToReg
  //   MemWrite
  //   AluOP
  //   AluSrcB
  //   RegWrite
  //   JAL
  //   RegDst
  //   Syscall
  //   流水调试日志用
  //   增加中断屏蔽字之后的中断服务程序进入处理
  //   MTC与MFC指令的数据处理
  //   中断服务程序返回处理
  //   周期数计算
endmodule

module \流水中断  (
);

  wire and_2_out, and_3_out, and_4_out, and_5_out, and_6_out, and_7_out, and_8_out, and_10_out, and_11_out,
       and_12_out, and_13_out, and_14_out, and_15_out, and_20_out, and_21_out, and_22_out, and_23_out, Bench,
       Benchif, CLK, comparator_1_eq, comparator_2_eq, comparator_3_eq, comparator_4_eq, comparator_5_eq,
       comparator_6_lt, d_ff_1_q, d_ff_2_q, d_ff_3_q, d_ff_4_qn, d_ff_5_qn, d_ff_6_qn, d_ff_7_qn,
       decoder_1_out1, decoder_1_out2, decoder_1_out3, Do, Do1, Do2, Do3, Enable, ERET, ex_mem_1_dout_1,
       ex_mem_1_dout_1_2, ex_mem_1_dout_1_3, ex_mem_1_dout_1_4, ex_mem_1_dout_1_5, ex_mem_1_dout_1_6,
       ex_mem_1_dout_1_7, ex_mem_1_dout_1_8, ex_mem_1_dout_1_9, ex_mem_1_dout_1_10,
       \ex_mem_1_传输状态out_表明当前传输数据有效 , EX_PC__0, Go, id_ex_1_dout_1, \id_ex_1_传输状态out_表明当前传输数据有效 , IE_q,
       \if_id_1_传输状态out_表明当前传输数据有效 , IR, IR1, IR2, IR3, JMP, Load_use, mem_wb_1_dout_1, mem_wb_1_dout_1_2,
       mem_wb_1_dout_1_3, mem_wb_1_dout_1_4, mem_wb_1_dout_1_5, mem_wb_1_dout_1_7, mips_alu_1_equal, MTC0,
       multiplexer_4_out, multiplexer_11_out, multiplexer_12_out, multiplexer_13_out, multiplexer_14_out,
       nor_1_out, nor_2_out, not_1_out, not_2_out, not_5_out, not_6_out, not_7_out, not_8_out, not_9_out,
       not_10_out, not_11_out, not_12_out, or_1_out, or_5_out, or_6_out, or_7_out, or_8_out, or_9_out,
       or_10_out, or_11_out, or_12_out, or_13_out, or_14_out, or_17_out, or_18_out, or_19_out, register_1_q,
       RST, rst1, rst2, rst3, Run, Stop1, Stop2, W1, W2, W3, \硬布线控制器_1_eret , \硬布线控制器_1_regdst ,
       \硬布线控制器_1_signedext ;
  wire [1:0] id_ex_1_dout_2, id_ex_1_dout_2_2, id_ex_1_dout_2_3, priority_encoder_1_out,
       priority_encoder_2_out, \数据相关检测_1_forwardr1 , \数据相关检测_1_forwardr2 , \硬布线控制器_1_mfc0 ;
  wire [2:0] id_ex_1_dout_4;
  wire [3:0] id_ex_1_dout_4_2, id_ex_1_dout_4_3, id_ex_1_dout_4_4, multiplexer_26_out, multiplexer_27_out,
       \中断屏蔽字 , \硬布线控制器_1_alu_op , \硬布线控制器_1_alu_src , \硬布线控制器_1_beq , \硬布线控制器_1_bltz ;
  wire [4:0] ex_mem_1_dout_5, id_ex_1_dout_5, id_ex_1_dout_5_2, mem_wb_1_dout_5, multiplexer_6_out,
       multiplexer_7_out, multiplexer_8_out, multiplexer_10_out, rd;
  wire [9:0] if_id_1_dout_ins_2;
  wire [15:0] \LoadUse次数 , \总周期数 , \无条件分支数 , \条件分支成功数 ;
  wire [31:0] adder_1_out, adder_2_out, bit_extender_1_out, bit_extender_2_out, bit_extender_3_out, EPC,
       EPC_out, ex_mem_1_dout_32, ex_mem_1_dout_32_2, ex_mem_1_dout_32_3, ex_mem_1_dout_32_4,
       ex_mem_1_dout_32_6, ex_mem_1_dout_32_7, EX_PC, id_ex_1_dout_32, id_ex_1_dout_32_2, id_ex_1_dout_32_3,
       id_ex_1_dout_32_4, id_ex_1_dout_32_5, id_ex_1_dout_32_7, ID_PC, IE_out, if_id_1_dout_ins,
       if_id_1_dout_pc_4, IF_PC, LedData, MEM_PC, mem_wb_1_dout_32_2, mem_wb_1_dout_32_3, mem_wb_1_dout_32_4,
       mem_wb_1_dout_32_7, MFC0Data, mips_alu_1_result, mips_ram_1_p8, mips_regifile_1_r1,
       mips_regifile_1_r2, MTC0Data, multiplexer_1_out, multiplexer_2_out, multiplexer_3_out,
       multiplexer_5_out, multiplexer_9_out, multiplexer_16_out, multiplexer_17_out, multiplexer_18_out,
       multiplexer_19_out, multiplexer_21_out, multiplexer_22_out, multiplexer_23_out, multiplexer_24_out,
       multiplexer_25_out, multiplexer_28_out, multiplexer_29_out, multiplexer_30_out, register_2_q,
       rom_1_data, shifter_1_out, shifter_2_out, WB_PC, \中断屏蔽字_out , \中断程序入口地址 ;

  Button \u_总复位  (.out(RST));
  Button _1 (.out(IR1));
  Button _2 (.out(IR2));
  Button _3 (.out(IR3));
  Multiplexer #(.width(32), .enable("false")) multiplexer_1 (
    .in0(multiplexer_2_out), .in1(EPC), .out(multiplexer_1_out), .sel(ERET));
  Multiplexer #(.width(32), .enable("false")) multiplexer_2 (
    .in0(multiplexer_3_out), .in1(\中断程序入口地址 ), .out(multiplexer_2_out), .sel(IR));
  Button \u_继续运行  (.out(Go));
  LED led_1 (.in(W1));
  LED led_2 (.in(W2));
  LED led_3 (.in(W3));
  not not_1 (not_1_out, Load_use);
  and and_1 (Run, Enable, not_1_out);
  and and_2 (and_2_out, mem_wb_1_dout_1_2, not_2_out);
  not not_2 (not_2_out, mem_wb_1_dout_1);
  Hex_Digit_Display hex_digit_display_1 (.value(LedData[31:28]));  // open: dp
  Register #(.width(32)) PC (.D(multiplexer_1_out), .en(Run), .Q(IF_PC), .clk(CLK), .clr(RST));
  Adder #(.width(32)) adder_1 (.a(IF_PC), .b(32'h4), .out(adder_1_out));  // open: cin, cout
  not not_3 (Enable, register_1_q);
  Register #(.width(1)) register_1 (.D(mem_wb_1_dout_1_2), .en(and_2_out), .Q(register_1_q), .clk(CLK), .clr(or_1_out));
  or or_1 (or_1_out, Go, RST);
  Comparator #(.width(32)) comparator_1 (.a(EX_PC), .b({32{1'b0}}), .eq(comparator_1_eq));  // open: gt, lt
  not not_4 (EX_PC__0, comparator_1_eq);
  Hex_Digit_Display hex_digit_display_2 (.value(LedData[27:24]));  // open: dp
  Hex_Digit_Display hex_digit_display_3 (.value(LedData[23:20]));  // open: dp
  Multiplexer #(.width(32), .enable("false")) multiplexer_3 (
    .in0(adder_1_out), .in1(multiplexer_23_out), .out(multiplexer_3_out), .sel(Bench));
  or or_2 (W1, Do1, d_ff_1_q);
  or or_3 (W2, Do2, d_ff_2_q);
  or or_4 (W3, Do3, d_ff_3_q);
  Comparator #(.width(5)) comparator_2 (.a(rd), .b(5'b00010), .eq(comparator_2_eq));  // open: gt, lt
  Comparator #(.width(5)) comparator_3 (.a(rd), .b(5'b00011), .eq(comparator_3_eq));  // open: gt, lt
  Hex_Digit_Display hex_digit_display_4 (.value(LedData[19:16]));  // open: dp
  Hex_Digit_Display hex_digit_display_5 (.value(LedData[15:12]));  // open: dp
  or or_5 (or_5_out, Bench, IR, ERET);
  ROM #(.addrWidth(10), .dataWidth(32)) rom_1 (.addr(IF_PC[11:2]), .data(rom_1_data));  // open: sel
  or or_6 (or_6_out, Load_use, register_1_q, 1'b0);
  D_Flip_Flop d_ff_1 (.clk(IR1), .D(1'b1), .Q(d_ff_1_q), .reset(Do1));  // open: Qn, preset, en
  D_Flip_Flop d_ff_2 (.clk(IR2), .D(1'b1), .Q(d_ff_2_q), .reset(Do2));  // open: Qn, preset, en
  D_Flip_Flop d_ff_3 (.clk(IR3), .D(1'b1), .Q(d_ff_3_q), .reset(Do3));  // open: Qn, preset, en
  and and_3 (and_3_out, MTC0, comparator_2_eq);
  Multiplexer #(.enable("false")) multiplexer_4 (.in0(IR), .in1(not_5_out), .out(multiplexer_4_out), .sel(and_4_out));
  not not_5 (not_5_out, IE_out[0]);
  or or_7 (or_7_out, IR, and_4_out, ERET);
  and and_4 (and_4_out, comparator_3_eq, MTC0);
  Hex_Digit_Display hex_digit_display_6 (.value(LedData[7:4]));  // open: dp
  Hex_Digit_Display hex_digit_display_7 (.value(LedData[11:8]));  // open: dp
  Clock clock_1 (.out(CLK));
  \数据相关检测  \u_数据相关检测_1  (
    .OP(if_id_1_dout_ins[31:26]), .EX_WriteReg_num(id_ex_1_dout_5_2), .EX_RegWrite(id_ex_1_dout_4_4[1]),
    .ForwardR1(\数据相关检测_1_forwardr1 ), .MEM_WriteReg_num(ex_mem_1_dout_5), .MEM_RegWrite(ex_mem_1_dout_1_6),
    .ForwardR2(\数据相关检测_1_forwardr2 ), .Func(if_id_1_dout_ins[5:0]), .ID_R1_num(multiplexer_7_out),
    .ID_R2_num(multiplexer_10_out), .EX_MemToReg(id_ex_1_dout_4_2[2]), .MEM_MemToReg(ex_mem_1_dout_1_4),
    .Load_Use(Load_use));  // open: 数据相关
  IF_ID if_id_1 (
    .Din_Ins(rom_1_data), .Din_PC_4(adder_1_out), .\传输状态In_表明当前传输数据有效 (1'b1), .CLK(CLK),
    .Dout_Ins({if_id_1_dout_ins[31:21], if_id_1_dout_ins_2[4:0], if_id_1_dout_ins_2[9:5], if_id_1_dout_ins[10:0]}),
    .Dout_PC_4(if_id_1_dout_pc_4), .\传输状态Out_表明当前传输数据有效 (\if_id_1_传输状态out_表明当前传输数据有效 ),
    .\同步清零_气泡_高电平有效 (or_5_out), .\使能端_低电平有效_stall_高电平有效 (or_6_out), .Din_PC(IF_PC), .Dout_PC(ID_PC));  // open: Din_Status, Dout_Status, Din_Addr, Dout_Addr, Din_Miss, Dout_Miss, Din_Hit, Dout_Hit
  or or_8 (or_8_out, d_ff_1_q, Do1);
  or or_9 (or_9_out, d_ff_2_q, Do2);
  or or_10 (or_10_out, d_ff_3_q, Do3);
  Multiplexer #(.width(32), .enable("false")) multiplexer_5 (
    .in0(MEM_PC), .in1(EPC_out), .out(multiplexer_5_out), .sel(and_3_out));
  or or_11 (or_11_out, IR, and_3_out);
  and and_5 (and_5_out, or_11_out, EX_PC__0);
  Register #(.width(1)) IE (.D(multiplexer_4_out), .en(or_7_out), .Q(IE_q), .clk(CLK));  // open: clr
  Hex_Digit_Display hex_digit_display_8 (.value(LedData[3:0]));  // open: dp
  and and_6 (and_6_out, or_8_out, ~rst1);  // AND_Gate
  and and_7 (and_7_out, or_9_out, ~rst2);  // AND_Gate
  and and_8 (and_8_out, or_10_out, ~rst3);  // AND_Gate
  Register #(.width(32)) u_EPC (.D(multiplexer_5_out), .en(and_5_out), .Q(EPC), .clk(CLK));  // open: clr
  not not_6 (not_6_out, IE_q);
  and and_9 (IR, not_6_out, Do);
  D_Flip_Flop u_IR1 (.clk(CLK), .D(and_6_out), .Q(Do1), .en(EX_PC__0));  // open: Qn, preset, reset
  D_Flip_Flop u_IR2 (.clk(CLK), .D(and_7_out), .Q(Do2), .en(EX_PC__0));  // open: Qn, preset, reset
  D_Flip_Flop u_IR3 (.clk(CLK), .D(and_8_out), .Q(Do3), .en(EX_PC__0));  // open: Qn, preset, reset
  // Probe on \总周期数 
  // Probe on \无条件分支数 
  // Probe on \条件分支成功数 
  // Probe on \LoadUse次数 
  // Probe on \LoadUse次数 
  \硬布线控制器  \u_硬布线控制器_1  (
    .Func(if_id_1_dout_ins[5:0]), .OP(if_id_1_dout_ins[31:26]), .ALU_OP(\硬布线控制器_1_alu_op ),
    .MemToReg(\硬布线控制器_1_beq [2]), .MemWrite(\硬布线控制器_1_beq [3]), .ALU_SRC(\硬布线控制器_1_alu_src [0]),
    .RegWrite(\硬布线控制器_1_alu_src [1]), .SysCALL(\硬布线控制器_1_alu_src [3]), .SignedExt(\硬布线控制器_1_signedext ),
    .RegDst(\硬布线控制器_1_regdst ), .JR(\硬布线控制器_1_bltz [2]), .JMP(\硬布线控制器_1_bltz [3]), .Beq(\硬布线控制器_1_beq [0]),
    .JAL(\硬布线控制器_1_alu_src [2]), .Bne(\硬布线控制器_1_beq [1]), .SH(\硬布线控制器_1_bltz [1]), .BLTZ(\硬布线控制器_1_bltz [0]),
    .ERET(\硬布线控制器_1_eret ), .MF(if_id_1_dout_ins[25:21]), .MFC0(\硬布线控制器_1_mfc0 [0]), .MTC0(\硬布线控制器_1_mfc0 [1]));
  Multiplexer #(.width(5), .enable("false")) multiplexer_6 (
    .in0(if_id_1_dout_ins_2[4:0]), .in1(if_id_1_dout_ins_2[9:5]), .out(multiplexer_6_out),
    .sel(\硬布线控制器_1_regdst ));
  assign bit_extender_1_out = {{16{1'b0}}, {if_id_1_dout_ins_2[9:5], if_id_1_dout_ins[10:0]}};  // Bit_Extender bit_extender_1
  assign bit_extender_2_out = {{16{if_id_1_dout_ins_2[9]}}, {if_id_1_dout_ins_2[9:5], if_id_1_dout_ins[10:0]}};  // Bit_Extender bit_extender_2
  assign bit_extender_3_out = {{6{if_id_1_dout_ins[25]}}, {if_id_1_dout_ins[25:21], if_id_1_dout_ins_2[4:0], if_id_1_dout_ins_2[9:5], if_id_1_dout_ins[10:0]}};  // Bit_Extender bit_extender_3
  // Probe on IF_PC[11:0]
  Multiplexer #(.width(5), .enable("false")) multiplexer_7 (
    .in0(if_id_1_dout_ins[25:21]), .in1(5'b00100), .out(multiplexer_7_out), .sel(\硬布线控制器_1_alu_src [3]));
  Multiplexer #(.width(5), .enable("false")) multiplexer_8 (
    .in0(multiplexer_6_out), .in1({5{1'b1}}), .out(multiplexer_8_out), .sel(\硬布线控制器_1_alu_src [2]));
  Multiplexer #(.width(32), .enable("false")) multiplexer_9 (
    .in0(bit_extender_1_out), .in1(bit_extender_2_out), .out(multiplexer_9_out), .sel(\硬布线控制器_1_signedext ));
  // Probe on ID_PC[11:0]
  Multiplexer #(.width(5), .enable("false")) multiplexer_10 (
    .in0(if_id_1_dout_ins_2[4:0]), .in1(5'b00010), .out(multiplexer_10_out), .sel(\硬布线控制器_1_alu_src [3]));
  Comparator #(.width(5)) comparator_4 (.a(rd), .b(5'b00001), .eq(comparator_4_eq));  // open: gt, lt
  // Probe on MEM_PC[11:0]
  // Probe on EX_PC[11:0]
  MIPS_Regifile mips_regifile_1 (
    .Din(multiplexer_30_out), .Clk(CLK), .R1(mips_regifile_1_r1), .R2(mips_regifile_1_r2),
    .WE(mem_wb_1_dout_1_4), .W_num(mem_wb_1_dout_5), .R1_num(multiplexer_7_out), .R2_num(multiplexer_10_out));
  and and_10 (and_10_out, MTC0, comparator_4_eq);
  // Probe on WB_PC[11:0]
  or or_12 (or_12_out, or_5_out, IR, Load_use);
  ID_EX id_ex_1 (
    .Din_4(\硬布线控制器_1_bltz ), .Din_4_2(\硬布线控制器_1_beq ), .Din_4_3(\硬布线控制器_1_alu_op ),
    .Din_4_4(\硬布线控制器_1_alu_src ), .Din_32(mips_regifile_1_r1), .Din_32_2(mips_regifile_1_r2),
    .Din_32_3(multiplexer_9_out), .Din_32_4(bit_extender_3_out), .Din_5(if_id_1_dout_ins[10:6]),
    .Din_32_5(if_id_1_dout_pc_4), .\传输状态In_表明当前传输数据有效 (\if_id_1_传输状态out_表明当前传输数据有效 ), .CLK(CLK),
    .Dout_4({JMP, id_ex_1_dout_4}), .Dout_4_2(id_ex_1_dout_4_2), .Dout_4_3(id_ex_1_dout_4_3),
    .Dout_4_4(id_ex_1_dout_4_4), .Dout_32(id_ex_1_dout_32), .Dout_32_2(id_ex_1_dout_32_2),
    .Dout_32_3(id_ex_1_dout_32_3), .Dout_32_4(id_ex_1_dout_32_4), .Dout_5(id_ex_1_dout_5),
    .Dout_32_5(id_ex_1_dout_32_5), .\传输状态Out_表明当前传输数据有效 (\id_ex_1_传输状态out_表明当前传输数据有效 ),
    .\同步清零_气泡_高电平有效 (or_12_out), .\使能端_低电平有效_stall_高电平有效 (or_13_out), .Din_5_2(multiplexer_8_out),
    .Dout_5_2(id_ex_1_dout_5_2), .Din_32_6(ID_PC), .Dout_32_6(EX_PC), .Din_2(\数据相关检测_1_forwardr1 ),
    .Dout_2(id_ex_1_dout_2), .Din_2_2(\数据相关检测_1_forwardr2 ), .Dout_2_2(id_ex_1_dout_2_2),
    .Din_2_3(\硬布线控制器_1_mfc0 ), .Dout_2_3(id_ex_1_dout_2_3), .Din_32_7({{22{1'b0}}, if_id_1_dout_ins_2}),
    .Dout_32_7(id_ex_1_dout_32_7), .Din_1(\硬布线控制器_1_eret ), .Dout_1(id_ex_1_dout_1));  // open: Din_1_2, Dout_1_2
  or or_13 (or_13_out, register_1_q, 1'b0);
  Multiplexer #(.enable("false")) multiplexer_11 (
    .in0(1'b0), .in1(\中断屏蔽字_out [0]), .out(multiplexer_11_out), .sel(and_10_out));
  Multiplexer #(.enable("false")) multiplexer_12 (
    .in0(1'b0), .in1(\中断屏蔽字_out [1]), .out(multiplexer_12_out), .sel(and_10_out));
  Multiplexer #(.enable("false")) multiplexer_13 (
    .in0(1'b0), .in1(\中断屏蔽字_out [2]), .out(multiplexer_13_out), .sel(and_10_out));
  Multiplexer #(.enable("false")) multiplexer_14 (
    .in0(1'b0), .in1(\中断屏蔽字_out [3]), .out(multiplexer_14_out), .sel(and_10_out));
  D_Flip_Flop d_ff_4 (
    .clk(CLK), .D(multiplexer_11_out), .Q(\中断屏蔽字 [0]), .Qn(d_ff_4_qn), .en(and_10_out));  // open: preset, reset
  D_Flip_Flop d_ff_5 (
    .clk(CLK), .D(multiplexer_12_out), .Q(\中断屏蔽字 [1]), .Qn(d_ff_5_qn), .en(and_10_out));  // open: preset, reset
  D_Flip_Flop d_ff_6 (
    .clk(CLK), .D(multiplexer_13_out), .Q(\中断屏蔽字 [2]), .Qn(d_ff_6_qn), .en(and_10_out));  // open: preset, reset
  D_Flip_Flop d_ff_7 (
    .clk(CLK), .D(multiplexer_14_out), .Q(\中断屏蔽字 [3]), .Qn(d_ff_7_qn), .en(and_10_out));  // open: preset, reset
  Multiplexer #(.select(2), .width(32), .enable("false")) multiplexer_15 (
    .in1({{28{1'b0}}, \中断屏蔽字 }), .in2(EPC), .out(MFC0Data), .sel(rd[1:0]));  // open: in0, in3
  Demultiplexer #(.select(2), .width(32), .enable("false")) demultiplexer_1 (
    .out1(\中断屏蔽字_out ), .out2(EPC_out), .out3(IE_out), .in(MTC0Data), .sel(rd[1:0]));  // open: out0
  Counter #(.width(16), .max('hffff)) counter_1 (
    .count(Enable), .Q(\总周期数 ), .clk(CLK), .clr(RST));  // open: load, D, carry
  Multiplexer #(.select(2), .width(32), .enable("false")) multiplexer_16 (
    .in0(id_ex_1_dout_32), .in1(mem_wb_1_dout_32_2), .in2(mem_wb_1_dout_32_3), .in3(ex_mem_1_dout_32_2),
    .out(multiplexer_16_out), .sel(id_ex_1_dout_2));
  Multiplexer #(.select(2), .width(32), .enable("false")) multiplexer_17 (
    .in0(id_ex_1_dout_32_2), .in1(mem_wb_1_dout_32_2), .in2(mem_wb_1_dout_32_3), .in3(ex_mem_1_dout_32_2),
    .out(multiplexer_17_out), .sel(id_ex_1_dout_2_2));
  and and_11 (and_11_out, 1'b0, d_ff_4_qn);
  and and_12 (and_12_out, Do1, d_ff_5_qn);
  and and_13 (and_13_out, Do2, d_ff_6_qn);
  and and_14 (and_14_out, Do3, d_ff_7_qn);
  Priority_Encoder #(.select(2)) priority_encoder_1 (
    .in0(1'b0), .in1(Do1), .in2(Do2), .in3(Do3), .out(priority_encoder_1_out));  // open: gs, en_out, en_in
  Decoder #(.select(2), .enable("false")) decoder_1 (
    .out1(decoder_1_out1), .out2(decoder_1_out2), .out3(decoder_1_out3), .sel(priority_encoder_1_out));  // open: out0
  Multiplexer #(.width(32), .enable("false")) multiplexer_18 (
    .in0(multiplexer_17_out), .in1({32{1'b0}}), .out(multiplexer_18_out), .sel(not_7_out));
  not not_7 (not_7_out, id_ex_1_dout_2_3[1]);
  Priority_Encoder #(.select(2)) priority_encoder_2 (
    .in0(and_11_out), .in1(and_12_out), .in2(and_13_out), .in3(and_14_out), .out(priority_encoder_2_out),
    .gs(Do));  // open: en_out, en_in
  Counter #(.width(16), .max('hffff)) counter_2 (
    .count(JMP), .Q(\无条件分支数 ), .clk(CLK), .clr(RST));  // open: load, D, carry
  and and_15 (and_15_out, comparator_5_eq, id_ex_1_dout_4_4[3]);
  not not_8 (not_8_out, comparator_5_eq);
  and and_16 (Stop1, not_8_out, id_ex_1_dout_4_4[3]);
  and and_17 (rst1, decoder_1_out1, ERET);
  and and_18 (rst2, decoder_1_out2, ERET);
  and and_19 (rst3, decoder_1_out3, ERET);
  Register #(.width(32)) register_2 (.D(multiplexer_16_out), .en(and_15_out), .Q(register_2_q), .clk(CLK), .clr(RST));
  Comparator #(.width(32)) comparator_5 (.a(32'h22), .b(multiplexer_17_out), .eq(comparator_5_eq));  // open: gt, lt
  Multiplexer #(.width(32), .enable("false")) multiplexer_19 (
    .in0(multiplexer_17_out), .in1(id_ex_1_dout_32_3), .out(multiplexer_19_out), .sel(id_ex_1_dout_4_4[0]));
  Shifter #(.width(32)) shifter_1 (.in(id_ex_1_dout_32_3), .\dist (5'b00010), .out(shifter_1_out));
  Shifter #(.width(32)) shifter_2 (.in(id_ex_1_dout_32_4), .\dist (5'b00010), .out(shifter_2_out));
  Multiplexer #(.select(2), .width(32), .enable("false")) multiplexer_20 (
    .in1(32'h4), .in2(32'h20c), .in3(32'h414), .out(\中断程序入口地址 ), .sel(priority_encoder_2_out));  // open: in0
  Counter #(.width(16), .max('hffff)) counter_3 (
    .count(Benchif), .Q(\条件分支成功数 ), .clk(CLK), .clr(RST));  // open: load, D, carry
  MIPS_ALU mips_alu_1 (
    .X(multiplexer_16_out), .Y(multiplexer_19_out), .AluOP(id_ex_1_dout_4_3), .Equal(mips_alu_1_equal),
    .Result(mips_alu_1_result), .shamt(id_ex_1_dout_5));  // open: Result_2
  not not_9 (not_9_out, mips_alu_1_equal);
  Adder #(.width(32)) adder_2 (.a(shifter_1_out), .b(id_ex_1_dout_32_5), .out(adder_2_out));  // open: cin, cout
  and and_20 (and_20_out, id_ex_1_dout_4_2[0], mips_alu_1_equal);
  or or_14 (or_14_out, and_20_out, and_21_out);
  and and_21 (and_21_out, id_ex_1_dout_4_2[1], not_9_out);
  nor nor_1 (nor_1_out, Stop2, Stop1);
  Comparator #(.width(32)) comparator_6 (.a(multiplexer_16_out), .b({32{1'b0}}), .lt(comparator_6_lt));  // open: gt, eq
  Counter #(.width(16), .max('hffff)) counter_4 (
    .count(and_22_out), .Q(\LoadUse次数 ), .clk(CLK), .clr(RST));  // open: load, D, carry
  and and_22 (and_22_out, nor_1_out, Enable, Load_use);
  and and_23 (and_23_out, id_ex_1_dout_4[0], comparator_6_lt);
  not not_10 (not_10_out, id_ex_1_dout_4[2]);
  or or_15 (Benchif, and_23_out, or_14_out);
  nor nor_2 (nor_2_out, and_23_out, or_14_out);
  Multiplexer #(.width(32), .enable("false")) multiplexer_21 (
    .in0(multiplexer_16_out), .in1(shifter_2_out), .out(multiplexer_21_out), .sel(not_10_out));
  Multiplexer #(.width(32), .enable("false")) multiplexer_22 (
    .in0(adder_2_out), .in1(id_ex_1_dout_32_5), .out(multiplexer_22_out), .sel(nor_2_out));
  not not_11 (not_11_out, JMP);
  or or_16 (Bench, and_23_out, or_14_out, JMP);
  Multiplexer #(.width(32), .enable("false")) multiplexer_23 (
    .in0(multiplexer_21_out), .in1(multiplexer_22_out), .out(multiplexer_23_out), .sel(not_11_out));
  or or_17 (or_17_out, register_1_q, 1'b0);
  or or_18 (or_18_out, ERET, IR);
  EX_MEM ex_mem_1 (
    .Din_1_4(id_ex_1_dout_4_2[2]), .Din_1_5(id_ex_1_dout_4_2[3]), .Din_32_2(mips_alu_1_result),
    .Din_32_3(multiplexer_17_out), .Din_32_4(id_ex_1_dout_32_5),
    .\传输状态In_表明当前传输数据有效 (\id_ex_1_传输状态out_表明当前传输数据有效 ), .CLK(CLK), .Dout_1_4(ex_mem_1_dout_1_4),
    .Dout_1_5(ex_mem_1_dout_1_5), .Dout_32_2(ex_mem_1_dout_32_2), .Dout_32_3(ex_mem_1_dout_32_3),
    .Dout_32_4(ex_mem_1_dout_32_4), .\传输状态Out_表明当前传输数据有效 (\ex_mem_1_传输状态out_表明当前传输数据有效 ),
    .\同步清零_气泡_高电平有效 (or_18_out), .\使能端_低电平有效_stall_高电平有效 (or_17_out), .Din_1_6(id_ex_1_dout_4_4[1]),
    .Dout_1_6(ex_mem_1_dout_1_6), .Din_1_7(id_ex_1_dout_4_4[2]), .Dout_1_7(ex_mem_1_dout_1_7),
    .Din_32(register_2_q), .Dout_32(ex_mem_1_dout_32), .Dout_1_3(ex_mem_1_dout_1_3),
    .Din_1_3(id_ex_1_dout_4_4[3]), .Din_1_2(comparator_5_eq), .Dout_1_2(ex_mem_1_dout_1_2),
    .Din_1(id_ex_1_dout_4[1]), .Dout_1(ex_mem_1_dout_1), .Din_5(id_ex_1_dout_5_2), .Dout_5(ex_mem_1_dout_5),
    .Din_32_5(EX_PC), .Dout_32_5(MEM_PC), .Din_1_8(id_ex_1_dout_2_3[1]), .Dout_1_8(ex_mem_1_dout_1_8),
    .Din_1_9(id_ex_1_dout_2_3[0]), .Dout_1_9(ex_mem_1_dout_1_9), .Dout_32_6(ex_mem_1_dout_32_6),
    .Dout_32_7(ex_mem_1_dout_32_7), .Din_32_6(multiplexer_18_out), .Din_32_7(id_ex_1_dout_32_7),
    .Din_1_10(id_ex_1_dout_1), .Dout_1_10(ex_mem_1_dout_1_10));
  not not_12 (not_12_out, ex_mem_1_dout_1_2);
  and and_24 (Stop2, not_12_out, ex_mem_1_dout_1_3);
  Multiplexer #(.width(32), .enable("false")) multiplexer_24 (
    .in0({{16{1'b0}}, ex_mem_1_dout_32_3[15:0]}), .in1({ex_mem_1_dout_32_3[15:0], {16{1'b0}}}),
    .out(multiplexer_24_out), .sel(ex_mem_1_dout_32_2[1]));
  Multiplexer #(.width(32), .enable("false")) multiplexer_25 (
    .in0(ex_mem_1_dout_32_3), .in1(multiplexer_24_out), .out(multiplexer_25_out), .sel(ex_mem_1_dout_1));
  Multiplexer #(.width(4), .enable("false")) multiplexer_26 (
    .in0(4'b1111), .in1(multiplexer_27_out), .out(multiplexer_26_out), .sel(ex_mem_1_dout_1));
  Multiplexer #(.width(4), .enable("false")) multiplexer_27 (
    .in0(4'b0011), .in1(4'b1100), .out(multiplexer_27_out), .sel(ex_mem_1_dout_32_2[1]));
  // MIPS_RAM mips_ram_1: pin names not known; wires that end beside it: ex_mem_1_dout_32_2[11:2], multiplexer_25_out, ex_mem_1_dout_1_5, multiplexer_26_out, CLK, 1'b1, RST, mips_ram_1_p8
  MEM_WB mem_wb_1 (
    .Din_1_4(ex_mem_1_dout_1_6), .Din_1_5(ex_mem_1_dout_1_7), .Din_32(ex_mem_1_dout_32),
    .Din_32_3(mips_ram_1_p8), .Din_32_4(ex_mem_1_dout_32_4),
    .\传输状态In_表明当前传输数据有效 (\ex_mem_1_传输状态out_表明当前传输数据有效 ), .CLK(CLK), .Dout_1_4(mem_wb_1_dout_1_4),
    .Dout_1_5(mem_wb_1_dout_1_5), .Dout_32(LedData), .Dout_32_3(mem_wb_1_dout_32_3),
    .Dout_32_4(mem_wb_1_dout_32_4), .\同步清零_气泡_高电平有效 (ERET), .\使能端_低电平有效_stall_高电平有效 (or_19_out),
    .Dout_1(mem_wb_1_dout_1), .Dout_1_2(mem_wb_1_dout_1_2), .Din_1(ex_mem_1_dout_1_2),
    .Din_1_2(ex_mem_1_dout_1_3), .Din_5(ex_mem_1_dout_5), .Dout_5(mem_wb_1_dout_5), .Din_32_5(MEM_PC),
    .Dout_32_5(WB_PC), .Din_1_3(ex_mem_1_dout_1_4), .Dout_1_3(mem_wb_1_dout_1_3),
    .Din_32_2(ex_mem_1_dout_32_2), .Dout_32_2(mem_wb_1_dout_32_2), .Din_1_6(ex_mem_1_dout_1_8),
    .Dout_1_6(MTC0), .Din_1_7(ex_mem_1_dout_1_9), .Dout_1_7(mem_wb_1_dout_1_7),
    .Din_32_6(ex_mem_1_dout_32_6), .Dout_32_6(MTC0Data), .Din_32_7(ex_mem_1_dout_32_7),
    .Dout_32_7({mem_wb_1_dout_32_7[31:10], rd, mem_wb_1_dout_32_7[4:0]}), .Din_1_8(ex_mem_1_dout_1_10),
    .Dout_1_8(ERET));  // open: 传输状态Out_表明当前传输数据有效
  or or_19 (or_19_out, register_1_q, 1'b0);
  Multiplexer #(.width(32), .enable("false")) multiplexer_28 (
    .in0(mem_wb_1_dout_32_2), .in1(mem_wb_1_dout_32_3), .out(multiplexer_28_out), .sel(mem_wb_1_dout_1_3));
  Multiplexer #(.width(32), .enable("false")) multiplexer_29 (
    .in0(multiplexer_28_out), .in1(mem_wb_1_dout_32_4), .out(multiplexer_29_out), .sel(mem_wb_1_dout_1_5));
  Multiplexer #(.width(32), .enable("false")) multiplexer_30 (
    .in0(multiplexer_29_out), .in1(MFC0Data), .out(multiplexer_30_out), .sel(mem_wb_1_dout_1_7));

  // Other names for the same wires on the sheet: 插入气泡数[15:0] = \LoadUse次数 

  // Notes on the sheet:
  //   中断源
  //   中断等待指示
  //   指令存储器
  //   数码管输出
  //   IF/ID
  //   指令字
  //   contents of rom_1 (hex, n*v repeats v):
  //   8000d87 23bdfffc afa10000 23bdfffc afa20000 23bdfffc afa30000 23bdfffc afa40000 23bdfffc afa50000
  //   23bdfffc afa60000 23bdfffc afa70000 23bdfffc afa80000 23bdfffc afa90000 23bdfffc afaa0000 23bdfffc
  //   afab0000 23bdfffc afac0000 23bdfffc afad0000 23bdfffc afae0000 23bdfffc afaf0000 23bdfffc afb00000
  //   23bdfffc afb10000 23bdfffc afb20000 23bdfffc afb30000 23bdfffc afb40000 23bdfffc afb50000 23bdfffc
  //   afb60000 23bdfffc afb70000 23bdfffc afb80000 23bdfffc afb90000 40010800 40021000 23bdfffc afa10000
  //   23bdfffc afa20000 20010003 40810800 20030001 40831800 20160001 20140006 20150001 168020 108100
  //   2149825 132020 20020022 c 1600fffa 295a022 1680fff7 40801800 8fa20000 23bd0004 8fa10000 23bd0004
  //   40821000 40810800 8fb90000 23bd0004 8fb80000 23bd0004 8fb70000 23bd0004 8fb60000 23bd0004 8fb50000
  //   23bd0004 8fb40000 23bd0004 8fb30000 23bd0004 8fb20000 23bd0004 8fb10000 23bd0004 8fb00000 23bd0004
  //   8faf0000 23bd0004 8fae0000 23bd0004 8fad0000 23bd0004 8fac0000 23bd0004 8fab0000 23bd0004 8faa0000
  //   23bd0004 8fa90000 23bd0004 8fa80000 23bd0004 8fa70000 23bd0004 8fa60000 23bd0004 8fa50000 23bd0004
  //   8fa40000 23bd0004 8fa30000 23bd0004 8fa20000 23bd0004 8fa10000 23bd0004 42000018 23bdfffc afa10000
  //   23bdfffc afa20000 23bdfffc afa30000 23bdfffc afa40000 23bdfffc afa50000 23bdfffc afa60000 23bdfffc
  //   afa70000 23bdfffc afa80000 23bdfffc afa90000 23bdfffc afaa0000 23bdfffc afab0000 23bdfffc afac0000
  //   23bdfffc afad0000 23bdfffc afae0000 23bdfffc afaf0000 23bdfffc afb00000 23bdfffc afb10000 23bdfffc
  //   afb20000 23bdfffc afb30000 23bdfffc afb40000 23bdfffc afb50000 23bdfffc afb60000 23bdfffc afb70000
  //   23bdfffc afb80000 23bdfffc afb90000 40010800 40021000 23bdfffc afa10000 23bdfffc afa20000 20010007
  //   40810800 20030001 40831800 20160002 20140006 20150001 168020 108100 2149825 132020 20020022 c
  //   1600fffa 295a022 1680fff7 40801800 8fa20000 23bd0004 8fa10000 23bd0004 40821000 40810800 8fb90000
  //   23bd0004 8fb80000 23bd0004 8fb70000 23bd0004 8fb60000 23bd0004 8fb50000 23bd0004 8fb40000 23bd0004
  //   8fb30000 23bd0004 8fb20000 23bd0004 8fb10000 23bd0004 8fb00000 23bd0004 8faf0000 23bd0004 8fae0000
  //   23bd0004 8fad0000 23bd0004 8fac0000 23bd0004 8fab0000 23bd0004 8faa0000 23bd0004 8fa90000 23bd0004
  //   8fa80000 23bd0004 8fa70000 23bd0004 8fa60000 23bd0004 8fa50000 23bd0004 8fa40000 23bd0004 8fa30000
  //   23bd0004 8fa20000 23bd0004 8fa10000 23bd0004 42000018 23bdfffc afa10000 23bdfffc afa20000 23bdfffc
  //   afa30000 23bdfffc afa40000 23bdfffc afa50000 23bdfffc afa60000 23bdfffc afa70000 23bdfffc afa80000
  //   23bdfffc afa90000 23bdfffc afaa0000 23bdfffc afab0000 23bdfffc afac0000 23bdfffc afad0000 23bdfffc
  //   afae0000 23bdfffc afaf0000 23bdfffc afb00000 23bdfffc afb10000 23bdfffc afb20000 23bdfffc afb30000
  //   23bdfffc afb40000 23bdfffc afb50000 23bdfffc afb60000 23bdfffc afb70000 23bdfffc afb80000 23bdfffc
  //   afb90000 40010800 40021000 23bdfffc afa10000 23bdfffc afa20000 2001000f 40810800 20030001 40831800
  //   20160003 20140006 20150001 168020 108100 2149825 132020 20020022 c 1600fffa 295a022 1680fff7
  //   40801800 8fa20000 23bd0004 8fa10000 23bd0004 40821000 40810800 8fb90000 23bd0004 8fb80000 23bd0004
  //   8fb70000 23bd0004 8fb60000 23bd0004 8fb50000 23bd0004 8fb40000 23bd0004 8fb30000 23bd0004 8fb20000
  //   23bd0004 8fb10000 23bd0004 8fb00000 23bd0004 8faf0000 23bd0004 8fae0000 23bd0004 8fad0000 23bd0004
  //   8fac0000 23bd0004 8fab0000 23bd0004 8faa0000 23bd0004 8fa90000 23bd0004 8fa80000 23bd0004 8fa70000
  //   23bd0004 8fa60000 23bd0004 8fa50000 23bd0004 8fa40000 23bd0004 8fa30000 23bd0004 8fa20000 23bd0004
  //   8fa10000 23bd0004 42000018 20110200 20020022 112020 c 2231ffff 1620fffc 20020032 c 2002000a c
  //   中断按键信号产生
  //   COP0模拟
  //   OP
  //   Func
  //   rs
  //   rt
  //   rd
  //   Reset 
  //   Reset 
  //   Reset 
  //   JMP
  //   JR
  //   SH
  //   Bltz
  //   Beq
  //   Bne
  //   MemToReg
  //   MemWrite
  //   AluOP
  //   AluSrcB
  //   RegWrite
  //   JAL
  //   RegDst
  //   Syscall
  //   流水调试日志用
  //   ID/EX
  //   增加中断屏蔽字之后的中断服务程序进入处理
  //   MTC与MFC指令的数据处理
  //   中断服务程序返回处理
  //   统计
  //   EX/MEM
  //   MEM/WB
endmodule
